// Logisim project data1.circ as structural Verilog: 24 circuits, main circuit ◆海明传输测试1
module \国标转区位码  (
  input  [15:0] GB2312,
  output [6:0] \区号 ,
  output [6:0] \位号 
);

  wire [15:7] adder_1_out;

  // Probe on GB2312
  // Probe on \区号 
  Adder #(.width(16)) adder_1 (
    .a(GB2312), .b(16'h5f60), .out({adder_1_out[15], \区号 , adder_1_out[7], \位号 }));  // open: cin, cout
  // Probe on \位号 

  // Notes on the sheet:
  //   请勿增改引脚，请勿修改子电路封装
  //   输入引脚区
  //   请在下方利用上方输入输出引脚的隧道标签信号构建电路，ctrl+d复制选择组件
  //   华中科技大学计算机学院 计算机组成原理课程组
  //   要求用加法器完成
  //   推荐用最新的logisim意大利hust改良版完成实验，EDU平台采用该版本进行测试
  //   输出引脚区
  //   探测区
endmodule

module \汉字显示  (
  output [15:0] EduCoder
);

  wire \时钟_out ;
  wire [6:0] \国标转区位码_1_位号 , \国标转区位码_1_区号 ;
  wire [7:0] counter_1_q;
  wire [31:0] \字库_1_p3 , \字库_1_p4 , \字库_1_p5 , \字库_1_p6 , \字库_1_p7 , \字库_1_p8 , \字库_1_p9 , \字库_1_p10 ,
       \字库_1_p11 , \字库_1_p12 , \字库_1_p13 , \字库_1_p14 , \字库_1_p15 , \字库_1_p16 , \字库_1_p17 , \字库_1_p18 ,
       \字库_1_p19 , \字库_1_p20 , \字库_1_p21 , \字库_1_p22 , \字库_1_p23 , \字库_1_p24 , \字库_1_p25 , \字库_1_p26 ,
       \字库_1_p27 , \字库_1_p28 , \字库_1_p29 , \字库_1_p30 , \字库_1_p31 , \字库_1_p32 , \字库_1_p33 , \字库_1_p34 ;

  Counter #(.width(8), .max('hff), .ongoal("wrap"), .trigger("rising"), .behavior("old")) counter_1 (
    .Q(counter_1_q), .clk(\时钟_out ));  // open: load, D, count, carry, clr, preset
  Clock #(.highDuration(1), .lowDuration(1)) \u_时钟  (.out(\时钟_out ));
  ROM #(.addrWidth(8), .dataWidth(16), .Select("high")) rom_1 (.addr(counter_1_q), .data(EduCoder));
  \国标转区位码  \u_国标转区位码_1  (.\位号 (\国标转区位码_1_位号 ), .\区号 (\国标转区位码_1_区号 ), .GB2312(EduCoder));
  // 字库 字库_1: pin names not known; wires that end beside it: \国标转区位码_1_区号 , \国标转区位码_1_位号 , \字库_1_p3 , \字库_1_p4 , \字库_1_p5 , \字库_1_p6 , \字库_1_p7 , \字库_1_p8 , \字库_1_p9 , \字库_1_p10 , \字库_1_p11 , \字库_1_p12 , \字库_1_p13 , \字库_1_p14 , \字库_1_p15 , \字库_1_p16 , \字库_1_p17 , \字库_1_p18 , \字库_1_p19 , \字库_1_p20 , \字库_1_p21 , \字库_1_p22 , \字库_1_p23 , \字库_1_p24 , \字库_1_p25 , \字库_1_p26 , \字库_1_p27 , \字库_1_p28 , \字库_1_p29 , \字库_1_p30 , \字库_1_p31 , \字库_1_p32 , \字库_1_p33 , \字库_1_p34 
  DotMatrix #(.inputtype("row"), .matrixcols(32), .matrixrows(32), .persist(0), .dotshape("circle")) dotmatrix_1 (
    .row0(\字库_1_p3 ), .row1(\字库_1_p4 ), .row2(\字库_1_p5 ), .row3(\字库_1_p6 ), .row4(\字库_1_p7 ),
    .row5(\字库_1_p8 ), .row6(\字库_1_p9 ), .row7(\字库_1_p10 ), .row8(\字库_1_p11 ), .row9(\字库_1_p12 ),
    .row10(\字库_1_p13 ), .row11(\字库_1_p14 ), .row12(\字库_1_p15 ), .row13(\字库_1_p16 ), .row14(\字库_1_p17 ),
    .row15(\字库_1_p18 ), .row16(\字库_1_p19 ), .row17(\字库_1_p20 ), .row18(\字库_1_p21 ), .row19(\字库_1_p22 ),
    .row20(\字库_1_p23 ), .row21(\字库_1_p24 ), .row22(\字库_1_p25 ), .row23(\字库_1_p26 ), .row24(\字库_1_p27 ),
    .row25(\字库_1_p28 ), .row26(\字库_1_p29 ), .row27(\字库_1_p30 ), .row28(\字库_1_p31 ), .row29(\字库_1_p32 ),
    .row30(\字库_1_p33 ), .row31(\字库_1_p34 ));

  // Notes on the sheet:
  //   计数器
  //   GB2312
  //   实现国标转区位码电路，使得系统每个时钟正确显示一个汉字
  //   请将下面这段文字转换成GB2312替换ROM存储器中内容
  //   contents of rom_1 (hex, n*v repeats v):
  //   a3b1 a3b2 a3b3 a3b4 a3b5 a3c1 a3c2 a3c3 a3c4 a3c5 a3c6 a3c7 a3e1 a3e2 a3e3 a3e4 a3e5 a3e6 a3e7 c7e1
  //   c7e1 b5c4 ced2 d7df c1cb a3ac d5fd c8e7 ced2 c7e1 c7e1 b5c4 c0b4 a3bb ced2 c7e1 c7e1 b5c4 d5d0 cad6
  //   a3ac d7f7 b1f0 cef7 ccec b5c4 d4c6 b2ca a1a3 c4c7 bad3 c5cf b5c4 bdf0 c1f8 a3ac cac7 cfa6 d1f4 d6d0
  //   b5c4 d0c2 c4ef a3bb b2a8 b9e2 c0ef b5c4 d1de d3b0 a3ac d4da ced2 b5c4 d0c4 cdb7 b5b4 d1fa a1a3 d0a
  //   １２３４５ＡＢＣＤＥＦＧａｂｃｄｅｆｇ轻轻的我走了，正如我轻轻的来；我轻轻的招手，作别西天的云彩。那河畔的金柳，是夕阳中的新娘；波光里的艳影，在我的心头荡漾。
endmodule

// 偶校验编码
module \偶校验编码  (
  input  [15:0] \原始数据 ,
  output [16:0] \偶校验编码 
);

  wire xor_1_out, xor_2_out, xor_3_out, xor_4_out, xor_5_out, xor_6_out, xor_7_out, xor_8_out, xor_9_out,
       xor_10_out, xor_11_out, xor_12_out, xor_13_out, xor_14_out;

  xor xor_1 (xor_1_out, \原始数据 [0], \原始数据 [1]);
  xor xor_2 (xor_2_out, \原始数据 [2], \原始数据 [3]);
  xor xor_3 (xor_3_out, \原始数据 [4], \原始数据 [5]);
  xor xor_4 (xor_4_out, \原始数据 [6], \原始数据 [7]);
  xor xor_5 (xor_5_out, \原始数据 [8], \原始数据 [9]);
  xor xor_6 (xor_6_out, \原始数据 [10], \原始数据 [11]);
  xor xor_7 (xor_7_out, \原始数据 [12], \原始数据 [13]);
  xor xor_8 (xor_8_out, \原始数据 [14], \原始数据 [15]);
  xor xor_9 (xor_9_out, xor_1_out, xor_2_out);
  xor xor_10 (xor_10_out, xor_3_out, xor_4_out);
  xor xor_11 (xor_11_out, xor_5_out, xor_6_out);
  xor xor_12 (xor_12_out, xor_7_out, xor_8_out);
  xor xor_13 (xor_13_out, xor_9_out, xor_10_out);
  xor xor_14 (xor_14_out, xor_11_out, xor_12_out);
  xor xor_15 (\偶校验编码 [16], xor_13_out, xor_14_out);

  assign \偶校验编码 [15:0] = \原始数据 ;

  // Other names for the same wires on the sheet: D1 = \原始数据 [0]; Data[15:0] = \原始数据 ;
  //   校验码[16:0] = {\偶校验编码 [16], \原始数据 }; D2 = \原始数据 [1]; D3 = \原始数据 [2]; D4 = \原始数据 [3]; D5 = \原始数据 [4];
  //   D6 = \原始数据 [5]; D7 = \原始数据 [6]; D8 = \原始数据 [7]; D9 = \原始数据 [8]; D10 = \原始数据 [9]; D11 = \原始数据 [10];
  //   D12 = \原始数据 [11]; D13 = \原始数据 [12]; D14 = \原始数据 [13]; D15 = \原始数据 [14]; D16 = \原始数据 [15]

  // Notes on the sheet:
  //   输入引脚区
  //   请勿增改引脚，请勿修改子电路封装
  //   电路功能：实现16位数据位的偶校验编码，输入：16位数据；输出：17位校验码（数据位+校验位）
  //   请在下方利用上方输入输出引脚的隧道信号构建电路，ctrl+d复制选择部件
  //   输出引脚区
endmodule

// 偶校验检错
module \偶校验检错  (
  input  [16:0] \偶校验编码 ,
  output \检错位 ,
  output [15:0] \数据位 
);

  wire xor_1_out, xor_2_out, xor_3_out, xor_4_out, xor_5_out, xor_6_out, xor_7_out, xor_8_out, xor_9_out,
       xor_10_out, xor_11_out, xor_12_out, xor_13_out, xor_14_out, xor_15_out;

  xor xor_1 (xor_1_out, \偶校验编码 [0], \偶校验编码 [1]);
  xor xor_2 (xor_2_out, \偶校验编码 [2], \偶校验编码 [3]);
  xor xor_3 (xor_3_out, \偶校验编码 [4], \偶校验编码 [5]);
  xor xor_4 (xor_4_out, \偶校验编码 [6], \偶校验编码 [7]);
  xor xor_5 (xor_5_out, \偶校验编码 [8], \偶校验编码 [9]);
  xor xor_6 (xor_6_out, \偶校验编码 [10], \偶校验编码 [11]);
  xor xor_7 (xor_7_out, \偶校验编码 [12], \偶校验编码 [13]);
  xor xor_8 (xor_8_out, \偶校验编码 [14], \偶校验编码 [15]);
  xor xor_9 (xor_9_out, xor_1_out, xor_2_out);
  xor xor_10 (xor_10_out, xor_9_out, xor_11_out);
  xor xor_11 (xor_11_out, xor_3_out, xor_4_out);
  xor xor_12 (xor_12_out, xor_5_out, xor_6_out);
  xor xor_13 (xor_13_out, xor_12_out, xor_14_out);
  xor xor_14 (xor_14_out, xor_7_out, xor_8_out);
  xor xor_15 (xor_15_out, xor_10_out, xor_13_out);
  xor xor_16 (\检错位 , xor_15_out, \偶校验编码 [16]);

  assign \数据位  = \偶校验编码 [15:0];

  // Other names for the same wires on the sheet: D1 = \偶校验编码 [0]; 偶校验码[16:0] = \偶校验编码 ; D2 = \偶校验编码 [1];
  //   D3 = \偶校验编码 [2]; D4 = \偶校验编码 [3]; D5 = \偶校验编码 [4]; D6 = \偶校验编码 [5]; D7 = \偶校验编码 [6]; D8 = \偶校验编码 [7];
  //   D9 = \偶校验编码 [8]; D10 = \偶校验编码 [9]; D11 = \偶校验编码 [10]; D12 = \偶校验编码 [11]; D13 = \偶校验编码 [12]; D14 = \偶校验编码 [13];
  //   D15 = \偶校验编码 [14]; D16 = \偶校验编码 [15]; P1 = \偶校验编码 [16]

  // Notes on the sheet:
  //   输入引脚区
  //   请勿增改引脚，请勿修改子电路封装
  //   电路功能：实现17位偶校验编码的检错以及数据提取。输入：17位校验码；输出：检错位、数据位
  //   请在下方利用上方输入输出引脚的隧道信号构建电路，ctrl+d复制选择部件
  //   输出引脚区
endmodule

// 海明编码
module \海明编码  (
  input  [15:0] \原始数据 ,
  output [21:0] \海明码 
);

  wire xor_1_out, xor_2_out, xor_3_out, xor_4_out, xor_5_out, xor_6_out, xor_7_out, xor_8_out, xor_9_out,
       xor_10_out, xor_11_out, xor_12_out, xor_13_out, xor_14_out, xor_15_out, xor_18_out, xor_19_out,
       xor_20_out, xor_21_out, xor_22_out, xor_23_out, xor_24_out, xor_25_out, xor_26_out, xor_27_out,
       xor_28_out, xor_29_out, xor_32_out, xor_33_out, xor_34_out, xor_35_out, xor_36_out, xor_37_out,
       xor_38_out, xor_39_out, xor_40_out, xor_41_out, xor_42_out, xor_43_out, xor_44_out, xor_46_out,
       xor_47_out, xor_48_out, xor_49_out, xor_50_out, xor_51_out, xor_52_out, xor_53_out, xor_54_out;

  xor xor_1 (xor_1_out, \原始数据 [0], \原始数据 [1]);
  xor xor_2 (xor_2_out, \原始数据 [3], \原始数据 [4]);
  xor xor_3 (xor_3_out, \原始数据 [6], \原始数据 [8]);
  xor xor_4 (xor_4_out, \原始数据 [10], \原始数据 [11]);
  xor xor_5 (xor_5_out, \原始数据 [13], \原始数据 [15]);
  xor xor_6 (xor_6_out, \原始数据 [0], \原始数据 [2]);
  xor xor_7 (xor_7_out, xor_6_out, xor_8_out);
  xor xor_8 (xor_8_out, \原始数据 [3], \原始数据 [5]);
  xor xor_9 (xor_9_out, \原始数据 [6], \原始数据 [9]);
  xor xor_10 (xor_10_out, xor_9_out, xor_11_out);
  xor xor_11 (xor_11_out, \原始数据 [10], \原始数据 [12]);
  xor xor_12 (xor_12_out, xor_1_out, xor_2_out);
  xor xor_13 (xor_13_out, xor_12_out, xor_14_out);
  xor xor_14 (xor_14_out, xor_3_out, xor_4_out);
  xor xor_15 (xor_15_out, xor_7_out, xor_10_out);
  xor xor_16 (\海明码 [0], xor_13_out, xor_5_out);
  xor xor_17 (\海明码 [1], xor_15_out, \原始数据 [13]);
  xor xor_18 (xor_18_out, \原始数据 [1], \原始数据 [2]);
  xor xor_19 (xor_19_out, \原始数据 [3], \原始数据 [7]);
  xor xor_20 (xor_20_out, \原始数据 [8], \原始数据 [9]);
  xor xor_21 (xor_21_out, \原始数据 [10], \原始数据 [14]);
  xor xor_22 (xor_22_out, \原始数据 [4], \原始数据 [5]);
  xor xor_23 (xor_23_out, \原始数据 [6], \原始数据 [7]);
  xor xor_24 (xor_24_out, \原始数据 [8], \原始数据 [9]);
  xor xor_25 (xor_25_out, xor_18_out, xor_19_out);
  xor xor_26 (xor_26_out, xor_20_out, xor_21_out);
  xor xor_27 (xor_27_out, xor_22_out, xor_23_out);
  xor xor_28 (xor_28_out, xor_25_out, xor_26_out);
  xor xor_29 (xor_29_out, xor_27_out, xor_24_out);
  xor xor_30 (\海明码 [3], xor_28_out, \原始数据 [15]);
  xor xor_31 (\海明码 [7], xor_29_out, \原始数据 [10]);
  xor xor_32 (xor_32_out, \原始数据 [11], \原始数据 [12]);
  xor xor_33 (xor_33_out, \原始数据 [13], \原始数据 [14]);
  xor xor_34 (xor_34_out, xor_32_out, xor_33_out);
  xor xor_35 (xor_35_out, \原始数据 [0], \原始数据 [1]);
  xor xor_36 (xor_36_out, \原始数据 [2], \原始数据 [3]);
  xor xor_37 (xor_37_out, \原始数据 [4], \原始数据 [5]);
  xor xor_38 (xor_38_out, \原始数据 [6], \原始数据 [7]);
  xor xor_39 (xor_39_out, \原始数据 [8], \原始数据 [9]);
  xor xor_40 (xor_40_out, \原始数据 [10], \原始数据 [11]);
  xor xor_41 (xor_41_out, \原始数据 [12], \原始数据 [13]);
  xor xor_42 (xor_42_out, \原始数据 [14], \原始数据 [15]);
  xor xor_43 (xor_43_out, \海明码 [0], \海明码 [1]);
  xor xor_44 (xor_44_out, \海明码 [3], \海明码 [7]);
  xor xor_45 (\海明码 [15], xor_34_out, \原始数据 [15]);
  xor xor_46 (xor_46_out, xor_35_out, xor_36_out);
  xor xor_47 (xor_47_out, xor_46_out, xor_48_out);
  xor xor_48 (xor_48_out, xor_37_out, xor_38_out);
  xor xor_49 (xor_49_out, xor_39_out, xor_40_out);
  xor xor_50 (xor_50_out, xor_49_out, xor_51_out);
  xor xor_51 (xor_51_out, xor_41_out, xor_42_out);
  xor xor_52 (xor_52_out, xor_43_out, xor_44_out);
  xor xor_53 (xor_53_out, xor_52_out, \海明码 [15]);
  xor xor_54 (xor_54_out, xor_47_out, xor_50_out);
  xor xor_55 (\海明码 [21], xor_54_out, xor_53_out);

  assign {\海明码 [20:16], \海明码 [14:8], \海明码 [6:4], \海明码 [2]} = \原始数据 ;

  // Other names for the same wires on the sheet: D12 = \原始数据 [11]; Data[15:0] = \原始数据 ; D14 = \原始数据 [13];
  //   D15 = \原始数据 [14]; D16 = \原始数据 [15]; P1 = \海明码 [0]; P2 = \海明码 [1]; D1 = \原始数据 [0]; P3 = \海明码 [3]; D2 = \原始数据 [1];
  //   D3 = \原始数据 [2]; D4 = \原始数据 [3]; P4 = \海明码 [7]; D5 = \原始数据 [4]; D6 = \原始数据 [5]; D7 = \原始数据 [6]; D8 = \原始数据 [7];
  //   D9 = \原始数据 [8]; D10 = \原始数据 [9]; D11 = \原始数据 [10]; P5 = \海明码 [15]; D13 = \原始数据 [12]; P6 = \海明码 [21]

  // Notes on the sheet:
  //   输入引脚区
  //   请勿增改引脚，请勿修改子电路封装
  //   电路功能：海明编码电路，可检两位错并纠一位错，输入：16位；输出：22位海明码（数据位+校验位）
  //   注意异或门需要设置多输入行为：奇数个1时输出为1，否则功能不正确
  //   请在下方利用上方输入输出引脚的隧道信号构建电路，ctrl+d复制选择部件
  //   输出引脚区
endmodule

// 海明解码
module \海明解码  (
  input  [21:0] \海明码 ,
  output \_0位错 ,
  output \_1位错 ,
  output \_2位错 ,
  output [15:0] \纠错后数据 
);

  wire G1, G2, G3, G4, G5, G6, not_1_out, not_3_out, not_4_out, not_5_out, not_6_out, not_7_out, not_8_out,
       not_9_out, not_10_out, not_11_out, not_12_out, not_13_out, not_14_out, not_15_out, not_16_out,
       not_17_out, not_18_out, not_19_out, or_1_out, or_2_out, or_3_out, or_4_out, or_5_out, or_6_out,
       or_7_out, or_8_out, or_9_out, or_10_out, or_11_out, or_12_out, or_13_out, or_14_out, or_15_out,
       xor_1_out, xor_2_out, xor_3_out, xor_4_out, xor_5_out, xor_6_out, xor_7_out, xor_8_out, xor_9_out,
       xor_10_out, xor_11_out, xor_12_out, xor_13_out, xor_14_out, xor_15_out, xor_16_out, xor_17_out,
       xor_20_out, xor_21_out, xor_22_out, xor_23_out, xor_24_out, xor_25_out, xor_26_out, xor_27_out,
       xor_28_out, xor_29_out, xor_30_out, xor_31_out, xor_32_out, xor_34_out, xor_36_out, xor_37_out,
       xor_38_out, xor_39_out, xor_40_out, xor_41_out, xor_42_out, xor_43_out, xor_44_out, xor_45_out,
       xor_46_out, xor_47_out, xor_48_out, xor_49_out, xor_50_out, xor_51_out, xor_52_out, xor_53_out,
       xor_54_out, xor_55_out, xor_56_out, xor_57_out, xor_58_out, xor_60_out, \解码器_1_g , \解码器_1_h ,
       \解码器_1_i , \解码器_1_j , \解码器_1_k , \解码器_1_l , \解码器_1_m , \解码器_1_n , \解码器_1_o , \解码器_1_p , \解码器_1_q ,
       \解码器_1_r , \解码器_1_s , \解码器_1_t , \解码器_1_u , \解码器_1_v ;
  wire [15:0] multiplexer_1_out;

  xor xor_1 (xor_1_out, \海明码 [2], \海明码 [4]);
  xor xor_2 (xor_2_out, \海明码 [6], \海明码 [8]);
  xor xor_3 (xor_3_out, \海明码 [10], \海明码 [12]);
  xor xor_4 (xor_4_out, \海明码 [14], \海明码 [16]);
  xor xor_5 (xor_5_out, \海明码 [18], \海明码 [20]);
  xor xor_6 (xor_6_out, \海明码 [2], \海明码 [5]);
  xor xor_7 (xor_7_out, \海明码 [6], \海明码 [9]);
  xor xor_8 (xor_8_out, \海明码 [10], \海明码 [13]);
  xor xor_9 (xor_9_out, \海明码 [14], \海明码 [17]);
  xor xor_10 (xor_10_out, xor_1_out, xor_2_out);
  xor xor_11 (xor_11_out, xor_3_out, xor_4_out);
  xor xor_12 (xor_12_out, xor_6_out, xor_7_out);
  xor xor_13 (xor_13_out, xor_12_out, xor_14_out);
  xor xor_14 (xor_14_out, xor_8_out, xor_9_out);
  or or_1 (or_1_out, G1, G2);
  or or_2 (or_2_out, G3, G4);
  or or_3 (or_3_out, G5, G6);
  or or_4 (or_4_out, G1, G2);
  or or_5 (or_5_out, G3, G4);
  or or_6 (or_6_out, G5, G6);
  or or_7 (or_7_out, G1, G2);
  or or_8 (or_8_out, G3, G4);
  or or_9 (or_9_out, G5, G6);
  not not_1 (not_1_out, G6);
  xor xor_15 (xor_15_out, xor_10_out, xor_11_out);
  xor xor_16 (xor_16_out, xor_13_out, \海明码 [18]);
  or or_10 (or_10_out, or_1_out, or_2_out);
  or or_11 (or_11_out, or_10_out, or_3_out);
  or or_12 (or_12_out, or_4_out, or_5_out);
  or or_13 (or_13_out, or_12_out, or_6_out);
  or or_14 (or_14_out, or_7_out, or_8_out);
  or or_15 (or_15_out, or_14_out, or_9_out);
  xor xor_17 (xor_17_out, xor_15_out, xor_5_out);
  xor xor_18 (G2, xor_16_out, \海明码 [1]);
  not not_2 (\_0位错 , or_11_out);
  and and_1 (\_1位错 , or_13_out, G6);
  and and_2 (\_2位错 , or_15_out, not_1_out);
  xor xor_19 (G1, xor_17_out, \海明码 [0]);
  \解码器  \u_解码器_1  (
    .a(G5), .b(G4), .c(G3), .d(G2), .e(G1), .G(\解码器_1_g ), .H(\解码器_1_h ), .I(\解码器_1_i ), .J(\解码器_1_j ),
    .K(\解码器_1_k ), .L(\解码器_1_l ), .M(\解码器_1_m ), .N(\解码器_1_n ), .O(\解码器_1_o ), .P(\解码器_1_p ), .Q(\解码器_1_q ),
    .R(\解码器_1_r ), .S(\解码器_1_s ), .T(\解码器_1_t ), .U(\解码器_1_u ), .V(\解码器_1_v ));
  not not_3 (not_3_out, \海明码 [2]);
  xor xor_20 (xor_20_out, \海明码 [4], \海明码 [5]);
  xor xor_21 (xor_21_out, \海明码 [6], \海明码 [11]);
  xor xor_22 (xor_22_out, \海明码 [12], \海明码 [13]);
  xor xor_23 (xor_23_out, \海明码 [14], \海明码 [19]);
  xor xor_24 (xor_24_out, \海明码 [8], \海明码 [9]);
  xor xor_25 (xor_25_out, \海明码 [10], \海明码 [11]);
  xor xor_26 (xor_26_out, \海明码 [12], \海明码 [13]);
  Multiplexer #(.select(1), .width(1), .disabled("Z"), .enable("false")) multiplexer_1 (
    .in0(\海明码 [2]), .in1(not_3_out), .out(multiplexer_1_out[0]), .sel(\解码器_1_v ));
  Multiplexer #(.select(1), .width(1), .disabled("Z"), .enable("false")) multiplexer_2 (
    .in0(\海明码 [4]), .in1(not_4_out), .out(multiplexer_1_out[1]), .sel(\解码器_1_u ));
  not not_4 (not_4_out, \海明码 [4]);
  not not_5 (not_5_out, \海明码 [5]);
  not not_6 (not_6_out, \海明码 [6]);
  xor xor_27 (xor_27_out, xor_20_out, xor_21_out);
  xor xor_28 (xor_28_out, xor_22_out, xor_23_out);
  xor xor_29 (xor_29_out, xor_24_out, xor_25_out);
  Multiplexer #(.select(1), .width(1), .disabled("Z"), .enable("false")) multiplexer_3 (
    .in0(\海明码 [5]), .in1(not_5_out), .out(multiplexer_1_out[2]), .sel(\解码器_1_t ));
  Multiplexer #(.select(1), .width(1), .disabled("Z"), .enable("false")) multiplexer_4 (
    .in0(\海明码 [6]), .in1(not_6_out), .out(multiplexer_1_out[3]), .sel(\解码器_1_s ));
  Multiplexer #(.select(1), .width(1), .disabled("Z"), .enable("false")) multiplexer_5 (
    .in0(\海明码 [8]), .in1(not_7_out), .out(multiplexer_1_out[4]), .sel(\解码器_1_r ));
  not not_7 (not_7_out, \海明码 [8]);
  not not_8 (not_8_out, \海明码 [9]);
  xor xor_30 (xor_30_out, xor_27_out, xor_28_out);
  xor xor_31 (xor_31_out, xor_29_out, xor_26_out);
  Multiplexer #(.select(1), .width(1), .disabled("Z"), .enable("false")) multiplexer_6 (
    .in0(\海明码 [9]), .in1(not_8_out), .out(multiplexer_1_out[5]), .sel(\解码器_1_q ));
  Multiplexer #(.select(1), .width(1), .disabled("Z"), .enable("false")) multiplexer_7 (
    .in0(\海明码 [10]), .in1(not_9_out), .out(multiplexer_1_out[6]), .sel(\解码器_1_p ));
  not not_9 (not_9_out, \海明码 [10]);
  not not_10 (not_10_out, \海明码 [11]);
  not not_11 (not_11_out, \海明码 [12]);
  xor xor_32 (xor_32_out, xor_30_out, \海明码 [20]);
  xor xor_33 (G3, xor_32_out, \海明码 [3]);
  xor xor_34 (xor_34_out, xor_31_out, \海明码 [14]);
  xor xor_35 (G4, xor_34_out, \海明码 [7]);
  Multiplexer #(.select(1), .width(1), .disabled("Z"), .enable("false")) multiplexer_8 (
    .in0(\海明码 [11]), .in1(not_10_out), .out(multiplexer_1_out[7]), .sel(\解码器_1_o ));
  Multiplexer #(.select(1), .width(1), .disabled("Z"), .enable("false")) multiplexer_9 (
    .in0(\海明码 [12]), .in1(not_11_out), .out(multiplexer_1_out[8]), .sel(\解码器_1_n ));
  Multiplexer #(.select(1), .width(1), .disabled("Z"), .enable("false")) multiplexer_10 (
    .in0(\海明码 [13]), .in1(not_12_out), .out(multiplexer_1_out[9]), .sel(\解码器_1_m ));
  not not_12 (not_12_out, \海明码 [13]);
  not not_13 (not_13_out, \海明码 [14]);
  not not_14 (not_14_out, \海明码 [16]);
  Multiplexer #(.select(1), .width(1), .disabled("Z"), .enable("false")) multiplexer_11 (
    .in0(\海明码 [14]), .in1(not_13_out), .out(multiplexer_1_out[10]), .sel(\解码器_1_l ));
  Multiplexer #(.select(1), .width(1), .disabled("Z"), .enable("false")) multiplexer_12 (
    .in0(\海明码 [16]), .in1(not_14_out), .out(multiplexer_1_out[11]), .sel(\解码器_1_k ));
  Multiplexer #(.select(1), .width(1), .disabled("Z"), .enable("false")) multiplexer_13 (
    .in0(\海明码 [17]), .in1(not_15_out), .out(multiplexer_1_out[12]), .sel(\解码器_1_j ));
  not not_15 (not_15_out, \海明码 [17]);
  not not_16 (not_16_out, \海明码 [18]);
  Multiplexer #(.select(1), .width(1), .disabled("Z"), .enable("false")) multiplexer_14 (
    .in0(\海明码 [18]), .in1(not_16_out), .out(multiplexer_1_out[13]), .sel(\解码器_1_i ));
  Multiplexer #(.select(1), .width(1), .disabled("Z"), .enable("false")) multiplexer_15 (
    .in0(\海明码 [19]), .in1(not_17_out), .out(multiplexer_1_out[14]), .sel(\解码器_1_h ));
  not not_17 (not_17_out, \海明码 [19]);
  not not_18 (not_18_out, \海明码 [20]);
  Multiplexer #(.select(1), .width(1), .disabled("Z"), .enable("false")) multiplexer_16 (
    .in0(\海明码 [20]), .in1(not_18_out), .out(multiplexer_1_out[15]), .sel(\解码器_1_g ));
  xor xor_36 (xor_36_out, \海明码 [16], \海明码 [17]);
  xor xor_37 (xor_37_out, \海明码 [18], \海明码 [19]);
  xor xor_38 (xor_38_out, \海明码 [2], \海明码 [4]);
  xor xor_39 (xor_39_out, \海明码 [5], \海明码 [6]);
  xor xor_40 (xor_40_out, \海明码 [8], \海明码 [9]);
  xor xor_41 (xor_41_out, \海明码 [10], \海明码 [11]);
  xor xor_42 (xor_42_out, \海明码 [12], \海明码 [13]);
  xor xor_43 (xor_43_out, \海明码 [14], \海明码 [16]);
  xor xor_44 (xor_44_out, \海明码 [17], \海明码 [18]);
  xor xor_45 (xor_45_out, \海明码 [19], \海明码 [20]);
  xor xor_46 (xor_46_out, \海明码 [0], \海明码 [1]);
  xor xor_47 (xor_47_out, \海明码 [3], \海明码 [7]);
  xor xor_48 (xor_48_out, \海明码 [15], \海明码 [21]);
  not not_19 (not_19_out, \_0位错 );
  Multiplexer #(.select(1), .width(16), .disabled("Z"), .enable("false")) multiplexer_17 (
    .in0({\海明码 [20:16], \海明码 [14:8], \海明码 [6:4], \海明码 [2]}), .in1(multiplexer_1_out), .out(\纠错后数据 ),
    .sel(not_19_out));
  xor xor_49 (xor_49_out, xor_36_out, xor_37_out);
  xor xor_50 (xor_50_out, xor_38_out, xor_39_out);
  xor xor_51 (xor_51_out, xor_40_out, xor_41_out);
  xor xor_52 (xor_52_out, xor_42_out, xor_43_out);
  xor xor_53 (xor_53_out, xor_44_out, xor_45_out);
  xor xor_54 (xor_54_out, xor_46_out, xor_47_out);
  xor xor_55 (xor_55_out, xor_49_out, \海明码 [20]);
  xor xor_56 (xor_56_out, xor_50_out, xor_51_out);
  xor xor_57 (xor_57_out, xor_52_out, xor_53_out);
  xor xor_58 (xor_58_out, xor_54_out, xor_48_out);
  xor xor_59 (G5, xor_55_out, \海明码 [15]);
  xor xor_60 (xor_60_out, xor_56_out, xor_57_out);
  xor xor_61 (G6, xor_60_out, xor_58_out);

  // Other names for the same wires on the sheet: D1 = \海明码 [2]; D2 = \海明码 [4]; D3 = \海明码 [5]; D4 = \海明码 [6];
  //   D5 = \海明码 [8]; D6 = \海明码 [9]; D7 = \海明码 [10]; D8 = \海明码 [11]; D9 = \海明码 [12]; D10 = \海明码 [13]; D11 = \海明码 [14];
  //   D12 = \海明码 [16]; D13 = \海明码 [17]; D14 = \海明码 [18]; D15 = \海明码 [19]; D16 = \海明码 [20]; P1 = \海明码 [0];
  //   P2 = \海明码 [1]; P3 = \海明码 [3]; P4 = \海明码 [7]; P5 = \海明码 [15]; P6 = \海明码 [21]

  // Notes on the sheet:
  //   输入引脚区
  //   输出引脚区
  //   注意异或门需要设置多输入行为：奇数个1时输出为1，否则功能不正确
  //   问题3，一开始没有考虑总检错位P6出错的情况，实际上G6在这里也需要相或
  //   电路功能：
  //   问题2，检错码一开始使用了检错位Pi来代替，从而在Pi错误时会错误的修改数据位
  //   请勿增改引脚，请勿修改子电路封装
  //   输入：22位海明码；输出：纠错后的数据、错误模式
  //   请在下方利用上方输入输出引脚的隧道信号构建电路，ctrl+d复制选择部件
  //   实现22位海明码的数据解码，能判断1位错，2位错，无错误，1位错自动纠错。
  //   问题1，总检错码的亦或项里没有带上P6总检错位
  //   总偶校验检错位
endmodule

// CRC编码
module \CRC编码  (
  input  [15:0] \原始数据 ,
  output [21:0] \CRC校验码 
);

  wire xor_1_out, xor_2_out, xor_3_out, xor_4_out, xor_5_out, xor_6_out, xor_8_out, xor_9_out, xor_10_out,
       xor_11_out, xor_12_out, xor_13_out, xor_14_out, xor_16_out, xor_17_out, xor_18_out, xor_19_out,
       xor_20_out, xor_21_out, xor_22_out, xor_23_out, xor_25_out, xor_26_out, xor_27_out, xor_28_out,
       xor_29_out, xor_30_out, xor_31_out, xor_32_out, xor_33_out, xor_34_out, xor_35_out, xor_36_out,
       xor_37_out, xor_38_out, xor_41_out, xor_42_out, xor_43_out, xor_44_out, xor_45_out, xor_46_out,
       xor_47_out, xor_48_out, xor_49_out, xor_50_out, xor_51_out, xor_52_out, xor_53_out, xor_54_out,
       xor_55_out, xor_56_out, xor_57_out, xor_58_out, xor_59_out;

  xor xor_1 (xor_1_out, \原始数据 [2], \原始数据 [4]);
  xor xor_2 (xor_2_out, xor_1_out, xor_3_out);
  xor xor_3 (xor_3_out, \原始数据 [5], \原始数据 [8]);
  xor xor_4 (xor_4_out, \原始数据 [9], \原始数据 [10]);
  xor xor_5 (xor_5_out, xor_4_out, xor_6_out);
  xor xor_6 (xor_6_out, \原始数据 [11], \原始数据 [12]);
  xor xor_7 (\CRC校验码 [4], xor_2_out, xor_5_out);
  xor xor_8 (xor_8_out, \原始数据 [1], \原始数据 [3]);
  xor xor_9 (xor_9_out, \原始数据 [4], \原始数据 [10]);
  xor xor_10 (xor_10_out, \原始数据 [7], \原始数据 [8]);
  xor xor_11 (xor_11_out, \原始数据 [9], \原始数据 [11]);
  xor xor_12 (xor_12_out, xor_8_out, xor_9_out);
  xor xor_13 (xor_13_out, xor_10_out, xor_11_out);
  xor xor_14 (xor_14_out, xor_12_out, xor_13_out);
  xor xor_15 (\CRC校验码 [3], xor_14_out, \原始数据 [15]);
  xor xor_16 (xor_16_out, \原始数据 [0], \原始数据 [2]);
  xor xor_17 (xor_17_out, \原始数据 [3], \原始数据 [8]);
  xor xor_18 (xor_18_out, \原始数据 [9], \原始数据 [10]);
  xor xor_19 (xor_19_out, \原始数据 [6], \原始数据 [7]);
  xor xor_20 (xor_20_out, \原始数据 [14], \原始数据 [15]);
  xor xor_21 (xor_21_out, xor_16_out, xor_17_out);
  xor xor_22 (xor_22_out, xor_18_out, xor_23_out);
  xor xor_23 (xor_23_out, xor_19_out, xor_20_out);
  xor xor_24 (\CRC校验码 [2], xor_21_out, xor_22_out);
  xor xor_25 (xor_25_out, \原始数据 [1], \原始数据 [4]);
  xor xor_26 (xor_26_out, \原始数据 [6], \原始数据 [7]);
  xor xor_27 (xor_27_out, \原始数据 [10], \原始数据 [11]);
  xor xor_28 (xor_28_out, \原始数据 [12], \原始数据 [13]);
  xor xor_29 (xor_29_out, \原始数据 [0], \原始数据 [3]);
  xor xor_30 (xor_30_out, xor_29_out, xor_31_out);
  xor xor_31 (xor_31_out, \原始数据 [5], \原始数据 [6]);
  xor xor_32 (xor_32_out, \原始数据 [9], \原始数据 [10]);
  xor xor_33 (xor_33_out, xor_32_out, xor_34_out);
  xor xor_34 (xor_34_out, \原始数据 [11], \原始数据 [12]);
  xor xor_35 (xor_35_out, xor_25_out, xor_26_out);
  xor xor_36 (xor_36_out, xor_27_out, xor_28_out);
  xor xor_37 (xor_37_out, xor_30_out, xor_33_out);
  xor xor_38 (xor_38_out, xor_35_out, xor_36_out);
  xor xor_39 (\CRC校验码 [1], xor_38_out, \原始数据 [14]);
  xor xor_40 (\CRC校验码 [0], xor_37_out, \原始数据 [13]);
  xor xor_41 (xor_41_out, \CRC校验码 [1], \CRC校验码 [2]);
  xor xor_42 (xor_42_out, \CRC校验码 [3], \CRC校验码 [4]);
  xor xor_43 (xor_43_out, \原始数据 [0], \原始数据 [1]);
  xor xor_44 (xor_44_out, \原始数据 [2], \原始数据 [3]);
  xor xor_45 (xor_45_out, \原始数据 [4], \原始数据 [5]);
  xor xor_46 (xor_46_out, \原始数据 [6], \原始数据 [7]);
  xor xor_47 (xor_47_out, \原始数据 [8], \原始数据 [9]);
  xor xor_48 (xor_48_out, \原始数据 [10], \原始数据 [11]);
  xor xor_49 (xor_49_out, \原始数据 [12], \原始数据 [13]);
  xor xor_50 (xor_50_out, \原始数据 [14], \原始数据 [15]);
  xor xor_51 (xor_51_out, xor_41_out, xor_42_out);
  xor xor_52 (xor_52_out, xor_43_out, xor_44_out);
  xor xor_53 (xor_53_out, xor_45_out, xor_46_out);
  xor xor_54 (xor_54_out, xor_47_out, xor_48_out);
  xor xor_55 (xor_55_out, xor_49_out, xor_50_out);
  xor xor_56 (xor_56_out, \CRC校验码 [0], xor_51_out);
  xor xor_57 (xor_57_out, xor_52_out, xor_53_out);
  xor xor_58 (xor_58_out, xor_57_out, xor_59_out);
  xor xor_59 (xor_59_out, xor_54_out, xor_55_out);
  xor xor_60 (\CRC校验码 [5], xor_56_out, xor_58_out);

  assign \CRC校验码 [21:6] = \原始数据 ;

  // Other names for the same wires on the sheet: CRC编码[21:0] = {\原始数据 , \CRC校验码 [5:0]}; r1 = \CRC校验码 [0];
  //   r2 = \CRC校验码 [1]; r3 = \CRC校验码 [2]; r4 = \CRC校验码 [3]; r5 = \CRC校验码 [4]; P = \CRC校验码 [5]; r6 = \CRC校验码 [5];
  //   D1 = \原始数据 [0]; Data[15:0] = \原始数据 ; D2 = \原始数据 [1]; D3 = \原始数据 [2]; D4 = \原始数据 [3]; D5 = \原始数据 [4];
  //   D6 = \原始数据 [5]; D7 = \原始数据 [6]; D9 = \原始数据 [8]; D8 = \原始数据 [7]; D10 = \原始数据 [9]; D11 = \原始数据 [10];
  //   D12 = \原始数据 [11]; D13 = \原始数据 [12]; D14 = \原始数据 [13]; D15 = \原始数据 [14]; D16 = \原始数据 [15]

  // Notes on the sheet:
  //   输入引脚区
  //   请勿增改引脚，请勿修改子电路封装
  //   注意异或门需要设置多输入行为：奇数个1时输出为1，否则功能不正确
  //   电路功能：CRC编码电路，可检两位错并纠一位错，输入：16位；输出：22位海明码（数据位+校验位）
  //   请在下方利用上方输入输出引脚的隧道信号构建电路，ctrl+d复制选择部件
  //   输出引脚区
endmodule

// CRC解码
module \CRC解码  (
  input  [21:0] \CRC编码 ,
  output \_0位错 ,
  output \_1位错 ,
  output \_2位错 ,
  output [15:0] \纠错后数据 
);

  wire \crc解码器_1_d1 , \crc解码器_1_d2 , \crc解码器_1_d3 , \crc解码器_1_d4 , \crc解码器_1_d5 , \crc解码器_1_d6 ,
       \crc解码器_1_d7 , \crc解码器_1_d8 , \crc解码器_1_d9 , \crc解码器_1_d10 , \crc解码器_1_d11 , \crc解码器_1_d12 ,
       \crc解码器_1_d13 , \crc解码器_1_d14 , \crc解码器_1_d15 , \crc解码器_1_d16 , \crc解码器_1_r1 , \crc解码器_1_r2 ,
       \crc解码器_1_r3 , \crc解码器_1_r4 , \crc解码器_1_r5 , not_1_out, or_1_out, or_2_out, or_3_out, or_4_out,
       xor_1_out, xor_2_out, xor_3_out, xor_4_out, xor_5_out, xor_6_out, xor_7_out, xor_8_out, xor_9_out,
       xor_10_out, xor_11_out, xor_12_out, xor_13_out, xor_14_out, xor_15_out, xor_16_out, xor_17_out,
       xor_18_out, xor_19_out, xor_20_out, xor_21_out, xor_22_out, xor_23_out, xor_24_out, xor_25_out,
       xor_26_out, xor_27_out, xor_28_out, xor_29_out, xor_30_out, xor_31_out, xor_32_out, xor_33_out,
       xor_34_out, xor_35_out, xor_36_out, xor_37_out, xor_38_out, xor_39_out, xor_40_out, xor_41_out,
       xor_42_out, xor_43_out, xor_44_out, xor_45_out, xor_46_out, xor_47_out, xor_48_out, xor_49_out,
       xor_50_out, xor_52_out, xor_53_out, xor_54_out, xor_55_out, xor_56_out, xor_57_out, xor_58_out,
       xor_59_out, xor_60_out, xor_61_out, xor_62_out, xor_63_out, xor_64_out, xor_65_out, xor_66_out,
       xor_67_out, xor_68_out, xor_69_out, xor_70_out, xor_71_out, xor_72_out, xor_73_out, xor_74_out,
       xor_75_out, xor_76_out, xor_77_out, xor_78_out, xor_79_out, xor_80_out, xor_81_out, xor_82_out,
       xor_83_out, xor_84_out, xor_85_out, xor_86_out, xor_87_out, xor_88_out, xor_89_out, xor_90_out,
       xor_91_out, xor_92_out, xor_93_out, xor_94_out, xor_95_out, xor_96_out, xor_97_out, xor_98_out,
       xor_99_out, xor_100_out, xor_101_out, xor_102_out, xor_103_out, xor_104_out, xor_105_out, xor_106_out,
       xor_107_out, xor_108_out, xor_109_out, xor_110_out, xor_111_out;

  xor xor_1 (xor_1_out, \CRC编码 [0], \CRC编码 [1]);
  xor xor_2 (xor_2_out, \CRC编码 [2], \CRC编码 [3]);
  xor xor_3 (xor_3_out, \CRC编码 [4], \CRC编码 [5]);
  xor xor_4 (xor_4_out, \CRC编码 [6], \CRC编码 [7]);
  xor xor_5 (xor_5_out, \CRC编码 [8], \CRC编码 [9]);
  xor xor_6 (xor_6_out, \CRC编码 [10], \CRC编码 [11]);
  xor xor_7 (xor_7_out, \CRC编码 [12], \CRC编码 [13]);
  xor xor_8 (xor_8_out, \CRC编码 [14], \CRC编码 [15]);
  xor xor_9 (xor_9_out, \CRC编码 [16], \CRC编码 [17]);
  xor xor_10 (xor_10_out, \CRC编码 [18], \CRC编码 [19]);
  xor xor_11 (xor_11_out, \CRC编码 [20], \CRC编码 [21]);
  xor xor_12 (xor_12_out, \CRC编码 [7], \CRC编码 [9]);
  xor xor_13 (xor_13_out, \CRC编码 [10], \CRC编码 [16]);
  xor xor_14 (xor_14_out, \CRC编码 [13], \CRC编码 [14]);
  xor xor_15 (xor_15_out, \CRC编码 [15], \CRC编码 [17]);
  xor xor_16 (xor_16_out, xor_1_out, xor_2_out);
  xor xor_17 (xor_17_out, xor_3_out, xor_4_out);
  xor xor_18 (xor_18_out, xor_5_out, xor_6_out);
  xor xor_19 (xor_19_out, xor_7_out, xor_8_out);
  xor xor_20 (xor_20_out, xor_9_out, xor_10_out);
  xor xor_21 (xor_21_out, xor_12_out, xor_13_out);
  xor xor_22 (xor_22_out, xor_14_out, xor_15_out);
  xor xor_23 (xor_23_out, \CRC编码 [6], \CRC编码 [8]);
  xor xor_24 (xor_24_out, \CRC编码 [9], \CRC编码 [14]);
  xor xor_25 (xor_25_out, \CRC编码 [15], \CRC编码 [16]);
  xor xor_26 (xor_26_out, \CRC编码 [12], \CRC编码 [13]);
  xor xor_27 (xor_27_out, \CRC编码 [20], \CRC编码 [21]);
  xor xor_28 (xor_28_out, \CRC编码 [7], \CRC编码 [10]);
  xor xor_29 (xor_29_out, \CRC编码 [12], \CRC编码 [13]);
  xor xor_30 (xor_30_out, \CRC编码 [16], \CRC编码 [17]);
  xor xor_31 (xor_31_out, \CRC编码 [18], \CRC编码 [19]);
  xor xor_32 (xor_32_out, \CRC编码 [6], \CRC编码 [9]);
  xor xor_33 (xor_33_out, \CRC编码 [11], \CRC编码 [12]);
  xor xor_34 (xor_34_out, \CRC编码 [15], \CRC编码 [16]);
  xor xor_35 (xor_35_out, \CRC编码 [17], \CRC编码 [18]);
  xor xor_36 (xor_36_out, xor_16_out, xor_17_out);
  xor xor_37 (xor_37_out, xor_36_out, xor_38_out);
  xor xor_38 (xor_38_out, xor_18_out, xor_19_out);
  xor xor_39 (xor_39_out, xor_20_out, xor_11_out);
  xor xor_40 (xor_40_out, \CRC编码 [8], \CRC编码 [10]);
  xor xor_41 (xor_41_out, \CRC编码 [11], \CRC编码 [14]);
  xor xor_42 (xor_42_out, \CRC编码 [15], \CRC编码 [16]);
  xor xor_43 (xor_43_out, \CRC编码 [17], \CRC编码 [18]);
  xor xor_44 (xor_44_out, xor_21_out, xor_22_out);
  xor xor_45 (xor_45_out, xor_23_out, xor_24_out);
  xor xor_46 (xor_46_out, xor_26_out, xor_27_out);
  xor xor_47 (xor_47_out, xor_28_out, xor_29_out);
  xor xor_48 (xor_48_out, xor_30_out, xor_31_out);
  xor xor_49 (xor_49_out, xor_32_out, xor_33_out);
  xor xor_50 (xor_50_out, xor_34_out, xor_35_out);
  xor xor_51 (\_1位错 , xor_37_out, xor_39_out);
  xor xor_52 (xor_52_out, xor_40_out, xor_41_out);
  xor xor_53 (xor_53_out, xor_52_out, xor_54_out);
  xor xor_54 (xor_54_out, xor_42_out, xor_43_out);
  xor xor_55 (xor_55_out, xor_44_out, \CRC编码 [21]);
  xor xor_56 (xor_56_out, xor_55_out, \CRC编码 [3]);
  xor xor_57 (xor_57_out, xor_45_out, xor_58_out);
  xor xor_58 (xor_58_out, xor_25_out, xor_46_out);
  xor xor_59 (xor_59_out, xor_47_out, xor_48_out);
  xor xor_60 (xor_60_out, xor_59_out, \CRC编码 [20]);
  xor xor_61 (xor_61_out, xor_49_out, xor_50_out);
  xor xor_62 (xor_62_out, xor_61_out, \CRC编码 [19]);
  xor xor_63 (xor_63_out, xor_53_out, \CRC编码 [4]);
  xor xor_64 (xor_64_out, xor_57_out, \CRC编码 [2]);
  xor xor_65 (xor_65_out, xor_60_out, \CRC编码 [1]);
  xor xor_66 (xor_66_out, xor_62_out, \CRC编码 [0]);
  or or_1 (or_1_out, xor_63_out, xor_56_out);
  or or_2 (or_2_out, xor_64_out, xor_65_out);
  or or_3 (or_3_out, or_1_out, or_2_out);
  or or_4 (or_4_out, or_3_out, xor_66_out);
  not not_1 (not_1_out, \_1位错 );
  not not_2 (\_0位错 , or_4_out);
  and and_1 (\_2位错 , or_4_out, not_1_out);
  xor xor_67 (xor_67_out, \CRC编码 [8], \CRC编码 [10]);
  xor xor_68 (xor_68_out, xor_67_out, xor_69_out);
  xor xor_69 (xor_69_out, \CRC编码 [11], \CRC编码 [14]);
  xor xor_70 (xor_70_out, \CRC编码 [15], \CRC编码 [16]);
  xor xor_71 (xor_71_out, xor_70_out, xor_72_out);
  xor xor_72 (xor_72_out, \CRC编码 [17], \CRC编码 [18]);
  xor xor_73 (xor_73_out, \CRC编码 [7], \CRC编码 [9]);
  xor xor_74 (xor_74_out, xor_73_out, xor_75_out);
  xor xor_75 (xor_75_out, \CRC编码 [10], \CRC编码 [16]);
  xor xor_76 (xor_76_out, \CRC编码 [13], \CRC编码 [14]);
  xor xor_77 (xor_77_out, xor_76_out, xor_78_out);
  xor xor_78 (xor_78_out, \CRC编码 [15], \CRC编码 [17]);
  xor xor_79 (xor_79_out, \CRC编码 [6], \CRC编码 [8]);
  xor xor_80 (xor_80_out, xor_79_out, xor_81_out);
  xor xor_81 (xor_81_out, \CRC编码 [9], \CRC编码 [14]);
  xor xor_82 (xor_82_out, \CRC编码 [15], \CRC编码 [16]);
  xor xor_83 (xor_83_out, \CRC编码 [12], \CRC编码 [13]);
  xor xor_84 (xor_84_out, xor_83_out, xor_85_out);
  xor xor_85 (xor_85_out, \CRC编码 [20], \CRC编码 [21]);
  xor xor_86 (xor_86_out, \CRC编码 [7], \CRC编码 [10]);
  xor xor_87 (xor_87_out, xor_86_out, xor_88_out);
  xor xor_88 (xor_88_out, \CRC编码 [12], \CRC编码 [13]);
  xor xor_89 (xor_89_out, \CRC编码 [16], \CRC编码 [17]);
  xor xor_90 (xor_90_out, xor_89_out, xor_91_out);
  xor xor_91 (xor_91_out, \CRC编码 [18], \CRC编码 [19]);
  xor xor_92 (xor_92_out, \CRC编码 [6], \CRC编码 [9]);
  xor xor_93 (xor_93_out, xor_92_out, xor_94_out);
  xor xor_94 (xor_94_out, \CRC编码 [11], \CRC编码 [12]);
  xor xor_95 (xor_95_out, \CRC编码 [15], \CRC编码 [16]);
  xor xor_96 (xor_96_out, xor_95_out, xor_97_out);
  xor xor_97 (xor_97_out, \CRC编码 [17], \CRC编码 [18]);
  xor xor_98 (xor_98_out, xor_68_out, xor_71_out);
  xor xor_99 (xor_99_out, xor_74_out, xor_77_out);
  xor xor_100 (xor_100_out, xor_82_out, xor_84_out);
  xor xor_101 (xor_101_out, xor_87_out, xor_90_out);
  xor xor_102 (xor_102_out, xor_93_out, xor_96_out);
  xor xor_103 (xor_103_out, xor_98_out, \CRC编码 [4]);
  xor xor_104 (xor_104_out, xor_99_out, \CRC编码 [21]);
  xor xor_105 (xor_105_out, xor_80_out, xor_100_out);
  xor xor_106 (xor_106_out, xor_101_out, \CRC编码 [20]);
  xor xor_107 (xor_107_out, xor_102_out, \CRC编码 [19]);
  xor xor_108 (xor_108_out, xor_104_out, \CRC编码 [3]);
  xor xor_109 (xor_109_out, xor_105_out, \CRC编码 [2]);
  xor xor_110 (xor_110_out, xor_106_out, \CRC编码 [1]);
  xor xor_111 (xor_111_out, xor_107_out, \CRC编码 [0]);
  \CRC解码器  \crc解码器_1  (
    .g5(xor_103_out), .g4(xor_108_out), .g3(xor_109_out), .g2(xor_110_out), .g1(xor_111_out),
    .d1(\crc解码器_1_d1 ), .d2(\crc解码器_1_d2 ), .d3(\crc解码器_1_d3 ), .d4(\crc解码器_1_d4 ), .d5(\crc解码器_1_d5 ),
    .d6(\crc解码器_1_d6 ), .d7(\crc解码器_1_d7 ), .d8(\crc解码器_1_d8 ), .d9(\crc解码器_1_d9 ), .d10(\crc解码器_1_d10 ),
    .d11(\crc解码器_1_d11 ), .d12(\crc解码器_1_d12 ), .d13(\crc解码器_1_d13 ), .d14(\crc解码器_1_d14 ),
    .d15(\crc解码器_1_d15 ), .d16(\crc解码器_1_d16 ), .r1(\crc解码器_1_r1 ), .r2(\crc解码器_1_r2 ), .r3(\crc解码器_1_r3 ),
    .r4(\crc解码器_1_r4 ), .r5(\crc解码器_1_r5 ));
  // XOR_Gate xor_112 has open pins: in0=\crc解码器_1_r5 , in1=\CRC编码 [4], out=open
  // XOR_Gate xor_113 has open pins: in0=\crc解码器_1_r4 , in1=\CRC编码 [3], out=open
  // XOR_Gate xor_114 has open pins: in0=\crc解码器_1_r3 , in1=\CRC编码 [2], out=open
  // XOR_Gate xor_115 has open pins: in0=\crc解码器_1_r2 , in1=\CRC编码 [1], out=open
  // XOR_Gate xor_116 has open pins: in0=\crc解码器_1_r1 , in1=\CRC编码 [0], out=open
  xor xor_117 (\纠错后数据 [15], \crc解码器_1_d16 , \CRC编码 [21]);
  xor xor_118 (\纠错后数据 [14], \crc解码器_1_d15 , \CRC编码 [20]);
  xor xor_119 (\纠错后数据 [13], \crc解码器_1_d14 , \CRC编码 [19]);
  xor xor_120 (\纠错后数据 [12], \crc解码器_1_d13 , \CRC编码 [18]);
  xor xor_121 (\纠错后数据 [11], \crc解码器_1_d12 , \CRC编码 [17]);
  xor xor_122 (\纠错后数据 [10], \crc解码器_1_d11 , \CRC编码 [16]);
  xor xor_123 (\纠错后数据 [9], \crc解码器_1_d10 , \CRC编码 [15]);
  xor xor_124 (\纠错后数据 [8], \crc解码器_1_d9 , \CRC编码 [14]);
  xor xor_125 (\纠错后数据 [7], \crc解码器_1_d8 , \CRC编码 [13]);
  xor xor_126 (\纠错后数据 [6], \crc解码器_1_d7 , \CRC编码 [12]);
  xor xor_127 (\纠错后数据 [5], \crc解码器_1_d6 , \CRC编码 [11]);
  xor xor_128 (\纠错后数据 [4], \crc解码器_1_d5 , \CRC编码 [10]);
  xor xor_129 (\纠错后数据 [3], \crc解码器_1_d4 , \CRC编码 [9]);
  xor xor_130 (\纠错后数据 [2], \crc解码器_1_d3 , \CRC编码 [8]);
  xor xor_131 (\纠错后数据 [1], \crc解码器_1_d2 , \CRC编码 [7]);
  xor xor_132 (\纠错后数据 [0], \crc解码器_1_d1 , \CRC编码 [6]);

  // Other names for the same wires on the sheet: CRC[21:0] = \CRC编码 ; r1 = \CRC编码 [0]; r2 = \CRC编码 [1];
  //   r3 = \CRC编码 [2]; r4 = \CRC编码 [3]; r5 = \CRC编码 [4]; r6 = \CRC编码 [5]; D1 = \CRC编码 [6]; D2 = \CRC编码 [7];
  //   D3 = \CRC编码 [8]; D4 = \CRC编码 [9]; D5 = \CRC编码 [10]; D6 = \CRC编码 [11]; D7 = \CRC编码 [12]; D8 = \CRC编码 [13];
  //   D9 = \CRC编码 [14]; D10 = \CRC编码 [15]; D11 = \CRC编码 [16]; D12 = \CRC编码 [17]; D13 = \CRC编码 [18]; D14 = \CRC编码 [19];
  //   D15 = \CRC编码 [20]; D16 = \CRC编码 [21]; 总校验位错 = \_1位错 

  // Notes on the sheet:
  //   输入引脚区
  //   输出引脚区
  //   注意异或门需要设置多输入行为：奇数个1时输出为1，否则功能不正确
  //   电路功能：
  //   请勿增改引脚，请勿修改子电路封装
  //   输入：22位CRC编码；输出：纠错后的数据、错误模式
  //   请在下方利用上方输入输出引脚的隧道信号构建电路，ctrl+d复制选择部件
  //   实现22位海CRC编码的数据解码，能判断1位错，2位错，无错误，1位错自动纠错。
endmodule

module \偶校验传输测试  (
);

  wire and_1_out, comparator_1_eq, \偶校验检错_1_检错位 , \时钟_2_out , \时钟_out ;
  wire [6:0] \国标转区位码_1_位号 , \国标转区位码_1_区号 , \国标转区位码_2_位号 , \国标转区位码_2_区号 ;
  wire [7:0] counter_1_q;
  wire [15:0] \发送 , \接收 ;
  wire [16:0] \n17位随机干扰_1_加扰后数据 , \n17位随机干扰_1_随机加扰屏蔽字 , \偶校验编码_1_偶校验编码 ;
  wire [31:0] \字库_1_p3 , \字库_1_p4 , \字库_1_p5 , \字库_1_p6 , \字库_1_p7 , \字库_1_p8 , \字库_1_p9 , \字库_1_p10 ,
       \字库_1_p11 , \字库_1_p12 , \字库_1_p13 , \字库_1_p14 , \字库_1_p15 , \字库_1_p16 , \字库_1_p17 , \字库_1_p18 ,
       \字库_1_p19 , \字库_1_p20 , \字库_1_p21 , \字库_1_p22 , \字库_1_p23 , \字库_1_p24 , \字库_1_p25 , \字库_1_p26 ,
       \字库_1_p27 , \字库_1_p28 , \字库_1_p29 , \字库_1_p30 , \字库_1_p31 , \字库_1_p32 , \字库_1_p33 , \字库_1_p34 ,
       \字库_2_p3 , \字库_2_p4 , \字库_2_p5 , \字库_2_p6 , \字库_2_p7 , \字库_2_p8 , \字库_2_p9 , \字库_2_p10 , \字库_2_p11 ,
       \字库_2_p12 , \字库_2_p13 , \字库_2_p14 , \字库_2_p15 , \字库_2_p16 , \字库_2_p17 , \字库_2_p18 , \字库_2_p19 ,
       \字库_2_p20 , \字库_2_p21 , \字库_2_p22 , \字库_2_p23 , \字库_2_p24 , \字库_2_p25 , \字库_2_p26 , \字库_2_p27 ,
       \字库_2_p28 , \字库_2_p29 , \字库_2_p30 , \字库_2_p31 , \字库_2_p32 , \字库_2_p33 , \字库_2_p34 ;

  Counter #(.width(8), .max('hff), .ongoal("wrap"), .trigger("rising"), .behavior("old")) counter_1 (
    .Q(counter_1_q), .clk(\时钟_out ));  // open: load, D, count, carry, clr, preset
  Clock #(.highDuration(1), .lowDuration(1)) \u_时钟  (.out(\时钟_out ));
  \国标转区位码  \u_国标转区位码_1  (.\位号 (\国标转区位码_1_位号 ), .\区号 (\国标转区位码_1_区号 ), .GB2312(\发送 ));
  ROM #(.addrWidth(8), .dataWidth(16), .Select("high")) rom_1 (.addr(counter_1_q), .data(\发送 ));
  // 字库 字库_1: pin names not known; wires that end beside it: \国标转区位码_1_区号 , \国标转区位码_1_位号 , \字库_1_p3 , \字库_1_p4 , \字库_1_p5 , \字库_1_p6 , \字库_1_p7 , \字库_1_p8 , \字库_1_p9 , \字库_1_p10 , \字库_1_p11 , \字库_1_p12 , \字库_1_p13 , \字库_1_p14 , \字库_1_p15 , \字库_1_p16 , \字库_1_p17 , \字库_1_p18 , \字库_1_p19 , \字库_1_p20 , \字库_1_p21 , \字库_1_p22 , \字库_1_p23 , \字库_1_p24 , \字库_1_p25 , \字库_1_p26 , \字库_1_p27 , \字库_1_p28 , \字库_1_p29 , \字库_1_p30 , \字库_1_p31 , \字库_1_p32 , \字库_1_p33 , \字库_1_p34 
  DotMatrix #(.inputtype("row"), .matrixcols(32), .matrixrows(32), .persist(0), .dotshape("circle")) dotmatrix_1 (
    .row0(\字库_1_p3 ), .row1(\字库_1_p4 ), .row2(\字库_1_p5 ), .row3(\字库_1_p6 ), .row4(\字库_1_p7 ),
    .row5(\字库_1_p8 ), .row6(\字库_1_p9 ), .row7(\字库_1_p10 ), .row8(\字库_1_p11 ), .row9(\字库_1_p12 ),
    .row10(\字库_1_p13 ), .row11(\字库_1_p14 ), .row12(\字库_1_p15 ), .row13(\字库_1_p16 ), .row14(\字库_1_p17 ),
    .row15(\字库_1_p18 ), .row16(\字库_1_p19 ), .row17(\字库_1_p20 ), .row18(\字库_1_p21 ), .row19(\字库_1_p22 ),
    .row20(\字库_1_p23 ), .row21(\字库_1_p24 ), .row22(\字库_1_p25 ), .row23(\字库_1_p26 ), .row24(\字库_1_p27 ),
    .row25(\字库_1_p28 ), .row26(\字库_1_p29 ), .row27(\字库_1_p30 ), .row28(\字库_1_p31 ), .row29(\字库_1_p32 ),
    .row30(\字库_1_p33 ), .row31(\字库_1_p34 ));
  // Probe on \发送 
  \偶校验编码  \u_偶校验编码_1  (.\原始数据 (\发送 ), .\偶校验编码 (\偶校验编码_1_偶校验编码 ));
  // Probe on \偶校验编码_1_偶校验编码 
  // Probe on \偶校验编码_1_偶校验编码 
  // Probe on \n17位随机干扰_1_随机加扰屏蔽字 
  \_17位随机干扰  \u_17位随机干扰_1  (
    .\_17位输入 (\偶校验编码_1_偶校验编码 ), .\随机加扰屏蔽字 (\n17位随机干扰_1_随机加扰屏蔽字 ), .\加扰后数据 (\n17位随机干扰_1_加扰后数据 ),
    .CLK(\时钟_2_out ));
  Clock #(.highDuration(1), .lowDuration(1)) \u_时钟_2  (.out(\时钟_2_out ));
  // Probe on \n17位随机干扰_1_加扰后数据 
  // Probe on \n17位随机干扰_1_加扰后数据 
  \国标转区位码  \u_国标转区位码_2  (.\位号 (\国标转区位码_2_位号 ), .\区号 (\国标转区位码_2_区号 ), .GB2312(\接收 ));
  // 字库 字库_2: pin names not known; wires that end beside it: \国标转区位码_2_区号 , \国标转区位码_2_位号 , \字库_2_p3 , \字库_2_p4 , \字库_2_p5 , \字库_2_p6 , \字库_2_p7 , \字库_2_p8 , \字库_2_p9 , \字库_2_p10 , \字库_2_p11 , \字库_2_p12 , \字库_2_p13 , \字库_2_p14 , \字库_2_p15 , \字库_2_p16 , \字库_2_p17 , \字库_2_p18 , \字库_2_p19 , \字库_2_p20 , \字库_2_p21 , \字库_2_p22 , \字库_2_p23 , \字库_2_p24 , \字库_2_p25 , \字库_2_p26 , \字库_2_p27 , \字库_2_p28 , \字库_2_p29 , \字库_2_p30 , \字库_2_p31 , \字库_2_p32 , \字库_2_p33 , \字库_2_p34 
  DotMatrix #(.inputtype("row"), .matrixcols(32), .matrixrows(32), .persist(0), .dotshape("circle")) dotmatrix_2 (
    .row0(\字库_2_p3 ), .row1(\字库_2_p4 ), .row2(\字库_2_p5 ), .row3(\字库_2_p6 ), .row4(\字库_2_p7 ),
    .row5(\字库_2_p8 ), .row6(\字库_2_p9 ), .row7(\字库_2_p10 ), .row8(\字库_2_p11 ), .row9(\字库_2_p12 ),
    .row10(\字库_2_p13 ), .row11(\字库_2_p14 ), .row12(\字库_2_p15 ), .row13(\字库_2_p16 ), .row14(\字库_2_p17 ),
    .row15(\字库_2_p18 ), .row16(\字库_2_p19 ), .row17(\字库_2_p20 ), .row18(\字库_2_p21 ), .row19(\字库_2_p22 ),
    .row20(\字库_2_p23 ), .row21(\字库_2_p24 ), .row22(\字库_2_p25 ), .row23(\字库_2_p26 ), .row24(\字库_2_p27 ),
    .row25(\字库_2_p28 ), .row26(\字库_2_p29 ), .row27(\字库_2_p30 ), .row28(\字库_2_p31 ), .row29(\字库_2_p32 ),
    .row30(\字库_2_p33 ), .row31(\字库_2_p34 ));
  LED #(.active("true")) \u_检错位  (.in(\偶校验检错_1_检错位 ));
  \偶校验检错  \u_偶校验检错_1  (.\检错位 (\偶校验检错_1_检错位 ), .\偶校验编码 (\n17位随机干扰_1_加扰后数据 ), .\数据位 (\接收 ));
  Comparator #(.width(16), .mode("twosComplement")) comparator_1 (
    .a(\发送 ), .b(\接收 ), .eq(comparator_1_eq));  // open: gt, lt
  // Probe on \接收 
  and and_1 (and_1_out, ~comparator_1_eq, ~\偶校验检错_1_检错位 );  // AND_Gate
  LED #(.active("true")) \u_数据正确  (.in(comparator_1_eq));
  LED #(.active("true")) \u_误报  (.in(and_1_out));

  // Notes on the sheet:
  //   发送方
  //   计数器
  //   发送方
  //   汉字显示
  //   GB2312
  //   contents of rom_1 (hex, n*v repeats v):
  //   bbaa d6d0 bfc6 bcbc b4f3 d1a7 cac7 b9fa bcd2 bdcc d3fd b2bf d6b1 caf4 b5c4 c8ab b9fa d6d8 b5e3 b4f3
  //   d1a7 a3ac d3c9 d4ad bbaa d6d0 c0ed b9a4 b4f3 d1a7 a1a2 cdac bcc3 d2bd bfc6 b4f3 d1a7 a1a2 cee4 baba
  //   b3c7 cad0 bda8 c9e8 d1a7 d4ba d3da a3b2 a3b0 a3b0 a3b0 c4ea a3b5 d4c2 a3b2 a3b6 c8d5 bacf b2a2 b3c9
  //   c1a2 a3ac cac7 cad7 c5fa c1d0 c8eb b9fa bcd2 a1b0 a3b2 a3b1 a3b1 b9a4 b3cc a1b1 d6d8 b5e3 bda8 c9e8
  //   bacd b9fa bcd2 a1b0 a3b9 a3b8 a3b5 b9a4 b3cc a1b1 bda8 c9e8 b8df d0a3 d6ae d2bb a1a3 d1a7 d0a3 d0a3
  //   d4b0 d5bc b5d8 c6df c7a7 d3e0 c4b6 a3ac d4b0 c4da caf7 c4be b4d0 dcd7 a3ac b1cc b2dd c8e7 d2f0 a3ac
  //   bbb7 beb3 d3c5 d1c5 a3ac beb0 c9ab d0e3 c0f6 a3ac c2cc bbaf b8b2 b8c7 c2ca 3732 25a3 acb1 bbd3 fece
  //   aaa1 b0c9 adc1 d6ca bdb4 f3d1 a7a1 b1a1
  //   发送方在ROM预存了一段中文文字，通过计数器驱动电路每个时钟传输一个汉字到接收方
  //   用户实现了国标转区位码电路后，可在中间窗口观察发送方和接收方汉字显示是否一致以观察检错性能
  //   电路功能：测试偶校验编解码电路正确性，仿真时设置加扰控制位和原始数据，按CTRL+T触发不同的干扰，检验编解码电路功能
  //   偶校验编解码传输电路
  //   接收方
  //   汉字显示
  //   Ctrl+T  Ctrl+K 驱动时钟触发随机干扰变化
  //   接收方
  //   请将时钟频率调到8Hz
endmodule

module \海明传输测试1  (
  input  [15:0] \原始数据 ,
  input  [1:0] \加扰控制 
);

  wire clock_1_out, comparator_1_eq, \海明解码_1__0位错 , \海明解码_1__1位错 , \海明解码_1__2位错 ;
  wire [15:0] \海明解码_1_纠错后数据 ;
  wire [21:0] \n22位随机干扰_1_加扰后数据 , \n22位随机干扰_1_随机加扰屏蔽字 , \海明编码_1_海明码 ;

  // Probe on \原始数据 
  // Probe on \海明编码_1_海明码 
  \海明编码  \u_海明编码_1  (.\原始数据 (\原始数据 ), .\海明码 (\海明编码_1_海明码 ));
  // Probe on \海明编码_1_海明码 
  // Probe on \n22位随机干扰_1_随机加扰屏蔽字 
  Clock #(.highDuration(1), .lowDuration(1)) clock_1 (.out(clock_1_out));
  // Probe on \n22位随机干扰_1_加扰后数据 
  \_22位随机干扰  \u_22位随机干扰_1  (
    .\加扰模式 (\加扰控制 ), .\随机加扰屏蔽字 (\n22位随机干扰_1_随机加扰屏蔽字 ), .\_22位输入 (\海明编码_1_海明码 ), .\加扰后数据 (\n22位随机干扰_1_加扰后数据 ),
    .CLK(clock_1_out));  // open: 增加三位错, EDU
  // Probe on \n22位随机干扰_1_加扰后数据 
  LED #(.active("true")) \u_两位错  (.in(\海明解码_1__2位错 ));
  LED #(.active("true")) OK (.in(\海明解码_1__0位错 ));
  LED #(.active("true")) \u_一位错  (.in(\海明解码_1__1位错 ));
  \海明解码  \u_海明解码_1  (
    .\_1位错 (\海明解码_1__1位错 ), .\_2位错 (\海明解码_1__2位错 ), .\_0位错 (\海明解码_1__0位错 ), .\海明码 (\n22位随机干扰_1_加扰后数据 ),
    .\纠错后数据 (\海明解码_1_纠错后数据 ));
  // Probe on \海明解码_1_纠错后数据 
  LED #(.active("true")) \u_数据正确  (.in(comparator_1_eq));
  Comparator #(.width(16), .mode("twosComplement")) comparator_1 (
    .a(\原始数据 ), .b(\海明解码_1_纠错后数据 ), .eq(comparator_1_eq));  // open: gt, lt

  // Notes on the sheet:
  //   发送方
  //   Ctrl+T 驱动时钟触发随机干扰变化
  //   海明编解码传输电路
  //   电路功能：测试海明编解码电路正确性，仿真时设置加扰控制位和原始数据，按CTRL+T触发不同的干扰，检验编解码电路功能
  //   加扰控制00：不加扰  01:1位加扰 10:2位加扰 11：随机加扰
  //   接收方
endmodule

module \海明传输测试2  (
  input  [1:0] \加扰控制 
);

  wire CLK, comparator_1_eq, \海明解码_1__0位错 , \海明解码_1__1位错 , \海明解码_1__2位错 ;
  wire [6:0] \国标转区位码_1_位号 , \国标转区位码_1_区号 , \国标转区位码_2_位号 , \国标转区位码_2_区号 ;
  wire [7:0] counter_1_q;
  wire [15:0] \发送 , \接收 ;
  wire [21:0] \n22位随机干扰_1_加扰后数据 , \n22位随机干扰_1_随机加扰屏蔽字 , \海明编码_1_海明码 ;
  wire [31:0] \字库_1_p3 , \字库_1_p4 , \字库_1_p5 , \字库_1_p6 , \字库_1_p7 , \字库_1_p8 , \字库_1_p9 , \字库_1_p10 ,
       \字库_1_p11 , \字库_1_p12 , \字库_1_p13 , \字库_1_p14 , \字库_1_p15 , \字库_1_p16 , \字库_1_p17 , \字库_1_p18 ,
       \字库_1_p19 , \字库_1_p20 , \字库_1_p21 , \字库_1_p22 , \字库_1_p23 , \字库_1_p24 , \字库_1_p25 , \字库_1_p26 ,
       \字库_1_p27 , \字库_1_p28 , \字库_1_p29 , \字库_1_p30 , \字库_1_p31 , \字库_1_p32 , \字库_1_p33 , \字库_1_p34 ,
       \字库_2_p3 , \字库_2_p4 , \字库_2_p5 , \字库_2_p6 , \字库_2_p7 , \字库_2_p8 , \字库_2_p9 , \字库_2_p10 , \字库_2_p11 ,
       \字库_2_p12 , \字库_2_p13 , \字库_2_p14 , \字库_2_p15 , \字库_2_p16 , \字库_2_p17 , \字库_2_p18 , \字库_2_p19 ,
       \字库_2_p20 , \字库_2_p21 , \字库_2_p22 , \字库_2_p23 , \字库_2_p24 , \字库_2_p25 , \字库_2_p26 , \字库_2_p27 ,
       \字库_2_p28 , \字库_2_p29 , \字库_2_p30 , \字库_2_p31 , \字库_2_p32 , \字库_2_p33 , \字库_2_p34 ;

  Counter #(.width(8), .max('hff), .ongoal("wrap"), .trigger("rising"), .behavior("old")) counter_1 (
    .Q(counter_1_q), .clk(CLK));  // open: load, D, count, carry, clr, preset
  Clock #(.highDuration(1), .lowDuration(1)) \u_时钟  (.out(CLK));
  \国标转区位码  \u_国标转区位码_1  (.\位号 (\国标转区位码_1_位号 ), .\区号 (\国标转区位码_1_区号 ), .GB2312(\发送 ));
  // 字库 字库_1: pin names not known; wires that end beside it: \国标转区位码_1_区号 , \国标转区位码_1_位号 , \字库_1_p3 , \字库_1_p4 , \字库_1_p5 , \字库_1_p6 , \字库_1_p7 , \字库_1_p8 , \字库_1_p9 , \字库_1_p10 , \字库_1_p11 , \字库_1_p12 , \字库_1_p13 , \字库_1_p14 , \字库_1_p15 , \字库_1_p16 , \字库_1_p17 , \字库_1_p18 , \字库_1_p19 , \字库_1_p20 , \字库_1_p21 , \字库_1_p22 , \字库_1_p23 , \字库_1_p24 , \字库_1_p25 , \字库_1_p26 , \字库_1_p27 , \字库_1_p28 , \字库_1_p29 , \字库_1_p30 , \字库_1_p31 , \字库_1_p32 , \字库_1_p33 , \字库_1_p34 
  DotMatrix #(.inputtype("row"), .matrixcols(32), .matrixrows(32), .persist(0), .dotshape("circle")) dotmatrix_1 (
    .row0(\字库_1_p3 ), .row1(\字库_1_p4 ), .row2(\字库_1_p5 ), .row3(\字库_1_p6 ), .row4(\字库_1_p7 ),
    .row5(\字库_1_p8 ), .row6(\字库_1_p9 ), .row7(\字库_1_p10 ), .row8(\字库_1_p11 ), .row9(\字库_1_p12 ),
    .row10(\字库_1_p13 ), .row11(\字库_1_p14 ), .row12(\字库_1_p15 ), .row13(\字库_1_p16 ), .row14(\字库_1_p17 ),
    .row15(\字库_1_p18 ), .row16(\字库_1_p19 ), .row17(\字库_1_p20 ), .row18(\字库_1_p21 ), .row19(\字库_1_p22 ),
    .row20(\字库_1_p23 ), .row21(\字库_1_p24 ), .row22(\字库_1_p25 ), .row23(\字库_1_p26 ), .row24(\字库_1_p27 ),
    .row25(\字库_1_p28 ), .row26(\字库_1_p29 ), .row27(\字库_1_p30 ), .row28(\字库_1_p31 ), .row29(\字库_1_p32 ),
    .row30(\字库_1_p33 ), .row31(\字库_1_p34 ));
  ROM #(.addrWidth(8), .dataWidth(16), .Select("high")) rom_1 (.addr(counter_1_q), .data(\发送 ));
  // Probe on \发送 
  // Probe on \海明编码_1_海明码 
  \海明编码  \u_海明编码_1  (.\原始数据 (\发送 ), .\海明码 (\海明编码_1_海明码 ));
  // Probe on \海明编码_1_海明码 
  // Probe on \n22位随机干扰_1_随机加扰屏蔽字 
  \_22位随机干扰  \u_22位随机干扰_1  (
    .\加扰模式 (\加扰控制 ), .\随机加扰屏蔽字 (\n22位随机干扰_1_随机加扰屏蔽字 ), .\_22位输入 (\海明编码_1_海明码 ), .\加扰后数据 (\n22位随机干扰_1_加扰后数据 ),
    .CLK(CLK));  // open: 增加三位错, EDU
  \国标转区位码  \u_国标转区位码_2  (.\位号 (\国标转区位码_2_位号 ), .\区号 (\国标转区位码_2_区号 ), .GB2312(\接收 ));
  // Probe on \n22位随机干扰_1_加扰后数据 
  // Probe on \n22位随机干扰_1_加扰后数据 
  // 字库 字库_2: pin names not known; wires that end beside it: \国标转区位码_2_区号 , \国标转区位码_2_位号 , \字库_2_p3 , \字库_2_p4 , \字库_2_p5 , \字库_2_p6 , \字库_2_p7 , \字库_2_p8 , \字库_2_p9 , \字库_2_p10 , \字库_2_p11 , \字库_2_p12 , \字库_2_p13 , \字库_2_p14 , \字库_2_p15 , \字库_2_p16 , \字库_2_p17 , \字库_2_p18 , \字库_2_p19 , \字库_2_p20 , \字库_2_p21 , \字库_2_p22 , \字库_2_p23 , \字库_2_p24 , \字库_2_p25 , \字库_2_p26 , \字库_2_p27 , \字库_2_p28 , \字库_2_p29 , \字库_2_p30 , \字库_2_p31 , \字库_2_p32 , \字库_2_p33 , \字库_2_p34 
  LED #(.active("true")) OK (.in(\海明解码_1__0位错 ));
  LED #(.active("true")) \u_一位错  (.in(\海明解码_1__1位错 ));
  LED #(.active("true")) \u_两位错  (.in(\海明解码_1__2位错 ));
  DotMatrix #(.inputtype("row"), .matrixcols(32), .matrixrows(32), .persist(0), .dotshape("circle")) dotmatrix_2 (
    .row0(\字库_2_p3 ), .row1(\字库_2_p4 ), .row2(\字库_2_p5 ), .row3(\字库_2_p6 ), .row4(\字库_2_p7 ),
    .row5(\字库_2_p8 ), .row6(\字库_2_p9 ), .row7(\字库_2_p10 ), .row8(\字库_2_p11 ), .row9(\字库_2_p12 ),
    .row10(\字库_2_p13 ), .row11(\字库_2_p14 ), .row12(\字库_2_p15 ), .row13(\字库_2_p16 ), .row14(\字库_2_p17 ),
    .row15(\字库_2_p18 ), .row16(\字库_2_p19 ), .row17(\字库_2_p20 ), .row18(\字库_2_p21 ), .row19(\字库_2_p22 ),
    .row20(\字库_2_p23 ), .row21(\字库_2_p24 ), .row22(\字库_2_p25 ), .row23(\字库_2_p26 ), .row24(\字库_2_p27 ),
    .row25(\字库_2_p28 ), .row26(\字库_2_p29 ), .row27(\字库_2_p30 ), .row28(\字库_2_p31 ), .row29(\字库_2_p32 ),
    .row30(\字库_2_p33 ), .row31(\字库_2_p34 ));
  \海明解码  \u_海明解码_1  (
    .\_1位错 (\海明解码_1__1位错 ), .\_2位错 (\海明解码_1__2位错 ), .\_0位错 (\海明解码_1__0位错 ), .\海明码 (\n22位随机干扰_1_加扰后数据 ),
    .\纠错后数据 (\接收 ));
  // Probe on \接收 
  Comparator #(.width(16), .mode("twosComplement")) comparator_1 (
    .a(\发送 ), .b(\接收 ), .eq(comparator_1_eq));  // open: gt, lt
  LED #(.active("true")) \u_数据正确  (.in(comparator_1_eq));

  // Notes on the sheet:
  //   发送方
  //   计数器
  //   发送方
  //   汉字显示
  //   GB2312
  //   contents of rom_1 (hex, n*v repeats v):
  //   bbaa d6d0 bfc6 bcbc b4f3 d1a7 cac7 b9fa bcd2 bdcc d3fd b2bf d6b1 caf4 b5c4 c8ab b9fa d6d8 b5e3 b4f3
  //   d1a7 a3ac d3c9 d4ad bbaa d6d0 c0ed b9a4 b4f3 d1a7 a1a2 cdac bcc3 d2bd bfc6 b4f3 d1a7 a1a2 cee4 baba
  //   b3c7 cad0 bda8 c9e8 d1a7 d4ba d3da a3b2 a3b0 a3b0 a3b0 c4ea a3b5 d4c2 a3b2 a3b6 c8d5 bacf b2a2 b3c9
  //   c1a2 a3ac cac7 cad7 c5fa c1d0 c8eb b9fa bcd2 a1b0 a3b2 a3b1 a3b1 b9a4 b3cc a1b1 d6d8 b5e3 bda8 c9e8
  //   bacd b9fa bcd2 a1b0 a3b9 a3b8 a3b5 b9a4 b3cc a1b1 bda8 c9e8 b8df d0a3 d6ae d2bb a1a3 d1a7 d0a3 d0a3
  //   d4b0 d5bc b5d8 c6df c7a7 d3e0 c4b6 a3ac d4b0 c4da caf7 c4be b4d0 dcd7 a3ac b1cc b2dd c8e7 d2f0 a3ac
  //   bbb7 beb3 d3c5 d1c5 a3ac beb0 c9ab d0e3 c0f6 a3ac c2cc bbaf b8b2 b8c7 c2ca 3732 25a3 acb1 bbd3 fece
  //   aaa1 b0c9 adc1 d6ca bdb4 f3d1 a7a1 b1a1
  //   Ctrl+T 驱动时钟触发随机干扰变化
  //   发送方在ROM预存了一段中文文字，通过计数器驱动电路每个时钟传输一个汉字到接收方
  //   电路功能：测试海明编解码电路正确性，仿真时设置加扰控制位和原始数据，按CTRL+T触发不同的干扰，检验编解码电路功能
  //   用户实现了国标转区位码电路后，可在中间窗口观察发送方和接收方汉字显示是否一致以观察海明检错纠错性能
  //   海明编解码传输电路
  //   接收方
  //   汉字显示
  //   Ctrl+T 驱动时钟触发随机干扰变化
  //   加扰控制00：不加扰  01:1位加扰 10:2位加扰 11：随机加扰
  //   加扰控制00：不加扰  01:1位加扰 10:2位加扰 11：随机加扰
  //   接收方
  //   请将时钟频率调到8Hz
endmodule

// Hamming
module \海明编码流水传输  (
  input  \加噪 ,
  input  EDU,
  output _1err,
  output _2err,
  output clr2,
  output clr3,
  output clr4,
  output en5
);

  wire CLK, \n16位流水接口_1_传输状态out_表明当前传输数据有效 , \n22位流水接口_1_传输状态out_表明当前传输数据有效 ,
       \n22位流水接口_2_传输状态out_表明当前传输数据有效 , not_1_out, \海明解码_1__0位错 ;
  wire [6:0] \国标转区位码_1_位号 , \国标转区位码_1_区号 , \字库_2_p1 , \字库_2_p2 ;
  wire [7:0] adder_1_out, CNT, multiplexer_1_out;
  wire [15:0] \n16位流水接口_1_dout16 , \发送 , \接收 , \海明解码_1_纠错后数据 ;
  wire [21:0] \n22位流水接口_1_dout22 , \n22位流水接口_2_dout22 , \n22位随机干扰_1_加扰后数据 , \海明编码_1_海明码 ;
  wire [31:0] \字库_1_p3 , \字库_1_p4 , \字库_1_p5 , \字库_1_p6 , \字库_1_p7 , \字库_1_p8 , \字库_1_p9 , \字库_1_p10 ,
       \字库_1_p11 , \字库_1_p12 , \字库_1_p13 , \字库_1_p14 , \字库_1_p15 , \字库_1_p16 , \字库_1_p17 , \字库_1_p18 ,
       \字库_1_p19 , \字库_1_p20 , \字库_1_p21 , \字库_1_p22 , \字库_1_p23 , \字库_1_p24 , \字库_1_p25 , \字库_1_p26 ,
       \字库_1_p27 , \字库_1_p28 , \字库_1_p29 , \字库_1_p30 , \字库_1_p31 , \字库_1_p32 , \字库_1_p33 , \字库_1_p34 ,
       \字库_2_p3 , \字库_2_p4 , \字库_2_p5 , \字库_2_p6 , \字库_2_p7 , \字库_2_p8 , \字库_2_p9 , \字库_2_p10 , \字库_2_p11 ,
       \字库_2_p12 , \字库_2_p13 , \字库_2_p14 , \字库_2_p15 , \字库_2_p16 , \字库_2_p17 , \字库_2_p18 , \字库_2_p19 ,
       \字库_2_p20 , \字库_2_p21 , \字库_2_p22 , \字库_2_p23 , \字库_2_p24 , \字库_2_p25 , \字库_2_p26 , \字库_2_p27 ,
       \字库_2_p28 , \字库_2_p29 , \字库_2_p30 , \字库_2_p31 , \字库_2_p32 , \字库_2_p33 , \字库_2_p34 ;

  Multiplexer #(.select(1), .width(8), .disabled("Z"), .enable("false")) multiplexer_1 (
    .in0(8'h1), .in1(8'hfd), .out(multiplexer_1_out), .sel(clr2));
  Register #(.width(8), .trigger("rising"), .Select("low")) register_1 (
    .D(adder_1_out), .Q(CNT), .clk(CLK));  // open: en, clr
  Clock #(.highDuration(1), .lowDuration(1)) \u_时钟  (.out(CLK));
  \国标转区位码  \u_国标转区位码_1  (.\位号 (\国标转区位码_1_位号 ), .\区号 (\国标转区位码_1_区号 ), .GB2312(\发送 ));
  Adder #(.width(8)) adder_1 (.a(multiplexer_1_out), .b(CNT), .out(adder_1_out));  // open: cin, cout
  // 字库 字库_1: pin names not known; wires that end beside it: \国标转区位码_1_区号 , \国标转区位码_1_位号 , \字库_1_p3 , \字库_1_p4 , \字库_1_p5 , \字库_1_p6 , \字库_1_p7 , \字库_1_p8 , \字库_1_p9 , \字库_1_p10 , \字库_1_p11 , \字库_1_p12 , \字库_1_p13 , \字库_1_p14 , \字库_1_p15 , \字库_1_p16 , \字库_1_p17 , \字库_1_p18 , \字库_1_p19 , \字库_1_p20 , \字库_1_p21 , \字库_1_p22 , \字库_1_p23 , \字库_1_p24 , \字库_1_p25 , \字库_1_p26 , \字库_1_p27 , \字库_1_p28 , \字库_1_p29 , \字库_1_p30 , \字库_1_p31 , \字库_1_p32 , \字库_1_p33 , \字库_1_p34 
  DotMatrix #(.inputtype("row"), .matrixcols(32), .matrixrows(32), .persist(0), .dotshape("circle")) dotmatrix_1 (
    .row0(\字库_1_p3 ), .row1(\字库_1_p4 ), .row2(\字库_1_p5 ), .row3(\字库_1_p6 ), .row4(\字库_1_p7 ),
    .row5(\字库_1_p8 ), .row6(\字库_1_p9 ), .row7(\字库_1_p10 ), .row8(\字库_1_p11 ), .row9(\字库_1_p12 ),
    .row10(\字库_1_p13 ), .row11(\字库_1_p14 ), .row12(\字库_1_p15 ), .row13(\字库_1_p16 ), .row14(\字库_1_p17 ),
    .row15(\字库_1_p18 ), .row16(\字库_1_p19 ), .row17(\字库_1_p20 ), .row18(\字库_1_p21 ), .row19(\字库_1_p22 ),
    .row20(\字库_1_p23 ), .row21(\字库_1_p24 ), .row22(\字库_1_p25 ), .row23(\字库_1_p26 ), .row24(\字库_1_p27 ),
    .row25(\字库_1_p28 ), .row26(\字库_1_p29 ), .row27(\字库_1_p30 ), .row28(\字库_1_p31 ), .row29(\字库_1_p32 ),
    .row30(\字库_1_p33 ), .row31(\字库_1_p34 ));
  ROM #(.addrWidth(8), .dataWidth(16), .Select("high")) rom_1 (.addr(CNT), .data(\发送 ));
  \_16位流水接口  \u_16位流水接口_1  (
    .Din16(\发送 ), .\传输状态In_表明当前传输数据有效 (1'b1), .CLK(CLK), .Dout16(\n16位流水接口_1_dout16 ),
    .\传输状态Out_表明当前传输数据有效 (\n16位流水接口_1_传输状态out_表明当前传输数据有效 ), .\同步清零_气泡_高电平有效 (clr2));  // open: 使能端_低电平有效_stall_高电平有效
  \海明编码  \u_海明编码_1  (.\原始数据 (\n16位流水接口_1_dout16 ), .\海明码 (\海明编码_1_海明码 ));
  \_22位流水接口  \u_22位流水接口_1  (
    .Din22(\海明编码_1_海明码 ), .\传输状态In_表明当前传输数据有效 (\n16位流水接口_1_传输状态out_表明当前传输数据有效 ), .CLK(CLK),
    .Dout22(\n22位流水接口_1_dout22 ), .\传输状态Out_表明当前传输数据有效 (\n22位流水接口_1_传输状态out_表明当前传输数据有效 ),
    .\同步清零_气泡_高电平有效 (clr2));  // open: 使能端_低电平有效_stall_高电平有效
  \_22位随机干扰  \u_22位随机干扰_1  (
    .\加扰模式 (2'b10), .\_22位输入 (\n22位流水接口_1_dout22 ), .\加扰后数据 (\n22位随机干扰_1_加扰后数据 ), .\增加三位错 (\加噪 ), .CLK(CLK),
    .EDU(EDU));  // open: 随机加扰屏蔽字
  // 字库 字库_2: pin names not known; wires that end beside it: \字库_2_p1 , \字库_2_p2 , \字库_2_p3 , \字库_2_p4 , \字库_2_p5 , \字库_2_p6 , \字库_2_p7 , \字库_2_p8 , \字库_2_p9 , \字库_2_p10 , \字库_2_p11 , \字库_2_p12 , \字库_2_p13 , \字库_2_p14 , \字库_2_p15 , \字库_2_p16 , \字库_2_p17 , \字库_2_p18 , \字库_2_p19 , \字库_2_p20 , \字库_2_p21 , \字库_2_p22 , \字库_2_p23 , \字库_2_p24 , \字库_2_p25 , \字库_2_p26 , \字库_2_p27 , \字库_2_p28 , \字库_2_p29 , \字库_2_p30 , \字库_2_p31 , \字库_2_p32 , \字库_2_p33 , \字库_2_p34 
  \国标转区位码  \u_国标转区位码_2  (.\位号 (\字库_2_p2 ), .\区号 (\字库_2_p1 ), .GB2312(\接收 ));
  \_22位流水接口  \u_22位流水接口_2  (
    .Din22(\n22位随机干扰_1_加扰后数据 ), .\传输状态In_表明当前传输数据有效 (\n22位流水接口_1_传输状态out_表明当前传输数据有效 ), .CLK(CLK),
    .Dout22(\n22位流水接口_2_dout22 ), .\传输状态Out_表明当前传输数据有效 (\n22位流水接口_2_传输状态out_表明当前传输数据有效 ),
    .\同步清零_气泡_高电平有效 (clr2));  // open: 使能端_低电平有效_stall_高电平有效
  DotMatrix #(.inputtype("row"), .matrixcols(32), .matrixrows(32), .persist(0), .dotshape("circle")) dotmatrix_2 (
    .row0(\字库_2_p3 ), .row1(\字库_2_p4 ), .row2(\字库_2_p5 ), .row3(\字库_2_p6 ), .row4(\字库_2_p7 ),
    .row5(\字库_2_p8 ), .row6(\字库_2_p9 ), .row7(\字库_2_p10 ), .row8(\字库_2_p11 ), .row9(\字库_2_p12 ),
    .row10(\字库_2_p13 ), .row11(\字库_2_p14 ), .row12(\字库_2_p15 ), .row13(\字库_2_p16 ), .row14(\字库_2_p17 ),
    .row15(\字库_2_p18 ), .row16(\字库_2_p19 ), .row17(\字库_2_p20 ), .row18(\字库_2_p21 ), .row19(\字库_2_p22 ),
    .row20(\字库_2_p23 ), .row21(\字库_2_p24 ), .row22(\字库_2_p25 ), .row23(\字库_2_p26 ), .row24(\字库_2_p27 ),
    .row25(\字库_2_p28 ), .row26(\字库_2_p29 ), .row27(\字库_2_p30 ), .row28(\字库_2_p31 ), .row29(\字库_2_p32 ),
    .row30(\字库_2_p33 ), .row31(\字库_2_p34 ));
  and and_1 (clr2, _2err, \n22位流水接口_2_传输状态out_表明当前传输数据有效 );
  LED #(.active("true")) \u_一位错  (.in(_1err));
  LED #(.active("true")) \u_两位错  (.in(_2err));
  LED #(.active("true")) \u_无错误  (.in(\海明解码_1__0位错 ));
  \海明解码  \u_海明解码_1  (
    .\_1位错 (_1err), .\_2位错 (_2err), .\_0位错 (\海明解码_1__0位错 ), .\海明码 (\n22位流水接口_2_dout22 ),
    .\纠错后数据 (\海明解码_1_纠错后数据 ));
  not not_1 (not_1_out, \n22位流水接口_2_传输状态out_表明当前传输数据有效 );
  or or_1 (en5, not_1_out, _2err);
  \_16位流水接口  \u_16位流水接口_2  (
    .Din16(\海明解码_1_纠错后数据 ), .\传输状态In_表明当前传输数据有效 (\n22位流水接口_2_传输状态out_表明当前传输数据有效 ), .CLK(CLK), .Dout16(\接收 ),
    .\使能端_低电平有效_stall_高电平有效 (en5));  // open: 传输状态Out_表明当前传输数据有效, 同步清零_气泡_高电平有效
  // Probe on \接收 

  assign clr3 = clr2;
  assign clr4 = clr2;

  // Notes on the sheet:
  //   海明码流水传输电路
  //   寄存器
  //   发送方
  //   汉字显示
  //   加法器
  //   GB2312
  //   1.取数阶段
  //   contents of rom_1 (hex, n*v repeats v):
  //   bbaa d6d0 bfc6 bcbc b4f3 d1a7 cac7 b9fa bcd2 bdcc d3fd b2bf d6b1 caf4 b5c4 c8ab b9fa d6d8 b5e3 b4f3
  //   d1a7 a3ac d3c9 d4ad bbaa d6d0 c0ed b9a4 b4f3 d1a7 a1a2 cdac bcc3 d2bd bfc6 b4f3 d1a7 a1a2 cee4 baba
  //   b3c7 cad0 bda8 c9e8 d1a7 d4ba d3da a3b2 a3b0 a3b0 a3b0 c4ea a3b5 d4c2 a3b2 a3b6 c8d5 bacf b2a2 b3c9
  //   c1a2 a3ac cac7 cad7 c5fa c1d0 c8eb b9fa bcd2 a1b0 a3b2 a3b1 a3b1 b9a4 b3cc a1b1 d6d8 b5e3 bda8 c9e8
  //   bacd b9fa bcd2 a1b0 a3b9 a3b8 a3b5 b9a4 b3cc a1b1 bda8 c9e8 b8df d0a3 d6ae d2bb a1a3 d1a7 d0a3 d0a3
  //   d4b0 d5bc b5d8 c6df c7a7 d3e0 c4b6 a3ac d4b0 c4da caf7 c4be b4d0 dcd7 a3ac b1cc b2dd c8e7 d2f0 a3ac
  //   bbb7 beb3 d3c5 d1c5 a3ac beb0 c9ab d0e3 c0f6 a3ac c2cc bbaf b8b2 b8c7 c2ca 3732 25a3 acb1 bbd3 fece
  //   aaa1 b0c9 adc1 d6ca bdb4 f3d1 a7a1 b1a1
  //   ~使能/Stall
  //   发送方在ROM预存了一段中文文字，通过计数器驱动电路每个时钟传输一个汉字
  //   清零是同步清零，也就是清零使能高电平后还需要时钟
  //   同步清零
  //   用户实现了国标转区位码电路后，可在中间窗口观察发送方和接收方汉字显示是否一致以观察海明检错纠错性能
  //   数据状态：高电平有效
  //   2.编码阶段
  //   如果不控制好使能端，则第三个寄存器一个时钟之后就会填入干扰后的编码，影响2err 的判断
  //   接收方
  //   汉字显示
  //   电路功能：采用流水方式进行数据编码传输，测试海明编码检错纠错能力，当出现2位错时，发送重传信号要求发送方重传，保证接收方按ROM中的地址顺序接受所有汉字
  //   3.传输阶段
  //   4.解码阶段
  //   此电路可帮助学生理解指令流水线工作原理，重传类似指令流水线中的分支指令
  //   en5低电平使能
  //   5.显示阶段
  //   请将时钟频率调到8Hz
  //   Ctrl+ K启动电路自动仿真
  //   EDUCODER在线测试引脚
  //   请勿增删改引脚
  //   方案1：控制使能端
  //   方案2：同时使用2err和数据有效端
endmodule

module \CRC传输测试1  (
  input  [15:0] \原始数据 ,
  input  [1:0] \加扰控制 
);

  wire clock_1_out, comparator_1_eq, \crc解码_1__0位错 , \crc解码_1__1位错 , \crc解码_1__2位错 ;
  wire [15:0] \crc解码_1_纠错后数据 ;
  wire [21:0] \crc编码_1_crc校验码 , \n22位随机干扰_1_加扰后数据 , \n22位随机干扰_1_随机加扰屏蔽字 ;

  // Probe on \原始数据 
  // Probe on \crc编码_1_crc校验码 
  \CRC编码  \crc编码_1  (.\原始数据 (\原始数据 ), .\CRC校验码 (\crc编码_1_crc校验码 ));
  // Probe on \crc编码_1_crc校验码 
  // Probe on \n22位随机干扰_1_随机加扰屏蔽字 
  Clock #(.highDuration(1), .lowDuration(1)) clock_1 (.out(clock_1_out));
  // Probe on \n22位随机干扰_1_加扰后数据 
  \_22位随机干扰  \u_22位随机干扰_1  (
    .\加扰模式 (\加扰控制 ), .\随机加扰屏蔽字 (\n22位随机干扰_1_随机加扰屏蔽字 ), .\_22位输入 (\crc编码_1_crc校验码 ),
    .\加扰后数据 (\n22位随机干扰_1_加扰后数据 ), .CLK(clock_1_out));  // open: 增加三位错, EDU
  // Probe on \n22位随机干扰_1_加扰后数据 
  LED #(.active("true")) OK (.in(\crc解码_1__0位错 ));
  LED #(.active("true")) \u_两位错  (.in(\crc解码_1__2位错 ));
  LED #(.active("true")) \u_一位错  (.in(\crc解码_1__1位错 ));
  \CRC解码  \crc解码_1  (
    .\CRC编码 (\n22位随机干扰_1_加扰后数据 ), .\_1位错 (\crc解码_1__1位错 ), .\_2位错 (\crc解码_1__2位错 ),
    .\纠错后数据 (\crc解码_1_纠错后数据 ), .\_0位错 (\crc解码_1__0位错 ));
  // Probe on \crc解码_1_纠错后数据 
  LED #(.active("true")) \u_数据正确  (.in(comparator_1_eq));
  Comparator #(.width(16), .mode("twosComplement")) comparator_1 (
    .a(\原始数据 ), .b(\crc解码_1_纠错后数据 ), .eq(comparator_1_eq));  // open: gt, lt

  // Notes on the sheet:
  //   发送方
  //   Ctrl+T 驱动时钟触发随机干扰变化
  //   CRC编解码传输电路
  //   电路功能：测试CRC编解码电路正确性，仿真时设置加扰控制位和原始数据，按CTRL+T触发不同的干扰，检验编解码电路功能
  //   加扰控制00：不加扰  01:1位加扰 10:2位加扰 11：随机加扰
  //   接收方
endmodule

module \CRC传输测试2  (
  input  [1:0] \加扰控制 
);

  wire CLK, comparator_1_eq, \crc解码_1__0位错 , \crc解码_1__1位错 , \crc解码_1__2位错 ;
  wire [6:0] \国标转区位码_1_位号 , \国标转区位码_1_区号 , \国标转区位码_2_位号 , \国标转区位码_2_区号 ;
  wire [7:0] counter_1_q;
  wire [15:0] \发送 , \接收 ;
  wire [21:0] \crc编码_1_crc校验码 , \n22位随机干扰_1_加扰后数据 , \n22位随机干扰_1_随机加扰屏蔽字 ;
  wire [31:0] \字库_1_p3 , \字库_1_p4 , \字库_1_p5 , \字库_1_p6 , \字库_1_p7 , \字库_1_p8 , \字库_1_p9 , \字库_1_p10 ,
       \字库_1_p11 , \字库_1_p12 , \字库_1_p13 , \字库_1_p14 , \字库_1_p15 , \字库_1_p16 , \字库_1_p17 , \字库_1_p18 ,
       \字库_1_p19 , \字库_1_p20 , \字库_1_p21 , \字库_1_p22 , \字库_1_p23 , \字库_1_p24 , \字库_1_p25 , \字库_1_p26 ,
       \字库_1_p27 , \字库_1_p28 , \字库_1_p29 , \字库_1_p30 , \字库_1_p31 , \字库_1_p32 , \字库_1_p33 , \字库_1_p34 ,
       \字库_2_p3 , \字库_2_p4 , \字库_2_p5 , \字库_2_p6 , \字库_2_p7 , \字库_2_p8 , \字库_2_p9 , \字库_2_p10 , \字库_2_p11 ,
       \字库_2_p12 , \字库_2_p13 , \字库_2_p14 , \字库_2_p15 , \字库_2_p16 , \字库_2_p17 , \字库_2_p18 , \字库_2_p19 ,
       \字库_2_p20 , \字库_2_p21 , \字库_2_p22 , \字库_2_p23 , \字库_2_p24 , \字库_2_p25 , \字库_2_p26 , \字库_2_p27 ,
       \字库_2_p28 , \字库_2_p29 , \字库_2_p30 , \字库_2_p31 , \字库_2_p32 , \字库_2_p33 , \字库_2_p34 ;

  Counter #(.width(8), .max('hff), .ongoal("wrap"), .trigger("rising"), .behavior("old")) counter_1 (
    .Q(counter_1_q), .clk(CLK));  // open: load, D, count, carry, clr, preset
  Clock #(.highDuration(1), .lowDuration(1)) \u_时钟  (.out(CLK));
  \国标转区位码  \u_国标转区位码_1  (.\位号 (\国标转区位码_1_位号 ), .\区号 (\国标转区位码_1_区号 ), .GB2312(\发送 ));
  DotMatrix #(.inputtype("row"), .matrixcols(32), .matrixrows(32), .persist(0), .dotshape("circle")) dotmatrix_1 (
    .row0(\字库_1_p3 ), .row1(\字库_1_p4 ), .row2(\字库_1_p5 ), .row3(\字库_1_p6 ), .row4(\字库_1_p7 ),
    .row5(\字库_1_p8 ), .row6(\字库_1_p9 ), .row7(\字库_1_p10 ), .row8(\字库_1_p11 ), .row9(\字库_1_p12 ),
    .row10(\字库_1_p13 ), .row11(\字库_1_p14 ), .row12(\字库_1_p15 ), .row13(\字库_1_p16 ), .row14(\字库_1_p17 ),
    .row15(\字库_1_p18 ), .row16(\字库_1_p19 ), .row17(\字库_1_p20 ), .row18(\字库_1_p21 ), .row19(\字库_1_p22 ),
    .row20(\字库_1_p23 ), .row21(\字库_1_p24 ), .row22(\字库_1_p25 ), .row23(\字库_1_p26 ), .row24(\字库_1_p27 ),
    .row25(\字库_1_p28 ), .row26(\字库_1_p29 ), .row27(\字库_1_p30 ), .row28(\字库_1_p31 ), .row29(\字库_1_p32 ),
    .row30(\字库_1_p33 ), .row31(\字库_1_p34 ));
  // 字库 字库_1: pin names not known; wires that end beside it: \国标转区位码_1_区号 , \国标转区位码_1_位号 , \字库_1_p3 , \字库_1_p4 , \字库_1_p5 , \字库_1_p6 , \字库_1_p7 , \字库_1_p8 , \字库_1_p9 , \字库_1_p10 , \字库_1_p11 , \字库_1_p12 , \字库_1_p13 , \字库_1_p14 , \字库_1_p15 , \字库_1_p16 , \字库_1_p17 , \字库_1_p18 , \字库_1_p19 , \字库_1_p20 , \字库_1_p21 , \字库_1_p22 , \字库_1_p23 , \字库_1_p24 , \字库_1_p25 , \字库_1_p26 , \字库_1_p27 , \字库_1_p28 , \字库_1_p29 , \字库_1_p30 , \字库_1_p31 , \字库_1_p32 , \字库_1_p33 , \字库_1_p34 
  ROM #(.addrWidth(8), .dataWidth(16), .Select("high")) rom_1 (.addr(counter_1_q), .data(\发送 ));
  // Probe on \发送 
  // Probe on \crc编码_1_crc校验码 
  \CRC编码  \crc编码_1  (.\原始数据 (\发送 ), .\CRC校验码 (\crc编码_1_crc校验码 ));
  // Probe on \crc编码_1_crc校验码 
  // Probe on \n22位随机干扰_1_随机加扰屏蔽字 
  \_22位随机干扰  \u_22位随机干扰_1  (
    .\加扰模式 (\加扰控制 ), .\随机加扰屏蔽字 (\n22位随机干扰_1_随机加扰屏蔽字 ), .\_22位输入 (\crc编码_1_crc校验码 ),
    .\加扰后数据 (\n22位随机干扰_1_加扰后数据 ), .CLK(CLK));  // open: 增加三位错, EDU
  \国标转区位码  \u_国标转区位码_2  (.\位号 (\国标转区位码_2_位号 ), .\区号 (\国标转区位码_2_区号 ), .GB2312(\接收 ));
  // Probe on \n22位随机干扰_1_加扰后数据 
  // Probe on \n22位随机干扰_1_加扰后数据 
  // 字库 字库_2: pin names not known; wires that end beside it: \国标转区位码_2_区号 , \国标转区位码_2_位号 , \字库_2_p3 , \字库_2_p4 , \字库_2_p5 , \字库_2_p6 , \字库_2_p7 , \字库_2_p8 , \字库_2_p9 , \字库_2_p10 , \字库_2_p11 , \字库_2_p12 , \字库_2_p13 , \字库_2_p14 , \字库_2_p15 , \字库_2_p16 , \字库_2_p17 , \字库_2_p18 , \字库_2_p19 , \字库_2_p20 , \字库_2_p21 , \字库_2_p22 , \字库_2_p23 , \字库_2_p24 , \字库_2_p25 , \字库_2_p26 , \字库_2_p27 , \字库_2_p28 , \字库_2_p29 , \字库_2_p30 , \字库_2_p31 , \字库_2_p32 , \字库_2_p33 , \字库_2_p34 
  LED #(.active("true")) \u_两位错  (.in(\crc解码_1__2位错 ));
  LED #(.active("true")) \u_一位错  (.in(\crc解码_1__1位错 ));
  LED #(.active("true")) \u_无错误  (.in(\crc解码_1__0位错 ));
  DotMatrix #(.inputtype("row"), .matrixcols(32), .matrixrows(32), .persist(0), .dotshape("circle")) dotmatrix_2 (
    .row0(\字库_2_p3 ), .row1(\字库_2_p4 ), .row2(\字库_2_p5 ), .row3(\字库_2_p6 ), .row4(\字库_2_p7 ),
    .row5(\字库_2_p8 ), .row6(\字库_2_p9 ), .row7(\字库_2_p10 ), .row8(\字库_2_p11 ), .row9(\字库_2_p12 ),
    .row10(\字库_2_p13 ), .row11(\字库_2_p14 ), .row12(\字库_2_p15 ), .row13(\字库_2_p16 ), .row14(\字库_2_p17 ),
    .row15(\字库_2_p18 ), .row16(\字库_2_p19 ), .row17(\字库_2_p20 ), .row18(\字库_2_p21 ), .row19(\字库_2_p22 ),
    .row20(\字库_2_p23 ), .row21(\字库_2_p24 ), .row22(\字库_2_p25 ), .row23(\字库_2_p26 ), .row24(\字库_2_p27 ),
    .row25(\字库_2_p28 ), .row26(\字库_2_p29 ), .row27(\字库_2_p30 ), .row28(\字库_2_p31 ), .row29(\字库_2_p32 ),
    .row30(\字库_2_p33 ), .row31(\字库_2_p34 ));
  \CRC解码  \crc解码_1  (
    .\CRC编码 (\n22位随机干扰_1_加扰后数据 ), .\_1位错 (\crc解码_1__1位错 ), .\_2位错 (\crc解码_1__2位错 ), .\纠错后数据 (\接收 ),
    .\_0位错 (\crc解码_1__0位错 ));
  // Probe on \接收 
  Comparator #(.width(16), .mode("twosComplement")) comparator_1 (
    .a(\发送 ), .b(\接收 ), .eq(comparator_1_eq));  // open: gt, lt
  LED #(.active("true")) \u_数据正确  (.in(comparator_1_eq));

  // Notes on the sheet:
  //   发送方
  //   计数器
  //   发送方
  //   汉字显示
  //   GB2312
  //   contents of rom_1 (hex, n*v repeats v):
  //   bbaa d6d0 bfc6 bcbc b4f3 d1a7 cac7 b9fa bcd2 bdcc d3fd b2bf d6b1 caf4 b5c4 c8ab b9fa d6d8 b5e3 b4f3
  //   d1a7 a3ac d3c9 d4ad bbaa d6d0 c0ed b9a4 b4f3 d1a7 a1a2 cdac bcc3 d2bd bfc6 b4f3 d1a7 a1a2 cee4 baba
  //   b3c7 cad0 bda8 c9e8 d1a7 d4ba d3da a3b2 a3b0 a3b0 a3b0 c4ea a3b5 d4c2 a3b2 a3b6 c8d5 bacf b2a2 b3c9
  //   c1a2 a3ac cac7 cad7 c5fa c1d0 c8eb b9fa bcd2 a1b0 a3b2 a3b1 a3b1 b9a4 b3cc a1b1 d6d8 b5e3 bda8 c9e8
  //   bacd b9fa bcd2 a1b0 a3b9 a3b8 a3b5 b9a4 b3cc a1b1 bda8 c9e8 b8df d0a3 d6ae d2bb a1a3 d1a7 d0a3 d0a3
  //   d4b0 d5bc b5d8 c6df c7a7 d3e0 c4b6 a3ac d4b0 c4da caf7 c4be b4d0 dcd7 a3ac b1cc b2dd c8e7 d2f0 a3ac
  //   bbb7 beb3 d3c5 d1c5 a3ac beb0 c9ab d0e3 c0f6 a3ac c2cc bbaf b8b2 b8c7 c2ca 3732 25a3 acb1 bbd3 fece
  //   aaa1 b0c9 adc1 d6ca bdb4 f3d1 a7a1 b1a1
  //   Ctrl+T 驱动时钟触发随机干扰变化
  //   电路功能：测试CRC编解码电路正确性，仿真时设置加扰控制位和原始数据，按CTRL+T触发不同的干扰，检验编解码电路功能
  //   发送方在ROM预存了一段中文文字，通过计数器驱动电路每个时钟传输一个汉字到接收方
  //   用户实现了国标转区位码电路后，可在中间窗口观察发送方和接收方汉字显示是否一致以观察海明检错纠错性能
  //   CRC编解码传输电路
  //   接收方
  //   汉字显示
  //   Ctrl+T 驱动时钟触发随机干扰变化
  //   加扰控制00：不加扰  01:1位加扰 10:2位加扰 11：随机加扰
  //   加扰控制00：不加扰  01:1位加扰 10:2位加扰 11：随机加扰
  //   接收方
  //   请将时钟频率调到8Hz
endmodule

// CRC
module \CRC编码流水传输  (
  input  \加噪 ,
  input  EDU,
  output _1err,
  output _2err,
  output clr2,
  output clr3,
  output clr4,
  output en5
);

  wire CLK, \crc解码_1__0位错 , \n16位流水接口_1_传输状态out_表明当前传输数据有效 , \n22位流水接口_1_传输状态out_表明当前传输数据有效 ,
       \n22位流水接口_2_传输状态out_表明当前传输数据有效 , not_1_out;
  wire [6:0] \国标转区位码_1_位号 , \国标转区位码_1_区号 , \字库_2_p1 , \字库_2_p2 ;
  wire [7:0] adder_1_out, CNT, multiplexer_1_out;
  wire [15:0] \crc解码_1_纠错后数据 , \n16位流水接口_1_dout16 , \发送 , \接收 ;
  wire [21:0] \crc编码_1_crc校验码 , \n22位流水接口_1_dout22 , \n22位流水接口_2_dout22 , \n22位随机干扰_1_加扰后数据 ;
  wire [31:0] \字库_1_p3 , \字库_1_p4 , \字库_1_p5 , \字库_1_p6 , \字库_1_p7 , \字库_1_p8 , \字库_1_p9 , \字库_1_p10 ,
       \字库_1_p11 , \字库_1_p12 , \字库_1_p13 , \字库_1_p14 , \字库_1_p15 , \字库_1_p16 , \字库_1_p17 , \字库_1_p18 ,
       \字库_1_p19 , \字库_1_p20 , \字库_1_p21 , \字库_1_p22 , \字库_1_p23 , \字库_1_p24 , \字库_1_p25 , \字库_1_p26 ,
       \字库_1_p27 , \字库_1_p28 , \字库_1_p29 , \字库_1_p30 , \字库_1_p31 , \字库_1_p32 , \字库_1_p33 , \字库_1_p34 ,
       \字库_2_p3 , \字库_2_p4 , \字库_2_p5 , \字库_2_p6 , \字库_2_p7 , \字库_2_p8 , \字库_2_p9 , \字库_2_p10 , \字库_2_p11 ,
       \字库_2_p12 , \字库_2_p13 , \字库_2_p14 , \字库_2_p15 , \字库_2_p16 , \字库_2_p17 , \字库_2_p18 , \字库_2_p19 ,
       \字库_2_p20 , \字库_2_p21 , \字库_2_p22 , \字库_2_p23 , \字库_2_p24 , \字库_2_p25 , \字库_2_p26 , \字库_2_p27 ,
       \字库_2_p28 , \字库_2_p29 , \字库_2_p30 , \字库_2_p31 , \字库_2_p32 , \字库_2_p33 , \字库_2_p34 ;

  Multiplexer #(.select(1), .width(8), .disabled("Z"), .enable("false")) multiplexer_1 (
    .in0(8'h1), .in1(8'hfd), .out(multiplexer_1_out), .sel(clr2));
  Register #(.width(8), .trigger("rising"), .Select("low")) register_1 (
    .D(adder_1_out), .Q(CNT), .clk(CLK));  // open: en, clr
  Clock #(.highDuration(1), .lowDuration(1)) \u_时钟  (.out(CLK));
  \国标转区位码  \u_国标转区位码_1  (.\位号 (\国标转区位码_1_位号 ), .\区号 (\国标转区位码_1_区号 ), .GB2312(\发送 ));
  Adder #(.width(8)) adder_1 (.a(multiplexer_1_out), .b(CNT), .out(adder_1_out));  // open: cin, cout
  DotMatrix #(.inputtype("row"), .matrixcols(32), .matrixrows(32), .persist(0), .dotshape("circle")) dotmatrix_1 (
    .row0(\字库_1_p3 ), .row1(\字库_1_p4 ), .row2(\字库_1_p5 ), .row3(\字库_1_p6 ), .row4(\字库_1_p7 ),
    .row5(\字库_1_p8 ), .row6(\字库_1_p9 ), .row7(\字库_1_p10 ), .row8(\字库_1_p11 ), .row9(\字库_1_p12 ),
    .row10(\字库_1_p13 ), .row11(\字库_1_p14 ), .row12(\字库_1_p15 ), .row13(\字库_1_p16 ), .row14(\字库_1_p17 ),
    .row15(\字库_1_p18 ), .row16(\字库_1_p19 ), .row17(\字库_1_p20 ), .row18(\字库_1_p21 ), .row19(\字库_1_p22 ),
    .row20(\字库_1_p23 ), .row21(\字库_1_p24 ), .row22(\字库_1_p25 ), .row23(\字库_1_p26 ), .row24(\字库_1_p27 ),
    .row25(\字库_1_p28 ), .row26(\字库_1_p29 ), .row27(\字库_1_p30 ), .row28(\字库_1_p31 ), .row29(\字库_1_p32 ),
    .row30(\字库_1_p33 ), .row31(\字库_1_p34 ));
  // 字库 字库_1: pin names not known; wires that end beside it: \国标转区位码_1_区号 , \国标转区位码_1_位号 , \字库_1_p3 , \字库_1_p4 , \字库_1_p5 , \字库_1_p6 , \字库_1_p7 , \字库_1_p8 , \字库_1_p9 , \字库_1_p10 , \字库_1_p11 , \字库_1_p12 , \字库_1_p13 , \字库_1_p14 , \字库_1_p15 , \字库_1_p16 , \字库_1_p17 , \字库_1_p18 , \字库_1_p19 , \字库_1_p20 , \字库_1_p21 , \字库_1_p22 , \字库_1_p23 , \字库_1_p24 , \字库_1_p25 , \字库_1_p26 , \字库_1_p27 , \字库_1_p28 , \字库_1_p29 , \字库_1_p30 , \字库_1_p31 , \字库_1_p32 , \字库_1_p33 , \字库_1_p34 
  ROM #(.addrWidth(8), .dataWidth(16), .Select("high")) rom_1 (.addr(CNT), .data(\发送 ));
  \_16位流水接口  \u_16位流水接口_1  (
    .Din16(\发送 ), .\传输状态In_表明当前传输数据有效 (1'b1), .CLK(CLK), .Dout16(\n16位流水接口_1_dout16 ),
    .\传输状态Out_表明当前传输数据有效 (\n16位流水接口_1_传输状态out_表明当前传输数据有效 ), .\同步清零_气泡_高电平有效 (clr2));  // open: 使能端_低电平有效_stall_高电平有效
  \CRC编码  \crc编码_1  (.\原始数据 (\n16位流水接口_1_dout16 ), .\CRC校验码 (\crc编码_1_crc校验码 ));
  \_22位流水接口  \u_22位流水接口_1  (
    .Din22(\crc编码_1_crc校验码 ), .\传输状态In_表明当前传输数据有效 (\n16位流水接口_1_传输状态out_表明当前传输数据有效 ), .CLK(CLK),
    .Dout22(\n22位流水接口_1_dout22 ), .\传输状态Out_表明当前传输数据有效 (\n22位流水接口_1_传输状态out_表明当前传输数据有效 ),
    .\同步清零_气泡_高电平有效 (clr2));  // open: 使能端_低电平有效_stall_高电平有效
  \_22位随机干扰  \u_22位随机干扰_1  (
    .\加扰模式 (2'b11), .\_22位输入 (\n22位流水接口_1_dout22 ), .\加扰后数据 (\n22位随机干扰_1_加扰后数据 ), .\增加三位错 (\加噪 ), .CLK(CLK),
    .EDU(EDU));  // open: 随机加扰屏蔽字
  // 字库 字库_2: pin names not known; wires that end beside it: \字库_2_p1 , \字库_2_p2 , \字库_2_p3 , \字库_2_p4 , \字库_2_p5 , \字库_2_p6 , \字库_2_p7 , \字库_2_p8 , \字库_2_p9 , \字库_2_p10 , \字库_2_p11 , \字库_2_p12 , \字库_2_p13 , \字库_2_p14 , \字库_2_p15 , \字库_2_p16 , \字库_2_p17 , \字库_2_p18 , \字库_2_p19 , \字库_2_p20 , \字库_2_p21 , \字库_2_p22 , \字库_2_p23 , \字库_2_p24 , \字库_2_p25 , \字库_2_p26 , \字库_2_p27 , \字库_2_p28 , \字库_2_p29 , \字库_2_p30 , \字库_2_p31 , \字库_2_p32 , \字库_2_p33 , \字库_2_p34 
  \国标转区位码  \u_国标转区位码_2  (.\位号 (\字库_2_p2 ), .\区号 (\字库_2_p1 ), .GB2312(\接收 ));
  \_22位流水接口  \u_22位流水接口_2  (
    .Din22(\n22位随机干扰_1_加扰后数据 ), .\传输状态In_表明当前传输数据有效 (\n22位流水接口_1_传输状态out_表明当前传输数据有效 ), .CLK(CLK),
    .Dout22(\n22位流水接口_2_dout22 ), .\传输状态Out_表明当前传输数据有效 (\n22位流水接口_2_传输状态out_表明当前传输数据有效 ),
    .\同步清零_气泡_高电平有效 (clr2));  // open: 使能端_低电平有效_stall_高电平有效
  DotMatrix #(.inputtype("row"), .matrixcols(32), .matrixrows(32), .persist(0), .dotshape("circle")) dotmatrix_2 (
    .row0(\字库_2_p3 ), .row1(\字库_2_p4 ), .row2(\字库_2_p5 ), .row3(\字库_2_p6 ), .row4(\字库_2_p7 ),
    .row5(\字库_2_p8 ), .row6(\字库_2_p9 ), .row7(\字库_2_p10 ), .row8(\字库_2_p11 ), .row9(\字库_2_p12 ),
    .row10(\字库_2_p13 ), .row11(\字库_2_p14 ), .row12(\字库_2_p15 ), .row13(\字库_2_p16 ), .row14(\字库_2_p17 ),
    .row15(\字库_2_p18 ), .row16(\字库_2_p19 ), .row17(\字库_2_p20 ), .row18(\字库_2_p21 ), .row19(\字库_2_p22 ),
    .row20(\字库_2_p23 ), .row21(\字库_2_p24 ), .row22(\字库_2_p25 ), .row23(\字库_2_p26 ), .row24(\字库_2_p27 ),
    .row25(\字库_2_p28 ), .row26(\字库_2_p29 ), .row27(\字库_2_p30 ), .row28(\字库_2_p31 ), .row29(\字库_2_p32 ),
    .row30(\字库_2_p33 ), .row31(\字库_2_p34 ));
  and and_1 (clr2, _2err, \n22位流水接口_2_传输状态out_表明当前传输数据有效 );
  LED #(.active("true")) \u_两位错  (.in(_2err));
  LED #(.active("true")) \u_一位错  (.in(_1err));
  LED #(.active("true")) \u_无错误  (.in(\crc解码_1__0位错 ));
  \CRC解码  \crc解码_1  (
    .\CRC编码 (\n22位流水接口_2_dout22 ), .\_1位错 (_1err), .\_2位错 (_2err), .\纠错后数据 (\crc解码_1_纠错后数据 ),
    .\_0位错 (\crc解码_1__0位错 ));
  not not_1 (not_1_out, \n22位流水接口_2_传输状态out_表明当前传输数据有效 );
  or or_1 (en5, not_1_out, _2err);
  \_16位流水接口  \u_16位流水接口_2  (
    .Din16(\crc解码_1_纠错后数据 ), .\传输状态In_表明当前传输数据有效 (\n22位流水接口_2_传输状态out_表明当前传输数据有效 ), .CLK(CLK), .Dout16(\接收 ),
    .\使能端_低电平有效_stall_高电平有效 (en5));  // open: 传输状态Out_表明当前传输数据有效, 同步清零_气泡_高电平有效
  // Probe on \接收 

  assign clr3 = clr2;
  assign clr4 = clr2;

  // Notes on the sheet:
  //   CRC编码流水传输电路
  //   寄存器
  //   发送方
  //   汉字显示
  //   加法器
  //   GB2312
  //   1.取数阶段
  //   contents of rom_1 (hex, n*v repeats v):
  //   bbaa d6d0 bfc6 bcbc b4f3 d1a7 cac7 b9fa bcd2 bdcc d3fd b2bf d6b1 caf4 b5c4 c8ab b9fa d6d8 b5e3 b4f3
  //   d1a7 a3ac d3c9 d4ad bbaa d6d0 c0ed b9a4 b4f3 d1a7 a1a2 cdac bcc3 d2bd bfc6 b4f3 d1a7 a1a2 cee4 baba
  //   b3c7 cad0 bda8 c9e8 d1a7 d4ba d3da a3b2 a3b0 a3b0 a3b0 c4ea a3b5 d4c2 a3b2 a3b6 c8d5 bacf b2a2 b3c9
  //   c1a2 a3ac cac7 cad7 c5fa c1d0 c8eb b9fa bcd2 a1b0 a3b2 a3b1 a3b1 b9a4 b3cc a1b1 d6d8 b5e3 bda8 c9e8
  //   bacd b9fa bcd2 a1b0 a3b9 a3b8 a3b5 b9a4 b3cc a1b1 bda8 c9e8 b8df d0a3 d6ae d2bb a1a3 d1a7 d0a3 d0a3
  //   d4b0 d5bc b5d8 c6df c7a7 d3e0 c4b6 a3ac d4b0 c4da caf7 c4be b4d0 dcd7 a3ac b1cc b2dd c8e7 d2f0 a3ac
  //   bbb7 beb3 d3c5 d1c5 a3ac beb0 c9ab d0e3 c0f6 a3ac c2cc bbaf b8b2 b8c7 c2ca 3732 25a3 acb1 bbd3 fece
  //   aaa1 b0c9 adc1 d6ca bdb4 f3d1 a7a1 b1a1
  //   ~使能/Stall
  //   发送方在ROM预存了一段中文文字，通过计数器驱动电路每个时钟传输一个汉字
  //   同步清零
  //   用户实现了国标转区位码电路后，可在中间窗口观察发送方和接收方汉字显示是否一致以观察海明检错纠错性能
  //   数据状态：高电平有效
  //   2.编码阶段
  //   接收方
  //   汉字显示
  //   电路功能：采用流水方式进行数据编码传输，测试海明编码检错纠错能力，当出现2位错时，发送重传信号要求发送方重传，保证接收方按ROM中的地址顺序接受所有汉字
  //   3.传输阶段
  //   4.解码阶段
  //   此电路可帮助学生理解指令流水线工作原理，重传类似指令流水线中的分支指令
  //   5.显示阶段
  //   请将时钟频率调到8Hz
  //   Ctrl+ K启动电路自动仿真
  //   EDUCODER在线测试引脚
  //   请勿增删改引脚
endmodule

// 随机干扰
module \_22位随机干扰  (
  input  CLK,
  input  [21:0] \_22位输入 ,
  input  EDU,
  input  [1:0] \加扰模式 ,
  input  \增加三位错 ,
  output [21:0] \随机加扰屏蔽字 ,
  output [21:0] \加扰后数据 
);

  wire comparator_1_eq, \随机信号_5_out ;
  wire [1:0] EDUerr, multiplexer_3_out, \随机信号_4_out ;
  wire [3:0] \随机信号_2_out , \随机信号_3_out , \随机信号_out ;
  wire [7:0] counter_1_q;
  wire [15:0] \_1位加扰A ;
  wire [21:0] \_1位加扰 , \_2位加扰 , \_3位加扰 , multiplexer_1_out, multiplexer_5_out, shifter_1_out, \随机加扰 ;
  wire [21:6] \_1位加扰B , \_1位加扰C ;

  Random #(.width(4), .seed(0), .trigger("rising")) \u_随机信号  (.clk(CLK), .out(\随机信号_out ));  // open: next, clr
  Decoder #(.select(4), .tristate("false"), .disabled("Z"), .enable("false")) decoder_1 (
    .out0(\_1位加扰A [0]), .out1(\_1位加扰A [1]), .out2(\_1位加扰A [2]), .out3(\_1位加扰A [3]), .out4(\_1位加扰A [4]),
    .out5(\_1位加扰A [5]), .out6(\_1位加扰A [6]), .out7(\_1位加扰A [7]), .out8(\_1位加扰A [8]), .out9(\_1位加扰A [9]),
    .out10(\_1位加扰A [10]), .out11(\_1位加扰A [11]), .out12(\_1位加扰A [12]), .out13(\_1位加扰A [13]),
    .out14(\_1位加扰A [14]), .out15(\_1位加扰A [15]), .sel(\随机信号_out ));
  Decoder #(.select(4), .tristate("false"), .disabled("Z"), .enable("false")) decoder_2 (
    .out0(\_1位加扰B [6]), .out1(\_1位加扰B [7]), .out2(\_1位加扰B [8]), .out3(\_1位加扰B [9]), .out4(\_1位加扰B [10]),
    .out5(\_1位加扰B [11]), .out6(\_1位加扰B [12]), .out7(\_1位加扰B [13]), .out8(\_1位加扰B [14]), .out9(\_1位加扰B [15]),
    .out10(\_1位加扰B [16]), .out11(\_1位加扰B [17]), .out12(\_1位加扰B [18]), .out13(\_1位加扰B [19]),
    .out14(\_1位加扰B [20]), .out15(\_1位加扰B [21]), .sel(\随机信号_2_out ));
  Random #(.width(4), .seed(18), .trigger("rising")) \u_随机信号_2  (.clk(CLK), .out(\随机信号_2_out ));  // open: next, clr
  Random #(.width(4), .seed(3), .trigger("rising")) \u_随机信号_3  (.clk(CLK), .out(\随机信号_3_out ));  // open: next, clr
  Random #(.width(2), .seed(21), .trigger("rising")) \u_随机信号_4  (.clk(CLK), .out(\随机信号_4_out ));  // open: next, clr
  Random #(.width(1), .seed(31), .trigger("rising")) \u_随机信号_5  (.clk(CLK), .out(\随机信号_5_out ));  // open: next, clr
  Decoder #(.select(4), .tristate("false"), .disabled("Z"), .enable("false")) decoder_3 (
    .out0(\_1位加扰C [6]), .out1(\_1位加扰C [7]), .out2(\_1位加扰C [8]), .out3(\_1位加扰C [9]), .out4(\_1位加扰C [10]),
    .out5(\_1位加扰C [11]), .out6(\_1位加扰C [12]), .out7(\_1位加扰C [13]), .out8(\_1位加扰C [14]), .out9(\_1位加扰C [15]),
    .out10(\_1位加扰C [16]), .out11(\_1位加扰C [17]), .out12(\_1位加扰C [18]), .out13(\_1位加扰C [19]),
    .out14(\_1位加扰C [20]), .out15(\_1位加扰C [21]), .sel(\随机信号_3_out ));
  Pull_Resistor #(.pull(1)) pull_resistor_1 (.node(\加扰模式 ));
  Pull_Resistor #(.pull(0)) pull_resistor_2 (.node(\增加三位错 ));
  Multiplexer #(.select(1), .width(22), .disabled("Z"), .enable("false")) multiplexer_1 (
    .in0({\_1位加扰B , {6{1'b0}}}), .in1(\_3位加扰 ), .out(multiplexer_1_out), .sel(\增加三位错 ));
  Multiplexer #(.select(2), .width(22), .disabled("Z"), .enable("false")) multiplexer_2 (
    .in0({22{1'b0}}), .in1({{6{1'b0}}, \_1位加扰A }), .in2(\_2位加扰 ), .in3(multiplexer_1_out), .out(\随机加扰 ),
    .sel(\随机信号_4_out ));
  Pull_Resistor #(.pull(0)) pull_resistor_3 (.node(EDU));
  Multiplexer #(.select(1), .width(2), .disabled("Z"), .enable("false")) multiplexer_3 (
    .in0(\加扰模式 ), .in1(EDUerr), .out(multiplexer_3_out), .sel(EDU));
  Shifter #(.width(22), .shift("rl")) shifter_1 (.in({{6{1'b0}}, \_1位加扰A }), .\dist (5'b00001), .out(shifter_1_out));
  Comparator #(.width(22), .mode("unsigned")) comparator_1 (
    .a({{6{1'b0}}, \_1位加扰A }), .b({\_1位加扰B , {6{1'b0}}}), .eq(comparator_1_eq));  // open: gt, lt
  Multiplexer #(.select(2), .width(22), .disabled("Z"), .enable("false")) multiplexer_4 (
    .in0({22{1'b0}}), .in1(\_1位加扰 ), .in2(\_2位加扰 ), .in3(\随机加扰 ), .out(\随机加扰屏蔽字 ), .sel(multiplexer_3_out));
  Multiplexer #(.select(1), .width(22), .disabled("Z"), .enable("false")) multiplexer_5 (
    .in0({{6{1'b0}}, \_1位加扰A }), .in1(shifter_1_out), .out(multiplexer_5_out), .sel(comparator_1_eq));
  Counter #(.width(8), .max('hff), .ongoal("wrap"), .trigger("rising"), .behavior("old")) counter_1 (
    .Q(counter_1_q), .clk(CLK));  // open: load, D, count, carry, clr, preset
  assign \_2位加扰  = multiplexer_5_out ^ {\_1位加扰B , {6{1'b0}}};  // XOR_Gate xor_1, 22 bits wide
  assign \_3位加扰  = \_2位加扰  ^ {\_1位加扰C , {6{1'b0}}};  // XOR_Gate xor_2, 22 bits wide
  ROM #(.addrWidth(8), .dataWidth(2), .Select("low")) rom_1 (.addr(counter_1_q), .data(EDUerr));
  Multiplexer #(.select(1), .width(22), .disabled("Z"), .enable("false")) multiplexer_6 (
    .in0(multiplexer_5_out), .in1({\_1位加扰B , {6{1'b0}}}), .out(\_1位加扰 ), .sel(\随机信号_5_out ));
  assign \加扰后数据  = \随机加扰屏蔽字  ^ \_22位输入 ;  // XOR_Gate xor_3, 22 bits wide

  // Notes on the sheet:
  //   在随机加扰模式中增加三位错
  //   两个随机信号分别负责高16位和第16位
  //   22位信道加扰屏蔽字生成电路，加扰模式引脚00：不加扰  01:1位加扰 10:2位加扰 11：0-2位随机加扰
  //   如果两个信号相同，其中一个移位
  //   contents of rom_1 (hex, n*v repeats v):
  //   2 2 1 1 1 4*0 4*2 1 1 1 0 1 0 0 2 0 2 5*0 1 0 1 4*0 2
endmodule

// 随机加扰
module \_17位随机干扰  (
  input  CLK,
  input  [16:0] \_17位输入 ,
  output [16:0] \随机加扰屏蔽字 ,
  output [16:0] \加扰后数据 
);

  wire [4:0] \随机数_2_out , \随机数_3_out , \随机数_out ;
  wire [16:0] or_1_out;
  wire [31:0] decoder_1_out31, decoder_2_out31, decoder_3_out31;

  Decoder #(.select(5), .tristate("false"), .disabled("Z"), .enable("false")) decoder_1 (
    .out0(decoder_1_out31[31]), .out1(decoder_1_out31[30]), .out2(decoder_1_out31[29]),
    .out3(decoder_1_out31[28]), .out4(decoder_1_out31[27]), .out5(decoder_1_out31[26]),
    .out6(decoder_1_out31[25]), .out7(decoder_1_out31[24]), .out8(decoder_1_out31[23]),
    .out9(decoder_1_out31[22]), .out10(decoder_1_out31[21]), .out11(decoder_1_out31[20]),
    .out12(decoder_1_out31[19]), .out13(decoder_1_out31[18]), .out14(decoder_1_out31[17]),
    .out15(decoder_1_out31[16]), .out16(decoder_1_out31[15]), .out17(decoder_1_out31[14]),
    .out18(decoder_1_out31[13]), .out19(decoder_1_out31[12]), .out20(decoder_1_out31[11]),
    .out21(decoder_1_out31[10]), .out22(decoder_1_out31[9]), .out23(decoder_1_out31[8]),
    .out24(decoder_1_out31[7]), .out25(decoder_1_out31[6]), .out26(decoder_1_out31[5]),
    .out27(decoder_1_out31[4]), .out28(decoder_1_out31[3]), .out29(decoder_1_out31[2]),
    .out30(decoder_1_out31[1]), .out31(decoder_1_out31[0]), .sel(\随机数_out ));
  Random #(.width(5), .seed(0), .trigger("rising")) \u_随机数  (.clk(CLK), .out(\随机数_out ));  // open: next, clr
  Random #(.width(5), .seed(18), .trigger("rising")) \u_随机数_2  (.clk(CLK), .out(\随机数_2_out ));  // open: next, clr
  Decoder #(.select(5), .tristate("false"), .disabled("Z"), .enable("false")) decoder_2 (
    .out0(decoder_2_out31[31]), .out1(decoder_2_out31[30]), .out2(decoder_2_out31[29]),
    .out3(decoder_2_out31[28]), .out4(decoder_2_out31[27]), .out5(decoder_2_out31[26]),
    .out6(decoder_2_out31[25]), .out7(decoder_2_out31[24]), .out8(decoder_2_out31[23]),
    .out9(decoder_2_out31[22]), .out10(decoder_2_out31[21]), .out11(decoder_2_out31[20]),
    .out12(decoder_2_out31[19]), .out13(decoder_2_out31[18]), .out14(decoder_2_out31[17]),
    .out15(decoder_2_out31[16]), .out16(decoder_2_out31[15]), .out17(decoder_2_out31[14]),
    .out18(decoder_2_out31[13]), .out19(decoder_2_out31[12]), .out20(decoder_2_out31[11]),
    .out21(decoder_2_out31[10]), .out22(decoder_2_out31[9]), .out23(decoder_2_out31[8]),
    .out24(decoder_2_out31[7]), .out25(decoder_2_out31[6]), .out26(decoder_2_out31[5]),
    .out27(decoder_2_out31[4]), .out28(decoder_2_out31[3]), .out29(decoder_2_out31[2]),
    .out30(decoder_2_out31[1]), .out31(decoder_2_out31[0]), .sel(\随机数_2_out ));
  Decoder #(.select(5), .tristate("false"), .disabled("Z"), .enable("false")) decoder_3 (
    .out0(decoder_3_out31[31]), .out1(decoder_3_out31[30]), .out2(decoder_3_out31[29]),
    .out3(decoder_3_out31[28]), .out4(decoder_3_out31[27]), .out5(decoder_3_out31[26]),
    .out6(decoder_3_out31[25]), .out7(decoder_3_out31[24]), .out8(decoder_3_out31[23]),
    .out9(decoder_3_out31[22]), .out10(decoder_3_out31[21]), .out11(decoder_3_out31[20]),
    .out12(decoder_3_out31[19]), .out13(decoder_3_out31[18]), .out14(decoder_3_out31[17]),
    .out15(decoder_3_out31[16]), .out16(decoder_3_out31[15]), .out17(decoder_3_out31[14]),
    .out18(decoder_3_out31[13]), .out19(decoder_3_out31[12]), .out20(decoder_3_out31[11]),
    .out21(decoder_3_out31[10]), .out22(decoder_3_out31[9]), .out23(decoder_3_out31[8]),
    .out24(decoder_3_out31[7]), .out25(decoder_3_out31[6]), .out26(decoder_3_out31[5]),
    .out27(decoder_3_out31[4]), .out28(decoder_3_out31[3]), .out29(decoder_3_out31[2]),
    .out30(decoder_3_out31[1]), .out31(decoder_3_out31[0]), .sel(\随机数_3_out ));
  Random #(.width(5), .seed(3), .trigger("rising")) \u_随机数_3  (.clk(CLK), .out(\随机数_3_out ));  // open: next, clr
  assign or_1_out = decoder_1_out31[16:0] | decoder_2_out31[16:0];  // OR_Gate or_1, 17 bits wide
  assign \随机加扰屏蔽字  = or_1_out | decoder_3_out31[16:0];  // OR_Gate or_2, 17 bits wide
  assign \加扰后数据  = \随机加扰屏蔽字  ^ \_17位输入 ;  // XOR_Gate xor_1, 17 bits wide
endmodule

module \_22位流水接口  (
  input  [21:0] Din22,
  input  \传输状态In_表明当前传输数据有效 ,
  input  CLK,
  input  \同步清零_气泡_高电平有效 ,
  input  \使能端_低电平有效_stall_高电平有效 ,
  output [21:0] Dout22,
  output \传输状态Out_表明当前传输数据有效 
);

  wire multiplexer_2_out, pull_resistor_2_node;
  wire [21:0] multiplexer_1_out;

  Multiplexer #(.select(1), .width(22), .disabled("Z"), .enable("false")) multiplexer_1 (
    .in0(Din22), .in1({22{1'b0}}), .out(multiplexer_1_out), .sel(\同步清零_气泡_高电平有效 ));
  Multiplexer #(.select(1), .width(1), .disabled("Z"), .enable("false")) multiplexer_2 (
    .in0(\传输状态In_表明当前传输数据有效 ), .in1(1'b0), .out(multiplexer_2_out), .sel(\同步清零_气泡_高电平有效 ));
  Pull_Resistor #(.pull(0)) pull_resistor_1 (.node(\同步清零_气泡_高电平有效 ));
  Register #(.width(22), .trigger("rising"), .Select("low")) register_1 (
    .D(multiplexer_1_out), .en(pull_resistor_2_node), .Q(Dout22), .clk(CLK));  // open: clr
  Register #(.width(1), .trigger("rising"), .Select("low")) register_2 (
    .D(multiplexer_2_out), .en(pull_resistor_2_node), .Q(\传输状态Out_表明当前传输数据有效 ), .clk(CLK));  // open: clr
  Pull_Resistor #(.pull(0)) pull_resistor_2 (.node(pull_resistor_2_node));
  not not_1 (pull_resistor_2_node, \使能端_低电平有效_stall_高电平有效 );

  // Notes on the sheet:
  //   同步清零_气泡_高电平有效: pull=down
  //   使能端_低电平有效_stall_高电平有效: pull=down
endmodule

module \_16位流水接口  (
  input  [15:0] Din16,
  input  \传输状态In_表明当前传输数据有效 ,
  input  CLK,
  input  \同步清零_气泡_高电平有效 ,
  input  \使能端_低电平有效_stall_高电平有效 ,
  output [15:0] Dout16,
  output \传输状态Out_表明当前传输数据有效 
);

  wire multiplexer_2_out, pull_resistor_2_node;
  wire [15:0] multiplexer_1_out;

  Multiplexer #(.select(1), .width(16), .disabled("Z"), .enable("false")) multiplexer_1 (
    .in0(Din16), .in1({16{1'b0}}), .out(multiplexer_1_out), .sel(\同步清零_气泡_高电平有效 ));
  Multiplexer #(.select(1), .width(1), .disabled("Z"), .enable("false")) multiplexer_2 (
    .in0(\传输状态In_表明当前传输数据有效 ), .in1(1'b0), .out(multiplexer_2_out), .sel(\同步清零_气泡_高电平有效 ));
  Pull_Resistor #(.pull(0)) pull_resistor_1 (.node(\同步清零_气泡_高电平有效 ));
  Register #(.width(16), .trigger("rising"), .Select("low")) register_1 (
    .D(multiplexer_1_out), .en(pull_resistor_2_node), .Q(Dout16), .clk(CLK));  // open: clr
  Register #(.width(1), .trigger("rising"), .Select("low")) register_2 (
    .D(multiplexer_2_out), .en(pull_resistor_2_node), .Q(\传输状态Out_表明当前传输数据有效 ), .clk(CLK));  // open: clr
  Pull_Resistor #(.pull(0)) pull_resistor_2 (.node(pull_resistor_2_node));
  not not_1 (pull_resistor_2_node, \使能端_低电平有效_stall_高电平有效 );
endmodule

module \流水模拟  (
);

  wire \时钟_out ;
  wire [15:0] counter_1_q, \n16位流水接口_1_dout16 , \n16位流水接口_2_dout16 , \n16位流水接口_3_dout16 ,
       \n16位流水接口_4_dout16 , \组合逻辑_1_out_2 , \组合逻辑_2_out_2 , \组合逻辑_3_out_2 ;

  Clock #(.highDuration(1), .lowDuration(1)) \u_时钟  (.out(\时钟_out ));
  Counter #(.width(16), .max('hffff), .ongoal("wrap"), .trigger("rising"), .behavior("old")) counter_1 (
    .Q(counter_1_q), .clk(\时钟_out ));  // open: load, D, count, carry, clr, preset
  // Probe on counter_1_q
  \_16位流水接口  \u_16位流水接口_1  (
    .Din16(counter_1_q), .CLK(\时钟_out ), .Dout16(\n16位流水接口_1_dout16 ));  // open: 传输状态In_表明当前传输数据有效, 传输状态Out_表明当前传输数据有效, 同步清零_气泡_高电平有效, 使能端_低电平有效_stall_高电平有效
  // Probe on \n16位流水接口_1_dout16 
  \组合逻辑  \u_组合逻辑_1  (.in_1(\n16位流水接口_1_dout16 ), .out_2(\组合逻辑_1_out_2 ));
  \_16位流水接口  \u_16位流水接口_2  (
    .Din16(\组合逻辑_1_out_2 ), .CLK(\时钟_out ), .Dout16(\n16位流水接口_2_dout16 ));  // open: 传输状态In_表明当前传输数据有效, 传输状态Out_表明当前传输数据有效, 同步清零_气泡_高电平有效, 使能端_低电平有效_stall_高电平有效
  // Probe on \n16位流水接口_2_dout16 
  \组合逻辑  \u_组合逻辑_2  (.in_1(\n16位流水接口_2_dout16 ), .out_2(\组合逻辑_2_out_2 ));
  \_16位流水接口  \u_16位流水接口_3  (
    .Din16(\组合逻辑_2_out_2 ), .CLK(\时钟_out ), .Dout16(\n16位流水接口_3_dout16 ));  // open: 传输状态In_表明当前传输数据有效, 传输状态Out_表明当前传输数据有效, 同步清零_气泡_高电平有效, 使能端_低电平有效_stall_高电平有效
  // Probe on \n16位流水接口_3_dout16 
  \组合逻辑  \u_组合逻辑_3  (.in_1(\n16位流水接口_3_dout16 ), .out_2(\组合逻辑_3_out_2 ));
  \_16位流水接口  \u_16位流水接口_4  (
    .Din16(\组合逻辑_3_out_2 ), .CLK(\时钟_out ), .Dout16(\n16位流水接口_4_dout16 ));  // open: 传输状态In_表明当前传输数据有效, 传输状态Out_表明当前传输数据有效, 同步清零_气泡_高电平有效, 使能端_低电平有效_stall_高电平有效
  // Probe on \n16位流水接口_4_dout16 

  // Notes on the sheet:
  //   计数器
  //   阶段1
  //   阶段2
  //   阶段3
  //   利用ctrl+T驱动该电路时钟，观察数据在流水线中传递的过程
  //   阶段4
  //   阶段5
endmodule

// 组合逻辑
module \组合逻辑  (
  input  [15:0] in_1,
  output [15:0] out_2
);


  assign out_2 = in_1;
endmodule

module \子电路外观测试  (
);

  wire \crc编码流水传输_1__1err , \crc编码流水传输_1__2err , \crc编码流水传输_1_clr2 , \crc编码流水传输_1_clr3 , \crc编码流水传输_1_clr4 ,
       \crc编码流水传输_1_en5 , \crc解码_1__0位错 , \crc解码_1__1位错 , \crc解码_1__2位错 , undriven_3, undriven_4, undriven_6,
       undriven_8, \偶校验检错_1_检错位 , \海明编码流水传输_1__1err , \海明编码流水传输_1__2err , \海明编码流水传输_1_clr2 ,
       \海明编码流水传输_1_clr3 , \海明编码流水传输_1_clr4 , \海明编码流水传输_1_en5 , \海明解码_1__0位错 , \海明解码_1__1位错 , \海明解码_1__2位错 ;
  wire [6:0] \国标转区位码_1_位号 , \国标转区位码_1_区号 ;
  wire [15:0] \crc解码_1_纠错后数据 , undriven, undriven_2, undriven_5, undriven_7, \偶校验检错_1_数据位 ,
       \汉字显示_1_educoder , \海明解码_1_纠错后数据 ;
  wire [16:0] \偶校验编码_1_偶校验编码 ;
  wire [21:0] \crc编码_1_crc校验码 , \海明编码_1_海明码 ;

  \国标转区位码  \u_国标转区位码_1  (.\位号 (\国标转区位码_1_位号 ), .\区号 (\国标转区位码_1_区号 ), .GB2312(undriven_2));
  \海明编码  \u_海明编码_1  (.\原始数据 (undriven), .\海明码 (\海明编码_1_海明码 ));
  \汉字显示  \u_汉字显示_1  (.EduCoder(\汉字显示_1_educoder ));
  \海明编码流水传输  \u_海明编码流水传输_1  (
    .EDU(undriven_3), .\加噪 (undriven_4), ._1err(\海明编码流水传输_1__1err ), ._2err(\海明编码流水传输_1__2err ),
    .clr2(\海明编码流水传输_1_clr2 ), .clr3(\海明编码流水传输_1_clr3 ), .clr4(\海明编码流水传输_1_clr4 ), .en5(\海明编码流水传输_1_en5 ));
  \海明解码  \u_海明解码_1  (
    .\_1位错 (\海明解码_1__1位错 ), .\_2位错 (\海明解码_1__2位错 ), .\_0位错 (\海明解码_1__0位错 ), .\海明码 (\海明编码_1_海明码 ),
    .\纠错后数据 (\海明解码_1_纠错后数据 ));
  \偶校验编码  \u_偶校验编码_1  (.\原始数据 (undriven_5), .\偶校验编码 (\偶校验编码_1_偶校验编码 ));
  \CRC编码流水传输  \crc编码流水传输_1  (
    .EDU(undriven_6), .\加噪 (undriven_8), ._1err(\crc编码流水传输_1__1err ), ._2err(\crc编码流水传输_1__2err ),
    .clr2(\crc编码流水传输_1_clr2 ), .clr3(\crc编码流水传输_1_clr3 ), .clr4(\crc编码流水传输_1_clr4 ), .en5(\crc编码流水传输_1_en5 ));
  \CRC编码  \crc编码_1  (.\原始数据 (undriven_7), .\CRC校验码 (\crc编码_1_crc校验码 ));
  \偶校验检错  \u_偶校验检错_1  (.\检错位 (\偶校验检错_1_检错位 ), .\偶校验编码 (\偶校验编码_1_偶校验编码 ), .\数据位 (\偶校验检错_1_数据位 ));
  \CRC解码  \crc解码_1  (
    .\CRC编码 (\crc编码_1_crc校验码 ), .\_1位错 (\crc解码_1__1位错 ), .\_2位错 (\crc解码_1__2位错 ), .\纠错后数据 (\crc解码_1_纠错后数据 ),
    .\_0位错 (\crc解码_1__0位错 ));

  // Notes on the sheet:
  //   GB2312
  //   国标转区位码电路封装测试
  //   原始数据
  //   GB2312
  //   EDU
  //   汉字显示电路封装测试
  //   1位错
  //   海明编码
  //   海明编解码电路封装测试
  //   加噪
  //   1err
  //   2err
  //   en5
  //   海明流水传输电路封装测试
  //   最好通过引脚悬浮提示看看连接是否正确，如果有问题，请调整封装引脚位置直至连接正确
  //   原始数据
  //   2位错
  //   0位错
  //   clr2
  //   clr3
  //   clr4
  //   原始数据
  //   EDU
  //   请勿在子电路中增删改，甚至移动引脚位置，这些都可能导致子电路外观---封装发生改变，从而使得测试电路无法正确测试
  //   提交EduCoder平台检测之前，请先检查一下对应子电路的封装连接是否正确，主要查看引脚位置是否连接正确，有否错位未连接等情况
  //   原始数据
  //   加噪
  //   1err
  //   2err
  //   en5
  //   CRC流水传输电路封装测试
  //   偶校验编码
  //   偶校验编解码电路封装测试
  //   clr2
  //   clr3
  //   clr4
  //   CRC编码
  //   CRC编解码电路封装测试
  //   检错位
  //   原始数据
  //   2位错
  //   1位错
  //   0位错
  //   原始数据
endmodule

module \解码器  (
  input  a,
  input  b,
  input  c,
  input  d,
  input  e,
  output G,
  output H,
  output I,
  output J,
  output K,
  output L,
  output M,
  output N,
  output O,
  output P,
  output Q,
  output R,
  output S,
  output T,
  output U,
  output V
);

  wire not_1_out, not_2_out, not_3_out, not_4_out, not_5_out, not_6_out, not_7_out, not_8_out, not_9_out,
       not_10_out, not_11_out, not_12_out, not_13_out, not_14_out, not_15_out, not_16_out, not_17_out,
       not_18_out, not_19_out, not_20_out, not_21_out, not_22_out, not_23_out, not_24_out, not_25_out,
       not_26_out, not_27_out, not_28_out, not_29_out, not_30_out, not_31_out, not_32_out, not_33_out,
       not_34_out, not_35_out, not_36_out, not_37_out, not_38_out, not_39_out, not_40_out;

  not not_1 (not_1_out, b);
  not not_2 (not_2_out, d);
  not not_3 (not_3_out, b);
  not not_4 (not_4_out, d);
  not not_5 (not_5_out, e);
  not not_6 (not_6_out, b);
  not not_7 (not_7_out, c);
  not not_8 (not_8_out, b);
  not not_9 (not_9_out, c);
  not not_10 (not_10_out, e);
  not not_11 (not_11_out, b);
  not not_12 (not_12_out, c);
  not not_13 (not_13_out, d);
  not not_14 (not_14_out, a);
  not not_15 (not_15_out, a);
  not not_16 (not_16_out, e);
  not not_17 (not_17_out, a);
  not not_18 (not_18_out, d);
  not not_19 (not_19_out, a);
  not not_20 (not_20_out, d);
  not not_21 (not_21_out, e);
  not not_22 (not_22_out, a);
  not not_23 (not_23_out, c);
  not not_24 (not_24_out, a);
  not not_25 (not_25_out, c);
  not not_26 (not_26_out, e);
  not not_27 (not_27_out, a);
  not not_28 (not_28_out, c);
  not not_29 (not_29_out, d);
  not not_30 (not_30_out, a);
  not not_31 (not_31_out, b);
  not not_32 (not_32_out, a);
  not not_33 (not_33_out, b);
  not not_34 (not_34_out, e);
  not not_35 (not_35_out, a);
  not not_36 (not_36_out, b);
  not not_37 (not_37_out, d);
  not not_38 (not_38_out, a);
  not not_39 (not_39_out, b);
  not not_40 (not_40_out, c);
  and and_1 (G, a, not_1_out, c, not_2_out, e);
  and and_2 (H, a, not_3_out, c, not_4_out, not_5_out);
  and and_3 (I, a, not_6_out, not_7_out, d, e);
  and and_4 (J, a, not_8_out, not_9_out, d, not_10_out);
  and and_5 (K, a, not_11_out, not_12_out, not_13_out, e);
  and and_6 (L, not_14_out, b, c, d, e);
  and and_7 (M, not_15_out, b, c, d, not_16_out);
  and and_8 (N, not_17_out, b, c, not_18_out, e);
  and and_9 (O, not_19_out, b, c, not_20_out, not_21_out);
  and and_10 (P, not_22_out, b, not_23_out, d, e);
  and and_11 (Q, not_24_out, b, not_25_out, d, not_26_out);
  and and_12 (R, not_27_out, b, not_28_out, not_29_out, e);
  and and_13 (S, not_30_out, not_31_out, c, d, e);
  and and_14 (T, not_32_out, not_33_out, c, d, not_34_out);
  and and_15 (U, not_35_out, not_36_out, c, not_37_out, e);
  and and_16 (V, not_38_out, not_39_out, not_40_out, d, e);
endmodule

module \CRC解码器  (
  input  g5,
  input  g4,
  input  g3,
  input  g2,
  input  g1,
  output d1,
  output d2,
  output d3,
  output d4,
  output d5,
  output d6,
  output d7,
  output d8,
  output d9,
  output d10,
  output d11,
  output d12,
  output d13,
  output d14,
  output d15,
  output d16,
  output r1,
  output r2,
  output r3,
  output r4,
  output r5
);

  wire not_1_out, not_2_out, not_3_out, not_4_out, not_5_out, not_6_out, not_7_out, not_8_out, not_9_out,
       not_10_out, not_11_out, not_12_out, not_13_out, not_14_out, not_15_out, not_16_out, not_17_out,
       not_18_out, not_19_out, not_20_out, not_21_out, not_22_out, not_23_out, not_24_out, not_25_out,
       not_26_out, not_27_out, not_28_out, not_29_out, not_30_out, not_31_out, not_32_out, not_33_out,
       not_34_out, not_35_out, not_36_out, not_37_out, not_38_out;

  not not_1 (not_1_out, g4);
  not not_2 (not_2_out, g2);
  not not_3 (not_3_out, g5);
  not not_4 (not_4_out, g3);
  not not_5 (not_5_out, g4);
  not not_6 (not_6_out, g5);
  not not_7 (not_7_out, g1);
  not not_8 (not_8_out, g4);
  not not_9 (not_9_out, g2);
  not not_10 (not_10_out, g4);
  not not_11 (not_11_out, g1);
  not not_12 (not_12_out, g2);
  not not_13 (not_13_out, g1);
  not not_14 (not_14_out, g2);
  and and_1 (d11, g5, g3, g2);
  not not_15 (not_15_out, g3);
  not not_16 (not_16_out, g4);
  not not_17 (not_17_out, g5);
  not not_18 (not_18_out, g3);
  not not_19 (not_19_out, g4);
  not not_20 (not_20_out, g1);
  not not_21 (not_21_out, g5);
  not not_22 (not_22_out, g2);
  not not_23 (not_23_out, g1);
  not not_24 (not_24_out, g5);
  not not_25 (not_25_out, g3);
  not not_26 (not_26_out, g2);
  not not_27 (not_27_out, g4);
  not not_28 (not_28_out, g3);
  not not_29 (not_29_out, g1);
  not not_30 (not_30_out, g5);
  not not_31 (not_31_out, g4);
  not not_32 (not_32_out, g2);
  not not_33 (not_33_out, g1);
  not not_34 (not_34_out, g3);
  not not_35 (not_35_out, g2);
  not not_36 (not_36_out, g4);
  not not_37 (not_37_out, g3);
  not not_38 (not_38_out, g1);
  and and_2 (d1, not_1_out, g3, not_2_out, g1);
  and and_3 (d2, not_3_out, g4, not_4_out, g2);
  and and_4 (d3, g5, not_5_out, g3);
  and and_5 (d4, not_6_out, g4, g1);
  and and_6 (d5, g5, g2, not_7_out);
  and and_7 (d6, g5, not_8_out, not_9_out, g1);
  and and_8 (d7, not_10_out, g3, g2, g1);
  and and_9 (d8, g4, g3, g2, not_11_out);
  and and_10 (d9, g5, g4, not_12_out, not_13_out);
  and and_11 (d10, g5, g4, not_14_out, g1);
  and and_12 (d12, g4, not_15_out, g1);
  and and_13 (d13, g5, not_16_out, g2);
  and and_14 (d14, not_17_out, not_18_out, g2, g1);
  and and_15 (d15, not_19_out, g3, g2, not_20_out);
  and and_16 (d16, not_21_out, g4, g3, not_22_out, not_23_out);
  and and_17 (r1, not_24_out, not_25_out, not_26_out, g1);
  and and_18 (r2, not_27_out, not_28_out, g2, not_29_out);
  and and_19 (r3, not_30_out, not_31_out, g3, not_32_out, not_33_out);
  and and_20 (r4, g4, not_34_out, not_35_out);
  and and_21 (r5, g5, not_36_out, not_37_out, not_38_out);
endmodule
