// Logisim project alu2.circ as structural Verilog
// CAS
module \_8位可控加减法器  (
  input  [7:0] X,
  input  [7:0] Y,
  input  Sub,
  output [7:0] S,
  output Cout,
  output Overflow
);

  wire xor_2_out, xor_3_out, xor_4_out, xor_5_out, xor_6_out, xor_7_out, xor_8_out, xor_9_out,
       \一位全加器fa封装1_1_si , \一位全加器fa封装1_2_cout , \一位全加器fa封装1_3_cout , \一位全加器fa封装1_4_cout , \一位全加器fa封装1_5_cout ,
       \一位全加器fa封装1_6_cout , \一位全加器fa封装1_7_cout , \一位全加器fa封装1_8_cout , \一位全加器fa封装1_9_cout ;
  wire [8:0] \运算指示 ;

  xor xor_1 (Overflow, \一位全加器fa封装1_1_si , S[7]);
  \一位全加器FA封装1  \u_一位全加器fa封装1_1  (
    .Cout(Cout), .Si(\一位全加器fa封装1_1_si ), .Cin(\一位全加器fa封装1_2_cout ), .Xi(X[7]), .Yi(xor_2_out));
  \一位全加器FA封装1  \u_一位全加器fa封装1_2  (
    .Cout(\一位全加器fa封装1_2_cout ), .Si(S[7]), .Cin(\一位全加器fa封装1_3_cout ), .Xi(X[7]), .Yi(xor_2_out));
  xor xor_2 (xor_2_out, Y[7], Sub);
  \一位全加器FA封装1  \u_一位全加器fa封装1_3  (
    .Cout(\一位全加器fa封装1_3_cout ), .Si(S[6]), .Cin(\一位全加器fa封装1_5_cout ), .Xi(X[6]), .Yi(xor_3_out));
  xor xor_3 (xor_3_out, Y[6], Sub);
  xor xor_4 (xor_4_out, Y[5], Sub);
  \一位全加器FA封装1  \u_一位全加器fa封装1_4  (
    .Cout(\一位全加器fa封装1_4_cout ), .Si(S[4]), .Cin(\一位全加器fa封装1_6_cout ), .Xi(X[4]), .Yi(xor_5_out));
  \一位全加器FA封装1  \u_一位全加器fa封装1_5  (
    .Cout(\一位全加器fa封装1_5_cout ), .Si(S[5]), .Cin(\一位全加器fa封装1_4_cout ), .Xi(X[5]), .Yi(xor_4_out));
  xor xor_5 (xor_5_out, Y[4], Sub);
  \一位全加器FA封装1  \u_一位全加器fa封装1_6  (
    .Cout(\一位全加器fa封装1_6_cout ), .Si(S[3]), .Cin(\一位全加器fa封装1_7_cout ), .Xi(X[3]), .Yi(xor_6_out));
  xor xor_6 (xor_6_out, Y[3], Sub);
  \一位全加器FA封装1  \u_一位全加器fa封装1_7  (
    .Cout(\一位全加器fa封装1_7_cout ), .Si(S[2]), .Cin(\一位全加器fa封装1_8_cout ), .Xi(X[2]), .Yi(xor_7_out));
  xor xor_7 (xor_7_out, Y[2], Sub);
  \一位全加器FA封装1  \u_一位全加器fa封装1_8  (
    .Cout(\一位全加器fa封装1_8_cout ), .Si(S[1]), .Cin(\一位全加器fa封装1_9_cout ), .Xi(X[1]), .Yi(xor_8_out));
  xor xor_8 (xor_8_out, Y[1], Sub);
  // Probe on X
  // Probe on Y
  // Probe on S
  \一位全加器FA封装1  \u_一位全加器fa封装1_9  (.Cout(\一位全加器fa封装1_9_cout ), .Si(S[0]), .Cin(Sub), .Xi(X[0]), .Yi(xor_9_out));
  xor xor_9 (xor_9_out, Y[0], Sub);
  DotMatrix #(.inputtype("column"), .matrixcols(3), .matrixrows(3), .persist(0), .dotshape("square")) dotmatrix_1 (
    .col0(\运算指示 [8:6]), .col1(\运算指示 [5:3]), .col2(\运算指示 [2:0]));
  // Probe on X
  // Probe on Y
  // Probe on S
  Multiplexer #(.select(1), .width(9), .disabled("Z"), .enable("false")) multiplexer_1 (
    .in0(9'hba), .in1(9'h92), .out(\运算指示 ), .sel(Sub));

  // Other names for the same wires on the sheet: OF = Overflow

  // Notes on the sheet:
  //   X: pull=down
  //   Sub: pull=down
  //   Cout: pull=down
  //   Y: pull=down
  //   Overflow: pull=down
  //   S: pull=down
  //   8位可控加减法器
  //   输入引脚区
  //   输出引脚区
  //   功能说明：  8位可控加减法器    Sub=0: S = X＋Y  Sub=1:S = X－Y   Cout为最高位进位位，Overflow为有符号溢出标志
  //   =
  //   有符号
  //   =
  //   无符号
endmodule

// CLA74182
module \_4位先行进位74182  (
  input  G4,
  input  P4,
  input  G3,
  input  P3,
  input  G2,
  input  P2,
  input  G1,
  input  P1,
  input  Cin,
  output C4,
  output C3,
  output C2,
  output C1,
  output G_star,
  output P_star
);

  wire and_2_out, and_3_out, and_4_out, and_5_out, and_6_out, and_7_out, and_8_out, and_9_out, and_10_out,
       and_11_out, and_12_out, and_13_out, and_14_out;

  and and_1 (P_star, P4, P3, P2, P1);
  or or_1 (C4, G4, and_2_out, and_3_out, and_5_out, and_8_out);
  and and_2 (and_2_out, P4, G3);
  and and_3 (and_3_out, P4, P3, G2);
  and and_4 (and_4_out, P4, G3);
  and and_5 (and_5_out, P4, P3, P2, G1);
  or or_2 (G_star, G4, and_4_out, and_6_out, and_7_out);
  and and_6 (and_6_out, P4, P3, G2);
  and and_7 (and_7_out, P4, P3, P2, G1);
  and and_8 (and_8_out, P4, P3, P2, P1, Cin);
  and and_9 (and_9_out, P3, G2);
  or or_3 (C3, G3, and_9_out, and_10_out, and_11_out);
  and and_10 (and_10_out, P3, P2, G1);
  and and_11 (and_11_out, P3, P2, P1, Cin);
  or or_4 (C2, G2, and_12_out, and_13_out);
  and and_12 (and_12_out, P2, G1);
  and and_13 (and_13_out, P2, P1, Cin);
  or or_5 (C1, G1, and_14_out);
  and and_14 (and_14_out, P1, Cin);

  // Notes on the sheet:
  //   P1: pull=down
  //   G3: pull=down
  //   P4: pull=down
  //   Cin: pull=down
  //   P2: pull=down
  //   G1: pull=down
  //   P3: pull=down
  //   G4: pull=down
  //   G2: pull=down
  //   输入引脚区
  //   4位先行进位电路
  //   请根据以上引脚以及隧道信号设计完成74LS182先行进位电路，尽可能使用多输入逻辑门，并分析电路延迟
  //   输出引脚区
endmodule

// 4位快速加法器
module \_4位快速加法器  (
  input  [3:0] X,
  input  [3:0] Y,
  input  C0,
  output [3:0] S,
  output C4,
  output C3,
  output G_star,
  output P_star
);

  wire and_1_out, and_2_out, and_3_out, and_4_out, \n4位先行进位74182_1_c1 , \n4位先行进位74182_1_c2 , xor_1_out,
       xor_2_out, xor_3_out, xor_4_out;

  \_4位先行进位74182  \u_4位先行进位74182_1  (
    .G4(and_1_out), .P4(xor_1_out), .G3(and_2_out), .P3(xor_2_out), .G2(and_3_out), .P2(xor_3_out),
    .G1(and_4_out), .P1(xor_4_out), .Cin(C0), .C4(C4), .C3(C3), .C2(\n4位先行进位74182_1_c2 ),
    .C1(\n4位先行进位74182_1_c1 ), .G_star(G_star), .P_star(P_star));
  and and_1 (and_1_out, X[3], Y[3]);
  \一位全加器FA封装1  \u_一位全加器fa封装1_1  (.Si(S[3]), .Cin(C3), .Xi(X[3]), .Yi(Y[3]));  // open: Cout
  xor xor_1 (xor_1_out, X[3], Y[3]);
  xor xor_2 (xor_2_out, X[2], Y[2]);
  and and_2 (and_2_out, X[2], Y[2]);
  \一位全加器FA封装1  \u_一位全加器fa封装1_2  (.Si(S[2]), .Cin(\n4位先行进位74182_1_c2 ), .Xi(X[2]), .Yi(Y[2]));  // open: Cout
  and and_3 (and_3_out, X[1], Y[1]);
  \一位全加器FA封装1  \u_一位全加器fa封装1_3  (.Si(S[1]), .Cin(\n4位先行进位74182_1_c1 ), .Xi(X[1]), .Yi(Y[1]));  // open: Cout
  xor xor_3 (xor_3_out, X[1], Y[1]);
  and and_4 (and_4_out, X[0], Y[0]);
  // Probe on X
  // Probe on Y
  // Probe on S
  \一位全加器FA封装1  \u_一位全加器fa封装1_4  (.Si(S[0]), .Cin(C0), .Xi(X[0]), .Yi(Y[0]));  // open: Cout
  xor xor_4 (xor_4_out, X[0], Y[0]);
  // Probe on X
  // Probe on Y
  // Probe on S

  // Notes on the sheet:
  //   Y: pull=down
  //   X: pull=down
  //   C0: pull=down
  //   输入引脚区
  //   4位快速加法器
  //   输出引脚区
  //   功能说明:4位Adder  S=X+Y，C4、C3分别为最高位、次高位进位位，C0为进位输入， G* P*为成组进位生成传递函数
  //   +
  //   =
  //   有符号加法
  //   +
  //   =
  //   无符号加法
endmodule

// 16位快速加法器
module \_16位快速加法器  (
  input  [15:0] X,
  input  [15:0] Y,
  input  C0,
  output C16,
  output C15,
  output G_star,
  output P_star,
  output [15:0] S
);

  wire \n4位先行进位74182_1_c1 , \n4位先行进位74182_1_c2 , \n4位先行进位74182_1_c3 , \n4位快速加法器_1_g_star ,
       \n4位快速加法器_1_p_star , \n4位快速加法器_2_g_star , \n4位快速加法器_2_p_star , \n4位快速加法器_3_g_star ,
       \n4位快速加法器_3_p_star , \n4位快速加法器_4_g_star , \n4位快速加法器_4_p_star ;

  \_4位先行进位74182  \u_4位先行进位74182_1  (
    .G4(\n4位快速加法器_1_g_star ), .P4(\n4位快速加法器_1_p_star ), .G3(\n4位快速加法器_2_g_star ), .P3(\n4位快速加法器_2_p_star ),
    .G2(\n4位快速加法器_3_g_star ), .P2(\n4位快速加法器_3_p_star ), .G1(\n4位快速加法器_4_g_star ), .P1(\n4位快速加法器_4_p_star ),
    .Cin(C0), .C3(\n4位先行进位74182_1_c3 ), .C2(\n4位先行进位74182_1_c2 ), .C1(\n4位先行进位74182_1_c1 ), .G_star(G_star),
    .P_star(P_star));  // open: C4
  \_4位快速加法器  \u_4位快速加法器_1  (
    .X(X[15:12]), .Y(Y[15:12]), .C0(\n4位先行进位74182_1_c3 ), .S(S[15:12]), .C4(C16),
    .G_star(\n4位快速加法器_1_g_star ), .P_star(\n4位快速加法器_1_p_star ), .C3(C15));
  \_4位快速加法器  \u_4位快速加法器_2  (
    .X(X[11:8]), .Y(Y[11:8]), .C0(\n4位先行进位74182_1_c2 ), .S(S[11:8]), .G_star(\n4位快速加法器_2_g_star ),
    .P_star(\n4位快速加法器_2_p_star ));  // open: C4, C3
  \_4位快速加法器  \u_4位快速加法器_3  (
    .X(X[7:4]), .Y(Y[7:4]), .C0(\n4位先行进位74182_1_c1 ), .S(S[7:4]), .G_star(\n4位快速加法器_3_g_star ),
    .P_star(\n4位快速加法器_3_p_star ));  // open: C4, C3
  // Probe on X
  // Probe on Y
  // Probe on S
  \_4位快速加法器  \u_4位快速加法器_4  (
    .X(X[3:0]), .Y(Y[3:0]), .C0(C0), .S(S[3:0]), .G_star(\n4位快速加法器_4_g_star ), .P_star(\n4位快速加法器_4_p_star ));  // open: C4, C3
  // Probe on X
  // Probe on Y
  // Probe on S

  // Other names for the same wires on the sheet: S0[3:0] = S[3:0]; S1[3:0] = S[7:4]; S2[3:0] = S[11:8];
  //   S3[3:0] = S[15:12]; X0[3:0] = X[3:0]; X1[3:0] = X[7:4]; X2[3:0] = X[11:8]; X3[3:0] = X[15:12]; Y0[3:0] = Y[3:0];
  //   Y1[3:0] = Y[7:4]; Y2[3:0] = Y[11:8]; Y3[3:0] = Y[15:12]

  // Notes on the sheet:
  //   X: pull=down
  //   C0: pull=down
  //   Y: pull=down
  //   输入引脚区
  //   16位快速加法器
  //   输出引脚区
  //   功能说明：16位Adder  S=X＋Y，C16、C15分别为最高位、次高位进位位，C0为进位输入， G* P*为成组进位生成传递函数
  //   +
  //   =
  //   有符号加法
  //   +
  //   =
  //   无符号加法
endmodule

// 32位加法器
module \_32位快速加法器  (
  input  C0,
  input  [31:0] X,
  input  [31:0] Y,
  output C32,
  output C31,
  output [31:0] S
);

  wire \n4位先行进位74182_1_c1 , \n16位快速加法器_2_g_star , \n16位快速加法器_2_p_star ;

  \_4位先行进位74182  \u_4位先行进位74182_1  (
    .G1(\n16位快速加法器_2_g_star ), .P1(\n16位快速加法器_2_p_star ), .Cin(C0), .C1(\n4位先行进位74182_1_c1 ));  // open: G4, P4, G3, P3, G2, P2, C4, C3, C2, G_star, P_star
  \_16位快速加法器  \u_16位快速加法器_1  (
    .X(X[31:16]), .Y(Y[31:16]), .C0(\n4位先行进位74182_1_c1 ), .S(S[31:16]), .C16(C32), .C15(C31));  // open: G_star, P_star
  // Probe on X
  // Probe on Y
  // Probe on S
  \_16位快速加法器  \u_16位快速加法器_2  (
    .X(X[15:0]), .Y(Y[15:0]), .C0(C0), .S(S[15:0]), .G_star(\n16位快速加法器_2_g_star ),
    .P_star(\n16位快速加法器_2_p_star ));  // open: C16, C15
  // Probe on X
  // Probe on Y
  // Probe on S

  // Other names for the same wires on the sheet: S0[3:0] = S[3:0]; S1[3:0] = S[7:4]; S2[3:0] = S[11:8];
  //   S3[3:0] = S[15:12]; S4[3:0] = S[19:16]; S5[3:0] = S[23:20]; S6[3:0] = S[27:24]; S7[3:0] = S[31:28];
  //   X0[3:0] = X[3:0]; X1[3:0] = X[7:4]; X2[3:0] = X[11:8]; X3[3:0] = X[15:12]; X4[3:0] = X[19:16];
  //   X5[3:0] = X[23:20]; X6[3:0] = X[27:24]; X7[3:0] = X[31:28]; Y0[3:0] = Y[3:0]; Y1[3:0] = Y[7:4];
  //   Y2[3:0] = Y[11:8]; Y3[3:0] = Y[15:12]; Y4[3:0] = Y[19:16]; Y5[3:0] = Y[23:20]; Y6[3:0] = Y[27:24];
  //   Y7[3:0] = Y[31:28]

  // Notes on the sheet:
  //   C0: pull=down
  //   Y: pull=down
  //   X: pull=down
  //   输入引脚区
  //   32位快速加法器
  //   功能说明：利用已完成的74182以及4位快速加法器构建速度最快的32位加法器 S = X ＋ Y，并分析电路延迟；
  //   输出引脚区
  //   +
  //   =
  //   有符号加法
  //   +
  //   =
  //   无符号加法
  //   C32、C31分别为最高位、次高位进位位，C0为进位输入
endmodule

// 5位阵列乘法器
module \_5位阵列乘法器  (
  input  [4:0] X,
  input  [4:0] Y,
  output [9:0] \乘积 
);

  wire X0Y1, X0Y2, X0Y3, X0Y4, X1Y0, X1Y1, X1Y2, X1Y3, X1Y4, X2Y0, X2Y1, X2Y2, X2Y3, X2Y4, X3Y0, X3Y1, X3Y2,
       X3Y3, X3Y4, X4Y0, X4Y1, X4Y2, X4Y3, X4Y4, \一位全加器fa封装3_2_cout , \一位全加器fa封装3_2_si , \一位全加器fa封装3_3_cout ,
       \一位全加器fa封装3_4_cout , \一位全加器fa封装3_4_si , \一位全加器fa封装3_5_cout , \一位全加器fa封装3_5_si , \一位全加器fa封装3_6_cout ,
       \一位全加器fa封装3_7_cout , \一位全加器fa封装3_7_si , \一位全加器fa封装3_8_cout , \一位全加器fa封装3_8_si , \一位全加器fa封装3_9_cout ,
       \一位全加器fa封装3_9_si , \一位全加器fa封装3_10_cout , \一位全加器fa封装3_11_cout , \一位全加器fa封装3_11_si ,
       \一位全加器fa封装3_12_cout , \一位全加器fa封装3_12_si , \一位全加器fa封装3_13_cout , \一位全加器fa封装3_13_si ,
       \一位全加器fa封装3_14_cout , \一位全加器fa封装3_15_cout , \一位全加器fa封装3_15_si , \一位全加器fa封装3_16_cout ,
       \一位全加器fa封装3_16_si , \一位全加器fa封装3_17_cout , \一位全加器fa封装3_18_cout , \一位全加器fa封装3_18_si ,
       \一位全加器fa封装3_19_cout , \一位全加器fa封装3_20_cout ;

  \一位全加器FA封装3  \u_一位全加器fa封装3_1  (
    .Cout(\乘积 [9]), .Si(\乘积 [8]), .Cin(\一位全加器fa封装3_2_cout ), .Xi(\一位全加器fa封装3_3_cout ), .Yi(X4Y4));
  // Probe on X
  \一位全加器FA封装3  \u_一位全加器fa封装3_2  (
    .Cout(\一位全加器fa封装3_2_cout ), .Si(\一位全加器fa封装3_2_si ), .Cin(\一位全加器fa封装3_4_cout ), .Xi(X3Y4), .Yi(X4Y3));
  \一位全加器FA封装3  \u_一位全加器fa封装3_3  (
    .Cout(\一位全加器fa封装3_3_cout ), .Si(\乘积 [7]), .Cin(\一位全加器fa封装3_5_cout ), .Xi(\一位全加器fa封装3_6_cout ),
    .Yi(\一位全加器fa封装3_2_si ));
  \一位全加器FA封装3  \u_一位全加器fa封装3_4  (
    .Cout(\一位全加器fa封装3_4_cout ), .Si(\一位全加器fa封装3_4_si ), .Cin(\一位全加器fa封装3_7_cout ), .Xi(X3Y3), .Yi(X4Y2));
  \一位全加器FA封装3  \u_一位全加器fa封装3_5  (
    .Cout(\一位全加器fa封装3_5_cout ), .Si(\一位全加器fa封装3_5_si ), .Cin(\一位全加器fa封装3_8_cout ), .Xi(X2Y4),
    .Yi(\一位全加器fa封装3_4_si ));
  \一位全加器FA封装3  \u_一位全加器fa封装3_6  (
    .Cout(\一位全加器fa封装3_6_cout ), .Si(\乘积 [6]), .Cin(\一位全加器fa封装3_9_cout ), .Xi(\一位全加器fa封装3_10_cout ),
    .Yi(\一位全加器fa封装3_5_si ));
  // Probe on Y
  \一位全加器FA封装3  \u_一位全加器fa封装3_7  (
    .Cout(\一位全加器fa封装3_7_cout ), .Si(\一位全加器fa封装3_7_si ), .Cin(\一位全加器fa封装3_11_cout ), .Xi(X3Y2), .Yi(X4Y1));
  \一位全加器FA封装3  \u_一位全加器fa封装3_8  (
    .Cout(\一位全加器fa封装3_8_cout ), .Si(\一位全加器fa封装3_8_si ), .Cin(\一位全加器fa封装3_12_cout ), .Xi(X2Y3),
    .Yi(\一位全加器fa封装3_7_si ));
  \一位全加器FA封装3  \u_一位全加器fa封装3_9  (
    .Cout(\一位全加器fa封装3_9_cout ), .Si(\一位全加器fa封装3_9_si ), .Cin(\一位全加器fa封装3_13_cout ), .Xi(X1Y4),
    .Yi(\一位全加器fa封装3_8_si ));
  \一位全加器FA封装3  \u_一位全加器fa封装3_10  (
    .Cout(\一位全加器fa封装3_10_cout ), .Si(\乘积 [5]), .Cin(\一位全加器fa封装3_14_cout ), .Xi(1'b0), .Yi(\一位全加器fa封装3_9_si ));
  \一位全加器FA封装3  \u_一位全加器fa封装3_11  (
    .Cout(\一位全加器fa封装3_11_cout ), .Si(\一位全加器fa封装3_11_si ), .Cin(1'b0), .Xi(X3Y1), .Yi(X4Y0));
  \一位全加器FA封装3  \u_一位全加器fa封装3_12  (
    .Cout(\一位全加器fa封装3_12_cout ), .Si(\一位全加器fa封装3_12_si ), .Cin(\一位全加器fa封装3_15_cout ), .Xi(X2Y2),
    .Yi(\一位全加器fa封装3_11_si ));
  \一位全加器FA封装3  \u_一位全加器fa封装3_13  (
    .Cout(\一位全加器fa封装3_13_cout ), .Si(\一位全加器fa封装3_13_si ), .Cin(\一位全加器fa封装3_16_cout ), .Xi(X1Y3),
    .Yi(\一位全加器fa封装3_12_si ));
  \一位全加器FA封装3  \u_一位全加器fa封装3_14  (
    .Cout(\一位全加器fa封装3_14_cout ), .Si(\乘积 [4]), .Cin(\一位全加器fa封装3_17_cout ), .Xi(X0Y4), .Yi(\一位全加器fa封装3_13_si ));
  \一位全加器FA封装3  \u_一位全加器fa封装3_15  (
    .Cout(\一位全加器fa封装3_15_cout ), .Si(\一位全加器fa封装3_15_si ), .Cin(1'b0), .Xi(X2Y1), .Yi(X3Y0));
  \一位全加器FA封装3  \u_一位全加器fa封装3_16  (
    .Cout(\一位全加器fa封装3_16_cout ), .Si(\一位全加器fa封装3_16_si ), .Cin(\一位全加器fa封装3_18_cout ), .Xi(X1Y2),
    .Yi(\一位全加器fa封装3_15_si ));
  \一位全加器FA封装3  \u_一位全加器fa封装3_17  (
    .Cout(\一位全加器fa封装3_17_cout ), .Si(\乘积 [3]), .Cin(\一位全加器fa封装3_19_cout ), .Xi(X0Y3), .Yi(\一位全加器fa封装3_16_si ));
  \一位全加器FA封装3  \u_一位全加器fa封装3_18  (
    .Cout(\一位全加器fa封装3_18_cout ), .Si(\一位全加器fa封装3_18_si ), .Cin(1'b0), .Xi(X1Y1), .Yi(X2Y0));
  \一位全加器FA封装3  \u_一位全加器fa封装3_19  (
    .Cout(\一位全加器fa封装3_19_cout ), .Si(\乘积 [2]), .Cin(\一位全加器fa封装3_20_cout ), .Xi(X0Y2), .Yi(\一位全加器fa封装3_18_si ));
  // Probe on X
  // Probe on Y
  // Probe on \乘积 
  \一位全加器FA封装3  \u_一位全加器fa封装3_20  (.Cout(\一位全加器fa封装3_20_cout ), .Si(\乘积 [1]), .Cin(1'b0), .Xi(X0Y1), .Yi(X1Y0));
  \_5位乘法与门阵列  \u_5位乘法与门阵列_1  (
    .X(X), .XY4({X4Y4, X3Y4, X2Y4, X1Y4, X0Y4}), .XY3({X4Y3, X3Y3, X2Y3, X1Y3, X0Y3}),
    .XY2({X4Y2, X3Y2, X2Y2, X1Y2, X0Y2}), .XY1({X4Y1, X3Y1, X2Y1, X1Y1, X0Y1}),
    .XY0({X4Y0, X3Y0, X2Y0, X1Y0, \乘积 [0]}), .Y(Y));

  // Other names for the same wires on the sheet: P[9:0] = \乘积 ; P1 = \乘积 [1]; P2 = \乘积 [2]; P3 = \乘积 [3];
  //   P4 = \乘积 [4]; P5 = \乘积 [5]; P6 = \乘积 [6]; P7 = \乘积 [7]; P8 = \乘积 [8]; P9 = \乘积 [9]; P0 = \乘积 [0];
  //   X0Y0 = \乘积 [0]; XY0[4:0] = {X4Y0, X3Y0, X2Y0, X1Y0, \乘积 [0]}; XY1[4:0] = {X4Y1, X3Y1, X2Y1, X1Y1, X0Y1};
  //   XY2[4:0] = {X4Y2, X3Y2, X2Y2, X1Y2, X0Y2}; XY3[4:0] = {X4Y3, X3Y3, X2Y3, X1Y3, X0Y3};
  //   XY4[4:0] = {X4Y4, X3Y4, X2Y4, X1Y4, X0Y4}

  // Notes on the sheet:
  //   Y: pull=down
  //   X: pull=down
  //   5位无符号阵列乘法器
  //   输入引脚区
  //   功能说明：利用一位全加器构成5位×5位的无符号数阵列乘法器，乘积=X×Y，并分析电路延迟；
  //   输出引脚区
  //   ×
  //   =
endmodule

// 6位补码乘法器
module \_6位补码阵列乘法器  (
  input  [5:0] X,
  input  [5:0] Y,
  output [10:0] \乘积 
);

  wire [4:0] X_t, Y_t;
  wire [5:0] negator_1_out, negator_3_out;
  wire [9:0] \n5位阵列乘法器_1_乘积 , negator_2_out;

  // Probe on X
  \_5位阵列乘法器  \u_5位阵列乘法器_1  (.\乘积 (\n5位阵列乘法器_1_乘积 ), .X(X_t), .Y(Y_t));
  Negator #(.width(6)) negator_1 (.in(X), .out(negator_1_out));
  // Probe on Y
  Multiplexer #(.select(1), .width(5), .disabled("Z"), .enable("false")) multiplexer_1 (
    .in0(X[4:0]), .in1(negator_1_out[4:0]), .out(X_t), .sel(X[5]));
  xor xor_1 (\乘积 [10], X[5], Y[5]);
  Multiplexer #(.select(1), .width(10), .disabled("Z"), .enable("false")) multiplexer_2 (
    .in0(\n5位阵列乘法器_1_乘积 ), .in1(negator_2_out), .out(\乘积 [9:0]), .sel(\乘积 [10]));
  Negator #(.width(10)) negator_2 (.in(\n5位阵列乘法器_1_乘积 ), .out(negator_2_out));
  Negator #(.width(6)) negator_3 (.in(Y), .out(negator_3_out));
  Multiplexer #(.select(1), .width(5), .disabled("Z"), .enable("false")) multiplexer_3 (
    .in0(Y[4:0]), .in1(negator_3_out[4:0]), .out(Y_t), .sel(Y[5]));
  // Probe on X
  // Probe on Y
  // Probe on \乘积 

  // Other names for the same wires on the sheet: P[10:0] = \乘积 ; P0 = \乘积 [0]; P1 = \乘积 [1]; P2 = \乘积 [2];
  //   P3 = \乘积 [3]; P4 = \乘积 [4]; P5 = \乘积 [5]; P6 = \乘积 [6]; P7 = \乘积 [7]; P8 = \乘积 [8]; P9 = \乘积 [9];
  //   P10 = \乘积 [10]; X4_0[4:0] = X[4:0]; Y4_0[4:0] = Y[4:0]

  // Notes on the sheet:
  //   6位补码阵列乘法器
  //   输入引脚区
  //   功能说明：利用五位阵列乘法器6位×6位的补码阵列乘法器，乘积P = X × Y，尝试计算 －32 × 1，分析结果  
  //   输出引脚区
  //   ×
  //   =
endmodule

module \_5位无符号乘法流水线  (
  output [4:0] X,
  output [9:0] P2,
  output [9:0] P3,
  output [9:0] P4,
  output [9:0] P5,
  output [4:0] Y
);

  wire CLK, not_1_out, OK, \一位全加器fa封装3_1_cout , \一位全加器fa封装3_1_si , \一位全加器fa封装3_2_cout , \一位全加器fa封装3_4_cout ,
       \一位全加器fa封装3_4_si , \一位全加器fa封装3_5_cout , \一位全加器fa封装3_5_si , \一位全加器fa封装3_6_cout , \一位全加器fa封装3_7_cout ,
       \一位全加器fa封装3_8_cout , \一位全加器fa封装3_9_cout , \一位全加器fa封装3_9_si , \一位全加器fa封装3_11_cout , \一位全加器fa封装3_11_si ,
       \一位全加器fa封装3_12_cout , \一位全加器fa封装3_13_cout , \一位全加器fa封装3_14_cout , \一位全加器fa封装3_14_si ,
       \一位全加器fa封装3_15_cout , \一位全加器fa封装3_15_si , \一位全加器fa封装3_16_cout , \一位全加器fa封装3_17_cout ,
       \一位全加器fa封装3_18_cout , \一位全加器fa封装3_19_cout , \一位全加器fa封装3_19_si , \一位全加器fa封装3_21_cout ,
       \一位全加器fa封装3_22_cout , \一位全加器fa封装3_22_si , \一位全加器fa封装3_23_cout , \一位全加器fa封装3_23_si ,
       \一位全加器fa封装3_24_cout , \一位全加器fa封装3_25_cout , \一位全加器fa封装3_26_cout , \一位全加器fa封装3_26_si ,
       \一位全加器fa封装3_27_cout , \一位全加器fa封装3_28_cout , \一位全加器fa封装3_29_cout , \一位全加器fa封装3_29_si ,
       \一位全加器fa封装3_31_cout , \一位全加器fa封装3_31_si , \一位全加器fa封装3_32_cout , \一位全加器fa封装3_33_cout ,
       \一位全加器fa封装3_34_cout , \一位全加器fa封装3_34_si , \一位全加器fa封装3_35_cout , \一位全加器fa封装3_35_si ,
       \一位全加器fa封装3_36_cout , \一位全加器fa封装3_37_cout , \一位全加器fa封装3_38_cout ;
  wire [3:0] \乘法线流水接口_3_out_19_2 ;
  wire [4:0] \n5位乘法与门阵列_1_xy0 , \n5位乘法与门阵列_1_xy1 , \n5位乘法与门阵列_1_xy2 , \n5位乘法与门阵列_1_xy3 , \n5位乘法与门阵列_1_xy4 ,
       X_t, Y_t, \乘法线流水接口_1_x_prime , \乘法线流水接口_1_xy0_prime , \乘法线流水接口_1_xy1_prime , \乘法线流水接口_1_xy2_prime ,
       \乘法线流水接口_1_xy3_2 , \乘法线流水接口_1_xy4_2 , \乘法线流水接口_1_y_prime , \乘法线流水接口_2_x_prime , \乘法线流水接口_2_xy0_prime ,
       \乘法线流水接口_2_xy1_prime , \乘法线流水接口_2_xy2_prime , \乘法线流水接口_2_xy3_2 , \乘法线流水接口_2_xy4_2 ,
       \乘法线流水接口_2_y_prime , \乘法线流水接口_3_x_prime , \乘法线流水接口_3_xy0_prime , \乘法线流水接口_3_xy1_prime ,
       \乘法线流水接口_3_xy2_prime , \乘法线流水接口_3_xy3_2 , \乘法线流水接口_3_xy4_2 , \乘法线流水接口_3_y_prime , \乘法线流水接口_4_x_prime ,
       \乘法线流水接口_4_y_prime ;
  wire [5:0] counter_1_q;
  wire [6:1] \一位全加器fa封装3_8_si ;
  wire [7:2] \一位全加器fa封装3_18_si ;
  wire [8:3] \一位全加器fa封装3_27_si ;
  wire [9:0] multiplier_1_out, P, \乘法线流水接口_1_out_19 , \乘法线流水接口_2_out_19 , \乘法线流水接口_4_out_19 ;
  wire [9:4] \一位全加器fa封装3_38_si , \乘法线流水接口_3_out_19 ;

  Clock #(.highDuration(1), .lowDuration(1)) clock_1 (.out(CLK));
  Counter #(.width(6), .max('h3f), .ongoal("wrap"), .trigger("rising"), .behavior("old")) counter_1 (
    .Q(counter_1_q), .clk(CLK));  // open: load, D, count, carry, clr, preset
  \_5位乘法与门阵列  \u_5位乘法与门阵列_1  (
    .X(X), .XY4(\n5位乘法与门阵列_1_xy4 ), .XY3(\n5位乘法与门阵列_1_xy3 ), .XY2(\n5位乘法与门阵列_1_xy2 ),
    .XY1(\n5位乘法与门阵列_1_xy1 ), .XY0(\n5位乘法与门阵列_1_xy0 ), .Y(Y));
  \一位全加器FA封装3  \u_一位全加器fa封装3_1  (
    .Cout(\一位全加器fa封装3_1_cout ), .Si(\一位全加器fa封装3_1_si ), .Cin(1'b0), .Xi(\n5位乘法与门阵列_1_xy1 [3]),
    .Yi(\n5位乘法与门阵列_1_xy0 [4]));
  \一位全加器FA封装3  \u_一位全加器fa封装3_2  (
    .Cout(\一位全加器fa封装3_2_cout ), .Si(\一位全加器fa封装3_8_si [4]), .Cin(\一位全加器fa封装3_4_cout ),
    .Xi(\一位全加器fa封装3_7_cout ), .Yi(\一位全加器fa封装3_1_si ));
  \一位全加器FA封装3  \u_一位全加器fa封装3_3  (
    .Cout(\一位全加器fa封装3_8_si [6]), .Si(\一位全加器fa封装3_8_si [5]), .Cin(\一位全加器fa封装3_1_cout ),
    .Xi(\一位全加器fa封装3_2_cout ), .Yi(\n5位乘法与门阵列_1_xy1 [4]));
  // Probe on X
  \一位全加器FA封装3  \u_一位全加器fa封装3_4  (
    .Cout(\一位全加器fa封装3_4_cout ), .Si(\一位全加器fa封装3_4_si ), .Cin(1'b0), .Xi(\n5位乘法与门阵列_1_xy1 [2]),
    .Yi(\n5位乘法与门阵列_1_xy0 [3]));
  \一位全加器FA封装3  \u_一位全加器fa封装3_5  (
    .Cout(\一位全加器fa封装3_5_cout ), .Si(\一位全加器fa封装3_5_si ), .Cin(1'b0), .Xi(\n5位乘法与门阵列_1_xy1 [1]),
    .Yi(\n5位乘法与门阵列_1_xy0 [2]));
  \一位全加器FA封装3  \u_一位全加器fa封装3_6  (
    .Cout(\一位全加器fa封装3_6_cout ), .Si(\一位全加器fa封装3_8_si [2]), .Cin(\一位全加器fa封装3_8_cout ), .Xi(1'b0),
    .Yi(\一位全加器fa封装3_5_si ));
  \一位全加器FA封装3  \u_一位全加器fa封装3_7  (
    .Cout(\一位全加器fa封装3_7_cout ), .Si(\一位全加器fa封装3_8_si [3]), .Cin(\一位全加器fa封装3_5_cout ),
    .Xi(\一位全加器fa封装3_6_cout ), .Yi(\一位全加器fa封装3_4_si ));
  ROM #(.addrWidth(6), .dataWidth(10), .Select("low")) rom_1 (.addr(counter_1_q), .data({Y, X}));
  // Probe on Y
  \一位全加器FA封装3  \u_一位全加器fa封装3_8  (
    .Cout(\一位全加器fa封装3_8_cout ), .Si(\一位全加器fa封装3_8_si [1]), .Cin(1'b0), .Xi(\n5位乘法与门阵列_1_xy1 [0]),
    .Yi(\n5位乘法与门阵列_1_xy0 [1]));
  \乘法线流水接口  \u_乘法线流水接口_1  (
    .X(X), .Y(Y), .XY0(\n5位乘法与门阵列_1_xy0 ), .XY1(\n5位乘法与门阵列_1_xy1 ), .XY2(\n5位乘法与门阵列_1_xy2 ),
    .XY3(\n5位乘法与门阵列_1_xy3 ), .XY4(\n5位乘法与门阵列_1_xy4 ),
    .in_8({3'b000, \一位全加器fa封装3_8_si , \n5位乘法与门阵列_1_xy0 [0]}), .CLK(CLK), .X_prime(\乘法线流水接口_1_x_prime ),
    .Y_prime(\乘法线流水接口_1_y_prime ), .XY0_prime(\乘法线流水接口_1_xy0_prime ), .XY1_prime(\乘法线流水接口_1_xy1_prime ),
    .XY2_prime(\乘法线流水接口_1_xy2_prime ), .XY3_2(\乘法线流水接口_1_xy3_2 ), .XY4_2(\乘法线流水接口_1_xy4_2 ),
    .out_19(\乘法线流水接口_1_out_19 ), .EDU(P2));  // open: 同步清零_高电平有效, 使能端_低电平有效
  \一位全加器FA封装3  \u_一位全加器fa封装3_9  (
    .Cout(\一位全加器fa封装3_9_cout ), .Si(\一位全加器fa封装3_9_si ), .Cin(1'b0), .Xi(\乘法线流水接口_1_xy2_prime [4]),
    .Yi(\乘法线流水接口_1_out_19 [6]));
  \一位全加器FA封装3  \u_一位全加器fa封装3_10  (
    .Si(\一位全加器fa封装3_18_si [7]), .Cin(\一位全加器fa封装3_9_cout ), .Xi(\一位全加器fa封装3_12_cout ), .Yi(1'b0));  // open: Cout
  // Probe on \乘法线流水接口_1_x_prime 
  \一位全加器FA封装3  \u_一位全加器fa封装3_11  (
    .Cout(\一位全加器fa封装3_11_cout ), .Si(\一位全加器fa封装3_11_si ), .Cin(1'b0), .Xi(\乘法线流水接口_1_xy2_prime [3]),
    .Yi(\乘法线流水接口_1_out_19 [5]));
  \一位全加器FA封装3  \u_一位全加器fa封装3_12  (
    .Cout(\一位全加器fa封装3_12_cout ), .Si(\一位全加器fa封装3_18_si [6]), .Cin(\一位全加器fa封装3_11_cout ),
    .Xi(\一位全加器fa封装3_13_cout ), .Yi(\一位全加器fa封装3_9_si ));
  \一位全加器FA封装3  \u_一位全加器fa封装3_13  (
    .Cout(\一位全加器fa封装3_13_cout ), .Si(\一位全加器fa封装3_18_si [5]), .Cin(\一位全加器fa封装3_14_cout ),
    .Xi(\一位全加器fa封装3_17_cout ), .Yi(\一位全加器fa封装3_11_si ));
  // Probe on X_t
  // Probe on Y_t
  // Probe on P
  // Probe on \乘法线流水接口_1_y_prime 
  \一位全加器FA封装3  \u_一位全加器fa封装3_14  (
    .Cout(\一位全加器fa封装3_14_cout ), .Si(\一位全加器fa封装3_14_si ), .Cin(1'b0), .Xi(\乘法线流水接口_1_xy2_prime [2]),
    .Yi(\乘法线流水接口_1_out_19 [4]));
  \一位全加器FA封装3  \u_一位全加器fa封装3_15  (
    .Cout(\一位全加器fa封装3_15_cout ), .Si(\一位全加器fa封装3_15_si ), .Cin(1'b0), .Xi(\乘法线流水接口_1_xy2_prime [1]),
    .Yi(\乘法线流水接口_1_out_19 [3]));
  \一位全加器FA封装3  \u_一位全加器fa封装3_16  (
    .Cout(\一位全加器fa封装3_16_cout ), .Si(\一位全加器fa封装3_18_si [3]), .Cin(\一位全加器fa封装3_18_cout ), .Xi(1'b0),
    .Yi(\一位全加器fa封装3_15_si ));
  \一位全加器FA封装3  \u_一位全加器fa封装3_17  (
    .Cout(\一位全加器fa封装3_17_cout ), .Si(\一位全加器fa封装3_18_si [4]), .Cin(\一位全加器fa封装3_15_cout ),
    .Xi(\一位全加器fa封装3_16_cout ), .Yi(\一位全加器fa封装3_14_si ));
  \乘法线流水接口  \u_乘法线流水接口_2  (
    .X(\乘法线流水接口_1_x_prime ), .Y(\乘法线流水接口_1_y_prime ), .XY0(\乘法线流水接口_1_xy0_prime ),
    .XY1(\乘法线流水接口_1_xy1_prime ), .XY2(\乘法线流水接口_1_xy2_prime ), .XY3(\乘法线流水接口_1_xy3_2 ),
    .XY4(\乘法线流水接口_1_xy4_2 ), .in_8({2'b00, \一位全加器fa封装3_18_si , \乘法线流水接口_1_out_19 [1:0]}), .CLK(CLK),
    .X_prime(\乘法线流水接口_2_x_prime ), .Y_prime(\乘法线流水接口_2_y_prime ), .XY0_prime(\乘法线流水接口_2_xy0_prime ),
    .XY1_prime(\乘法线流水接口_2_xy1_prime ), .XY2_prime(\乘法线流水接口_2_xy2_prime ), .XY3_2(\乘法线流水接口_2_xy3_2 ),
    .XY4_2(\乘法线流水接口_2_xy4_2 ), .out_19(\乘法线流水接口_2_out_19 ), .EDU(P3));  // open: 同步清零_高电平有效, 使能端_低电平有效
  \一位全加器FA封装3  \u_一位全加器fa封装3_18  (
    .Cout(\一位全加器fa封装3_18_cout ), .Si(\一位全加器fa封装3_18_si [2]), .Cin(1'b0), .Xi(\乘法线流水接口_1_xy2_prime [0]),
    .Yi(\乘法线流水接口_1_out_19 [2]));
  LED #(.active("true")) led_1 (.in(OK));
  \一位全加器FA封装3  \u_一位全加器fa封装3_19  (
    .Cout(\一位全加器fa封装3_19_cout ), .Si(\一位全加器fa封装3_19_si ), .Cin(1'b0), .Xi(\乘法线流水接口_2_xy3_2 [4]),
    .Yi(\乘法线流水接口_2_out_19 [7]));
  \一位全加器FA封装3  \u_一位全加器fa封装3_20  (
    .Si(\一位全加器fa封装3_27_si [8]), .Cin(\一位全加器fa封装3_19_cout ), .Xi(\一位全加器fa封装3_21_cout ), .Yi(1'b0));  // open: Cout
  \一位全加器FA封装3  \u_一位全加器fa封装3_21  (
    .Cout(\一位全加器fa封装3_21_cout ), .Si(\一位全加器fa封装3_27_si [7]), .Cin(\一位全加器fa封装3_22_cout ),
    .Xi(\一位全加器fa封装3_25_cout ), .Yi(\一位全加器fa封装3_19_si ));
  // Probe on \乘法线流水接口_2_x_prime 
  \一位全加器FA封装3  \u_一位全加器fa封装3_22  (
    .Cout(\一位全加器fa封装3_22_cout ), .Si(\一位全加器fa封装3_22_si ), .Cin(1'b0), .Xi(\乘法线流水接口_2_xy3_2 [3]),
    .Yi(\乘法线流水接口_2_out_19 [6]));
  \一位全加器FA封装3  \u_一位全加器fa封装3_23  (
    .Cout(\一位全加器fa封装3_23_cout ), .Si(\一位全加器fa封装3_23_si ), .Cin(1'b0), .Xi(\乘法线流水接口_2_xy3_2 [2]),
    .Yi(\乘法线流水接口_2_out_19 [5]));
  \一位全加器FA封装3  \u_一位全加器fa封装3_24  (
    .Cout(\一位全加器fa封装3_24_cout ), .Si(\一位全加器fa封装3_27_si [5]), .Cin(\一位全加器fa封装3_26_cout ),
    .Xi(\一位全加器fa封装3_28_cout ), .Yi(\一位全加器fa封装3_23_si ));
  \一位全加器FA封装3  \u_一位全加器fa封装3_25  (
    .Cout(\一位全加器fa封装3_25_cout ), .Si(\一位全加器fa封装3_27_si [6]), .Cin(\一位全加器fa封装3_23_cout ),
    .Xi(\一位全加器fa封装3_24_cout ), .Yi(\一位全加器fa封装3_22_si ));
  // Probe on \乘法线流水接口_2_y_prime 
  \一位全加器FA封装3  \u_一位全加器fa封装3_26  (
    .Cout(\一位全加器fa封装3_26_cout ), .Si(\一位全加器fa封装3_26_si ), .Cin(1'b0), .Xi(\乘法线流水接口_2_xy3_2 [1]),
    .Yi(\乘法线流水接口_2_out_19 [4]));
  \一位全加器FA封装3  \u_一位全加器fa封装3_27  (
    .Cout(\一位全加器fa封装3_27_cout ), .Si(\一位全加器fa封装3_27_si [3]), .Cin(1'b0), .Xi(\乘法线流水接口_2_xy3_2 [0]),
    .Yi(\乘法线流水接口_2_out_19 [3]));
  \一位全加器FA封装3  \u_一位全加器fa封装3_28  (
    .Cout(\一位全加器fa封装3_28_cout ), .Si(\一位全加器fa封装3_27_si [4]), .Cin(\一位全加器fa封装3_27_cout ), .Xi(1'b0),
    .Yi(\一位全加器fa封装3_26_si ));
  \乘法线流水接口  \u_乘法线流水接口_3  (
    .X(\乘法线流水接口_2_x_prime ), .Y(\乘法线流水接口_2_y_prime ), .XY0(\乘法线流水接口_2_xy0_prime ),
    .XY1(\乘法线流水接口_2_xy1_prime ), .XY2(\乘法线流水接口_2_xy2_prime ), .XY3(\乘法线流水接口_2_xy3_2 ),
    .XY4(\乘法线流水接口_2_xy4_2 ), .in_8({1'b0, \一位全加器fa封装3_27_si , \乘法线流水接口_2_out_19 [2:0]}), .CLK(CLK),
    .X_prime(\乘法线流水接口_3_x_prime ), .Y_prime(\乘法线流水接口_3_y_prime ), .XY0_prime(\乘法线流水接口_3_xy0_prime ),
    .XY1_prime(\乘法线流水接口_3_xy1_prime ), .XY2_prime(\乘法线流水接口_3_xy2_prime ), .XY3_2(\乘法线流水接口_3_xy3_2 ),
    .XY4_2(\乘法线流水接口_3_xy4_2 ), .out_19({\乘法线流水接口_3_out_19 , \乘法线流水接口_3_out_19_2 }), .EDU(P4));  // open: 同步清零_高电平有效, 使能端_低电平有效
  \一位全加器FA封装3  \u_一位全加器fa封装3_29  (
    .Cout(\一位全加器fa封装3_29_cout ), .Si(\一位全加器fa封装3_29_si ), .Cin(1'b0), .Xi(\乘法线流水接口_3_xy4_2 [4]),
    .Yi(\乘法线流水接口_3_out_19 [8]));
  \一位全加器FA封装3  \u_一位全加器fa封装3_30  (
    .Si(\一位全加器fa封装3_38_si [9]), .Cin(\一位全加器fa封装3_29_cout ), .Xi(\一位全加器fa封装3_32_cout ), .Yi(1'b0));  // open: Cout
  // Probe on \乘法线流水接口_3_x_prime 
  \一位全加器FA封装3  \u_一位全加器fa封装3_31  (
    .Cout(\一位全加器fa封装3_31_cout ), .Si(\一位全加器fa封装3_31_si ), .Cin(1'b0), .Xi(\乘法线流水接口_3_xy4_2 [3]),
    .Yi(\乘法线流水接口_3_out_19 [7]));
  \一位全加器FA封装3  \u_一位全加器fa封装3_32  (
    .Cout(\一位全加器fa封装3_32_cout ), .Si(\一位全加器fa封装3_38_si [8]), .Cin(\一位全加器fa封装3_31_cout ),
    .Xi(\一位全加器fa封装3_33_cout ), .Yi(\一位全加器fa封装3_29_si ));
  \一位全加器FA封装3  \u_一位全加器fa封装3_33  (
    .Cout(\一位全加器fa封装3_33_cout ), .Si(\一位全加器fa封装3_38_si [7]), .Cin(\一位全加器fa封装3_34_cout ),
    .Xi(\一位全加器fa封装3_36_cout ), .Yi(\一位全加器fa封装3_31_si ));
  // Probe on \乘法线流水接口_3_y_prime 
  \一位全加器FA封装3  \u_一位全加器fa封装3_34  (
    .Cout(\一位全加器fa封装3_34_cout ), .Si(\一位全加器fa封装3_34_si ), .Cin(1'b0), .Xi(\乘法线流水接口_3_xy4_2 [2]),
    .Yi(\乘法线流水接口_3_out_19 [6]));
  \一位全加器FA封装3  \u_一位全加器fa封装3_35  (
    .Cout(\一位全加器fa封装3_35_cout ), .Si(\一位全加器fa封装3_35_si ), .Cin(1'b0), .Xi(\乘法线流水接口_3_xy4_2 [1]),
    .Yi(\乘法线流水接口_3_out_19 [5]));
  \一位全加器FA封装3  \u_一位全加器fa封装3_36  (
    .Cout(\一位全加器fa封装3_36_cout ), .Si(\一位全加器fa封装3_38_si [6]), .Cin(\一位全加器fa封装3_35_cout ),
    .Xi(\一位全加器fa封装3_37_cout ), .Yi(\一位全加器fa封装3_34_si ));
  \一位全加器FA封装3  \u_一位全加器fa封装3_37  (
    .Cout(\一位全加器fa封装3_37_cout ), .Si(\一位全加器fa封装3_38_si [5]), .Cin(\一位全加器fa封装3_38_cout ), .Xi(1'b0),
    .Yi(\一位全加器fa封装3_35_si ));
  \乘法线流水接口  \u_乘法线流水接口_4  (
    .X(\乘法线流水接口_3_x_prime ), .Y(\乘法线流水接口_3_y_prime ), .XY0(\乘法线流水接口_3_xy0_prime ),
    .XY1(\乘法线流水接口_3_xy1_prime ), .XY2(\乘法线流水接口_3_xy2_prime ), .XY3(\乘法线流水接口_3_xy3_2 ),
    .XY4(\乘法线流水接口_3_xy4_2 ), .in_8({\一位全加器fa封装3_38_si , \乘法线流水接口_3_out_19_2 }), .CLK(CLK),
    .X_prime(\乘法线流水接口_4_x_prime ), .Y_prime(\乘法线流水接口_4_y_prime ), .out_19(\乘法线流水接口_4_out_19 ), .EDU(P5));  // open: XY0_prime, XY1_prime, XY2_prime, XY3_2, XY4_2, 同步清零_高电平有效, 使能端_低电平有效
  \一位全加器FA封装3  \u_一位全加器fa封装3_38  (
    .Cout(\一位全加器fa封装3_38_cout ), .Si(\一位全加器fa封装3_38_si [4]), .Cin(1'b0), .Xi(\乘法线流水接口_3_xy4_2 [0]),
    .Yi(\乘法线流水接口_3_out_19 [4]));
  // Probe on \乘法线流水接口_4_x_prime 
  // Probe on \乘法线流水接口_4_y_prime 
  // Probe on multiplier_1_out
  // Probe on \乘法线流水接口_4_out_19 
  Multiplier #(.width(5)) multiplier_1 (
    .a(\乘法线流水接口_4_x_prime ), .b(\乘法线流水接口_4_y_prime ), .out(multiplier_1_out[4:0]),
    .cout(multiplier_1_out[9:5]));  // open: cin
  Comparator #(.width(10), .mode("twosComplement")) comparator_1 (
    .a(multiplier_1_out), .b(\乘法线流水接口_4_out_19 ), .eq(OK));  // open: gt, lt
  not not_1 (not_1_out, OK);
  LED #(.active("true")) \u_不正确  (.in(not_1_out));

  // Other names for the same wires on the sheet: 被乘数X[4:0] = X; 乘数Y[4:0] = Y

  // Notes on the sheet:
  //   contents of rom_1 (hex, n*v repeats v):
  //   3fe 58 23 1e 2c 34 66 380 3c0 55 3b3 12 18 3dc 390 390 3b9 45 1e 398 21 14 5c 6 3d2 3aa 41 28 394
  //   38c 5a 3f8 28 1c 48 3b4 3b2 45 3bc 0 399 3e0 26 44 69 55 8 3e0 8 4b 38a 0 3b4 1a 78 393 0 18 40 3b0
  //   390 3f0 7e 50
  //   第1步
  //   ×
  //   =
  //   第2步
  //   第3步
  //   第4步
endmodule

module \原码一位乘法器  (
  input  [7:0] X,
  input  [7:0] Y,
  output [15:0] \乘积 
);

  wire counter_1_carry, counter_2_q, counter_3_carry, \n8位串行加法器_1_cout , not_1_out, RST, xor_1_out, \时钟_out ;
  wire [0:0] \n8位串行加法器_1_s ;
  wire [7:0] multiplexer_1_out, multiplexer_2_out, multiplexer_3_out;

  Counter #(.width(4), .max('h9), .ongoal("stay"), .trigger("rising"), .behavior("new")) counter_1 (
    .carry(counter_1_carry), .clk(\时钟_out ), .clr(RST));  // open: load, D, count, Q, preset, down
  Clock #(.highDuration(1), .lowDuration(1)) \u_时钟  (.out(\时钟_out ));
  Counter #(.width(1), .max('h1), .ongoal("stay"), .trigger("rising"), .behavior("new")) counter_2 (
    .Q(counter_2_q), .clk(\时钟_out ), .clr(RST));  // open: load, D, count, carry, preset, down
  not not_1 (not_1_out, counter_1_carry);
  Counter #(.width(4), .max('h9), .ongoal("stay"), .trigger("rising"), .behavior("new")) counter_3 (
    .carry(counter_3_carry), .clk(\时钟_out ), .clr(RST));  // open: load, D, count, Q, preset, down
  Multiplexer #(.select(1), .width(1), .disabled("Z"), .enable("false")) multiplexer_1 (
    .in0(\n8位串行加法器_1_cout ), .in1(xor_1_out), .out(multiplexer_1_out[7]), .sel(counter_3_carry));
  xor xor_1 (xor_1_out, Y[7], X[7]);
  Register #(.width(8), .trigger("rising"), .Select("low")) register_1 (
    .D(multiplexer_1_out), .en(not_1_out), .Q(\乘积 [15:8]), .clk(\时钟_out ), .clr(RST));
  Button \u_复位  (.out(RST));
  // Probe on \乘积 [15:8]
  \_8位串行加法器  \u_8位串行加法器_1  (
    .X(\乘积 [15:8]), .Y(multiplexer_2_out), .Cin(1'b0), .S({multiplexer_1_out[6:0], \n8位串行加法器_1_s [0]}),
    .Cout(\n8位串行加法器_1_cout ));  // open: Overflow
  Multiplexer #(.select(1), .width(8), .disabled("Z"), .enable("false")) multiplexer_2 (
    .in0({8{1'b0}}), .in1(X), .out(multiplexer_2_out), .sel(\乘积 [0]));
  // Probe on \乘积 [7:0]
  Multiplexer #(.select(1), .width(8), .disabled("Z"), .enable("false")) multiplexer_3 (
    .in0(Y), .in1({\n8位串行加法器_1_s [0], \乘积 [7:1]}), .out(multiplexer_3_out), .sel(counter_2_q));
  Register #(.width(8), .trigger("rising"), .Select("low")) Y_2 (
    .D(multiplexer_3_out), .en(not_1_out), .Q(\乘积 [7:0]), .clk(\时钟_out ), .clr(RST));
  // Probe on X
  // Probe on Y
  // Probe on \乘积 

  // Notes on the sheet:
  //   8位无符号一位乘法器
  //   ∑
  //   功能说明: 原码一位乘法器   乘积=X*Y，要求采用原码一位乘法实现，最终结果能输出在乘积引脚上
  //   逻辑右移一位
  //   ∑+Yn|X|
  //   后续所有实验中凡是涉及存储器件，如寄存器、计数器、RAM等，必须增加统一的复位信号RST，方便系统复位
  //   输入输出引脚区
  //   ×
  //   =
  //   核心算法：{ ∑ , Y } = { ∑ ＋ Y  |X|  , Y  } / 2
  //   这里对符号位的运算留了一手，方便后续改进
  //   而且，没有检查运算完成后能否自动停止
  //   n
  //   平台给的算例可能存在问题，它并没有考虑最后的符号位，而且原码乘法也把符号位乘进去了
endmodule

module \补码一位乘法器  (
  input  [7:0] X,
  input  [7:0] Y,
  output [15:0] \乘积 
);

  wire clock_1_out, counter_1_carry, counter_2_q, counter_3_q, multiplexer_3_out, \n8位串行加法器_1_cout ,
       not_1_out, RST;
  wire [0:0] \n8位串行加法器_1_s ;
  wire [1:1] Yn_1_2_q;
  wire [7:0] multiplexer_1_out, multiplexer_2_out, negator_1_out, or_1_out;

  Counter #(.width(4), .max('h9), .ongoal("stay"), .trigger("rising"), .behavior("new")) counter_1 (
    .carry(counter_1_carry), .clk(clock_1_out), .clr(RST));  // open: load, D, count, Q, preset, down
  not not_1 (not_1_out, counter_1_carry);
  Clock #(.highDuration(1), .lowDuration(1)) clock_1 (.out(clock_1_out));
  Negator #(.width(8)) negator_1 (.in(X), .out(negator_1_out));
  // Probe on \乘积 [15:8]
  Register #(.width(8), .trigger("rising"), .Select("low")) register (
    .D(or_1_out), .en(not_1_out), .Q(\乘积 [15:8]), .clk(clock_1_out), .clr(RST));
  or or_1 (or_1_out[7], \n8位串行加法器_1_cout , or_1_out[6]);
  Multiplexer #(.select(2), .width(8), .disabled("Z"), .enable("false")) multiplexer_1 (
    .in0({8{1'b0}}), .in1(negator_1_out), .in2(X), .in3({8{1'b0}}), .out(multiplexer_1_out),
    .sel({Yn_1_2_q[1], \乘积 [0]}));
  Counter #(.width(1), .max('h1), .ongoal("stay"), .trigger("rising"), .behavior("new")) counter_2 (
    .Q(counter_2_q), .clk(clock_1_out), .clr(RST));  // open: load, D, count, carry, preset, down
  Button \u_复位  (.out(RST));
  Multiplexer #(.select(1), .width(8), .disabled("Z"), .enable("false")) multiplexer_2 (
    .in0(Y), .in1({\n8位串行加法器_1_s [0], \乘积 [7:1]}), .out(multiplexer_2_out), .sel(counter_2_q));
  \_8位串行加法器  \u_8位串行加法器_1  (
    .X(\乘积 [15:8]), .Y(multiplexer_1_out), .S({or_1_out[6:0], \n8位串行加法器_1_s [0]}), .Cout(\n8位串行加法器_1_cout ));  // open: Cin, Overflow
  // Probe on \乘积 [7:0]
  Register #(.width(8), .trigger("rising"), .Select("low")) Y_2 (
    .D(multiplexer_2_out), .en(not_1_out), .Q(\乘积 [7:0]), .clk(clock_1_out), .clr(RST));
  // Probe on Yn_1_2_q[1]
  Counter #(.width(1), .max('h1), .ongoal("stay"), .trigger("rising"), .behavior("new")) counter_3 (
    .Q(counter_3_q), .clk(clock_1_out), .clr(RST));  // open: load, D, count, carry, preset, down
  Multiplexer #(.select(1), .width(1), .disabled("Z"), .enable("false")) multiplexer_3 (
    .in0(1'b0), .in1(\乘积 [0]), .out(multiplexer_3_out), .sel(counter_3_q));
  Register #(.width(1), .trigger("rising"), .Select("low")) Yn_1_2 (
    .D(multiplexer_3_out), .en(not_1_out), .Q(Yn_1_2_q[1]), .clk(clock_1_out), .clr(RST));
  // Probe on X
  // Probe on Y
  // Probe on \乘积 

  // Notes on the sheet:
  //   8位补码 Booth一位乘法器
  //   功能说明: 补码一位乘法器   乘积=X×Y，要求采用补码一位乘法实现，最终结果能输出在乘积引脚上
  //   注意这里是算术右移而不是逻辑右移
  //   算术右移一位
  //   ∑+ (Yn+1-Yn)补
  //   ∑+=(Yn+1-Yn)[X]补/2
  //   输入输出引脚区
  //   核心算法：{ ∑,Y } = { ∑ ＋（Y      －  Y  ）[X]   , Y } / 2
  //   ×
  //   =
  //   n
  //   n+1
  //   补
endmodule

// ALU
module \算术逻辑运算单元ALU  (
  input  [31:0] X,
  input  [31:0] Y,
  input  [3:0] AluOP,
  output Signed_Overflow,
  output UnSigned_Overflow,
  output Equal,
  output [31:0] Result,
  output [31:0] Result_2
);

  wire comparator_1_lt, comparator_2_lt, comparator_3_lt, comparator_4_lt, comparator_5_gt,
       \n32位快速加法器_1_c31 , \n32位快速加法器_1_c32 , \n32位快速加法器_2_c31 , \n32位快速加法器_2_c32 , or_2_out, xor_2_out,
       xor_3_out;
  wire [4:0] bitselector_1_out, bitselector_2_out, bitselector_3_out;
  wire [31:0] and_1_out, bit_extender_1_out, bit_extender_2_out, divider_1_out, divider_1_rem,
       \n32x32乘法器_1_out_3 , \n32x32乘法器_1_out_4 , \n32位快速加法器_1_s , \n32位快速加法器_2_s , negator_1_out, nor_1_out,
       or_1_out, shifter_1_out, shifter_2_out, shifter_3_out, xor_1_out;

  // Probe on X
  // Probe on X
  // Probe on Y
  // Probe on Y
  Negator #(.width(32)) negator_1 (.in(Y), .out(negator_1_out));
  \_32位快速加法器  \u_32位快速加法器_1  (
    .X(X), .Y(negator_1_out), .C0(1'b0), .S(\n32位快速加法器_1_s ), .C32(\n32位快速加法器_1_c32 ), .C31(\n32位快速加法器_1_c31 ));
  // Probe on AluOP
  \_32位快速加法器  \u_32位快速加法器_2  (
    .X(X), .Y(Y), .C0(1'b0), .S(\n32位快速加法器_2_s ), .C32(\n32位快速加法器_2_c32 ), .C31(\n32位快速加法器_2_c31 ));
  // Probe on Result
  // Probe on Result
  BitSelector #(.width(32), .group(5)) bitselector_1 (.in(Y), .out(bitselector_1_out), .sel(3'b000));
  BitSelector #(.width(32), .group(5)) bitselector_2 (.in(Y), .out(bitselector_2_out), .sel(3'b000));
  BitSelector #(.width(32), .group(5)) bitselector_3 (.in(Y), .out(bitselector_3_out), .sel(3'b000));
  Divider #(.width(32)) divider_1 (.a(X), .b(Y), .out(divider_1_out), .rem(divider_1_rem));  // open: upper
  assign and_1_out = X & Y;  // AND_Gate and_1, 32 bits wide
  assign or_1_out = X | Y;  // OR_Gate or_1, 32 bits wide
  assign xor_1_out = X ^ Y;  // XOR_Gate xor_1, 32 bits wide
  assign nor_1_out = ~(X | Y);  // NOR_Gate nor_1, 32 bits wide
  Comparator #(.width(32), .mode("twosComplement")) comparator_1 (.a(X), .b(Y), .lt(comparator_1_lt));  // open: gt, eq
  Comparator #(.width(32), .mode("unsigned")) comparator_2 (.a(X), .b(Y), .lt(comparator_2_lt));  // open: gt, eq
  Shifter #(.width(32), .shift("ll")) shifter_1 (.in(X), .\dist (bitselector_1_out), .out(shifter_1_out));
  Shifter #(.width(32), .shift("ar")) shifter_2 (.in(X), .\dist (bitselector_2_out), .out(shifter_2_out));
  Shifter #(.width(32), .shift("lr")) shifter_3 (.in(X), .\dist (bitselector_3_out), .out(shifter_3_out));
  assign bit_extender_1_out = {{31{1'b0}}, comparator_1_lt};  // Bit_Extender bit_extender_1
  assign bit_extender_2_out = {{31{1'b0}}, comparator_2_lt};  // Bit_Extender bit_extender_2
  // Probe on Result_2
  \_32X32乘法器  \u_32x32乘法器_1  (.a(X), .b(Y), .out_3(\n32x32乘法器_1_out_3 ), .out_4(\n32x32乘法器_1_out_4 ));
  Multiplexer #(.select(4), .width(32), .disabled("Z"), .enable("false")) multiplexer_1 (
    .in0(shifter_1_out), .in1(shifter_2_out), .in2(shifter_3_out), .in3(\n32x32乘法器_1_out_4 ),
    .in4(divider_1_out), .in5(\n32位快速加法器_2_s ), .in6(\n32位快速加法器_1_s ), .in7(and_1_out), .in8(or_1_out),
    .in9(xor_1_out), .in10(nor_1_out), .in11(bit_extender_1_out), .in12(bit_extender_2_out), .out(Result),
    .sel(AluOP));  // open: in13, in14, in15
  Multiplexer #(.select(4), .width(32), .disabled("Z"), .enable("false")) multiplexer_2 (
    .in0({32{1'b0}}), .in1({32{1'b0}}), .in2({32{1'b0}}), .in3(\n32x32乘法器_1_out_3 ), .in4(divider_1_rem),
    .in5({32{1'b0}}), .in6({32{1'b0}}), .in7({32{1'b0}}), .in8({32{1'b0}}), .in9({32{1'b0}}),
    .in10({32{1'b0}}), .in11({32{1'b0}}), .in12({32{1'b0}}), .in13({32{1'b0}}), .in14({32{1'b0}}),
    .in15({32{1'b0}}), .out(Result_2), .sel(AluOP));
  xor xor_2 (xor_2_out, \n32位快速加法器_2_c31 , \n32位快速加法器_2_c32 );
  xor xor_3 (xor_3_out, \n32位快速加法器_1_c31 , \n32位快速加法器_1_c32 );
  Multiplexer #(.select(4), .width(1), .disabled("Z"), .enable("false")) multiplexer_3 (
    .in0(1'b0), .in1(1'b0), .in2(1'b0), .in3(1'b0), .in4(1'b0), .in5(xor_2_out), .in6(xor_3_out), .in7(1'b0),
    .in8(1'b0), .in9(1'b0), .in10(1'b0), .in11(1'b0), .in12(1'b0), .in13(1'b0), .in14(1'b0), .in15(1'b0),
    .out(Signed_Overflow), .sel(AluOP));
  Comparator #(.width(32), .mode("unsigned")) comparator_3 (
    .a(\n32位快速加法器_2_s ), .b(X), .lt(comparator_3_lt));  // open: gt, eq
  Comparator #(.width(32), .mode("unsigned")) comparator_4 (
    .a(\n32位快速加法器_2_s ), .b(Y), .lt(comparator_4_lt));  // open: gt, eq
  Comparator #(.width(32), .mode("unsigned")) comparator_5 (
    .a(\n32位快速加法器_1_s ), .b(X), .gt(comparator_5_gt));  // open: eq, lt
  Comparator #(.width(32), .mode("twosComplement")) comparator_6 (.a(X), .b(Y), .eq(Equal));  // open: gt, lt
  Multiplexer #(.select(4), .width(1), .disabled("Z"), .enable("false")) multiplexer_4 (
    .in0(1'b0), .in1(1'b0), .in2(1'b0), .in3(1'b0), .in4(1'b0), .in5(or_2_out), .in6(comparator_5_gt),
    .in7(1'b0), .in8(1'b0), .in9(1'b0), .in10(1'b0), .in11(1'b0), .in12(1'b0), .in13(1'b0), .in14(1'b0),
    .in15(1'b0), .out(UnSigned_Overflow), .sel(AluOP));
  or or_2 (or_2_out, comparator_3_lt, comparator_4_lt);

  // Other names for the same wires on the sheet: OF = Signed_Overflow; Result2[31:0] = Result_2; S[3:0] = AluOP;
  //   UOF = UnSigned_Overflow

  // Notes on the sheet:
  //   X: pull=down
  //   AluOP: pull=down
  //   Y: pull=down
  //   32位MIPS运算器
  //   32位MIPS运算器
  //   不要改变此引脚区域内容，也不要改变ALU封装形式
  //   输入引脚
  //   请在下方利用上方输入输出引脚的隧道信号构建ALU电路，ctrl+d复制选择部件
  //   华中科技大学计算机学院 计算机组成原理，鸣谢加州大学伯克利CS61C课程
  //   输出引脚
  //   探测区域
  //   出现的问题：
  //   1、多路选择器有的选择端悬空，而且还是S可能选择到的选择端
  //   2、无符号溢出判断没有理解清楚，减法运算只需要比较被减数和差，而且是无符号比较
endmodule

module \子电路外观测试  (
);

  wire C0, C1, C2, C3, C4, G1, G2, G3, G4, G_star, \n4位快速加法器_1_c3 , \n4位快速加法器_1_c4 , \n4位快速加法器_1_g_star ,
       \n4位快速加法器_1_p_star , \n8位可控加减法器_1_cout , \n8位可控加减法器_1_overflow , \n16位快速加法器_1_c15 , \n16位快速加法器_1_c16 ,
       \n16位快速加法器_1_g_star , \n16位快速加法器_1_p_star , \n32位快速加法器_1_c31 , \n32位快速加法器_1_c32 , P1, P2, P3, P4,
       P_star, undriven_7, undriven_8, undriven_13, undriven_18;
  wire [3:0] \n4位快速加法器_1_s , undriven_2, undriven_6;
  wire [4:0] \n5位无符号乘法流水线_1_x , \n5位无符号乘法流水线_1_y , undriven, undriven_5;
  wire [5:0] undriven_9, undriven_10;
  wire [7:0] \n8位可控加减法器_1_s , undriven_3, undriven_4, undriven_14, undriven_15, undriven_19, undriven_20;
  wire [9:0] \n5位无符号乘法流水线_1_p2 , \n5位无符号乘法流水线_1_p3 , \n5位无符号乘法流水线_1_p4 , \n5位无符号乘法流水线_1_p5 , \n5位阵列乘法器_1_乘积 ;
  wire [10:0] \n6位补码阵列乘法器_1_乘积 ;
  wire [15:0] \n16位快速加法器_1_s , undriven_11, undriven_12, \原码一位乘法器_1_乘积 , \补码一位乘法器_1_乘积 ;
  wire [31:0] \n32位快速加法器_1_s , undriven_16, undriven_17;

  \_8位可控加减法器  \u_8位可控加减法器_1  (
    .X(undriven_3), .Y(undriven_4), .Sub(undriven_7), .S(\n8位可控加减法器_1_s ), .Cout(\n8位可控加减法器_1_cout ),
    .Overflow(\n8位可控加减法器_1_overflow ));
  \_5位阵列乘法器  \u_5位阵列乘法器_1  (.\乘积 (\n5位阵列乘法器_1_乘积 ), .X(undriven), .Y(undriven_5));
  \_4位快速加法器  \u_4位快速加法器_1  (
    .X(undriven_2), .Y(undriven_6), .C0(undriven_8), .S(\n4位快速加法器_1_s ), .C4(\n4位快速加法器_1_c4 ),
    .G_star(\n4位快速加法器_1_g_star ), .P_star(\n4位快速加法器_1_p_star ), .C3(\n4位快速加法器_1_c3 ));
  \_6位补码阵列乘法器  \u_6位补码阵列乘法器_1  (.\乘积 (\n6位补码阵列乘法器_1_乘积 ), .X(undriven_9), .Y(undriven_10));
  \_4位先行进位74182  \u_4位先行进位74182_1  (
    .G4(G4), .P4(P4), .G3(G3), .P3(P3), .G2(G2), .P2(P2), .G1(G1), .P1(P1), .Cin(C0), .C4(C4), .C3(C3),
    .C2(C2), .C1(C1), .G_star(G_star), .P_star(P_star));
  \_16位快速加法器  \u_16位快速加法器_1  (
    .X(undriven_11), .Y(undriven_12), .C0(undriven_13), .S(\n16位快速加法器_1_s ), .C16(\n16位快速加法器_1_c16 ),
    .G_star(\n16位快速加法器_1_g_star ), .P_star(\n16位快速加法器_1_p_star ), .C15(\n16位快速加法器_1_c15 ));
  \_5位无符号乘法流水线  \u_5位无符号乘法流水线_1  (
    .X(\n5位无符号乘法流水线_1_x ), .Y(\n5位无符号乘法流水线_1_y ), .P2(\n5位无符号乘法流水线_1_p2 ), .P3(\n5位无符号乘法流水线_1_p3 ),
    .P4(\n5位无符号乘法流水线_1_p4 ), .P5(\n5位无符号乘法流水线_1_p5 ));
  \_32位快速加法器  \u_32位快速加法器_1  (
    .X(undriven_16), .Y(undriven_17), .C0(undriven_18), .S(\n32位快速加法器_1_s ), .C32(\n32位快速加法器_1_c32 ),
    .C31(\n32位快速加法器_1_c31 ));
  \原码一位乘法器  \u_原码一位乘法器_1  (.X(undriven_14), .Y(undriven_15), .\乘积 (\原码一位乘法器_1_乘积 ));
  \补码一位乘法器  \u_补码一位乘法器_1  (.X(undriven_19), .Y(undriven_20), .\乘积 (\补码一位乘法器_1_乘积 ));

  // Notes on the sheet:
  //   Cout
  //   C4
  //   C3
  //   S
  //   OF
  //   X
  //   可控加减法电路封装测试
  //   S
  //   G*
  //   X
  //   4位快速加法器封装测试
  //   X
  //   P
  //   5位阵列乘法器封装测试
  //   SUB
  //   Y
  //   P*
  //   C0
  //   Y
  //   Y
  //   X
  //   P
  //   6位补码乘法器封装测试
  //   P*
  //   G*
  //   C16
  //   C15
  //   X
  //   16位快速加法器封装测试
  //   Y
  //   最好通过引脚悬浮提示看看连接是否正确，如果有问题，请调整封装引脚位置直至连接正确
  //   S
  //   Y
  //   X
  //   Y
  //   请勿在子电路中增删改，甚至移动引脚位置，这些都可能导致子电路外观---封装发生改变，从而使得测试电路无法正确测试
  //   提交EduCoder平台检测之前，请先检查一下对应子电路的封装连接是否正确，主要查看引脚位置是否连接正确，有否错位未连接等情况
  //   C0
  //   P2
  //   P3
  //   P4
  //   P5
  //   乘法流水线封装测试
  //   74182封装测试
  //   C32
  //   C31
  //   X
  //   X
  //   Y
  //   S
  //   Y
  //   32位快速加法器封装测试
  //   P
  //   原码一位乘法封装测试
  //   C0
  //   X
  //   Y
  //   P
  //   补码一位乘法封装测试
endmodule

module \ALU自动测试  (
  output [7:0] Test_num,
  output Equal
);

  wire ADD, AND, and_1_out, CF, CF_S, CLK, comparator_2_eq, comparator_3_eq, DIV, \EQ__标志 , EQ_OK, EQ_S,
       Halt, MUL, multiplexer_1_out, NEQ, nHalt, NOR, OF, OF_OK, OR, priority_encoder_1_gs, ROK, SAR, SCMP,
       SLL, SLR, SUB, tunnel, UCMP, UOF_OK, XOR, \与 , \乘法 , \减法 , \加法 , \异或 , \悬空检测 , \或 , \或非 , \无符号比较 ,
       \无符号溢出标志 , \有符号比较 , \有符号溢出标志 , \算术右移 , \逻辑右移 , \逻辑左移 , \除法 ;
  wire [2:2] FLAG_Standard;
  wire [3:0] ALUOP, High, Low, Mid;
  wire [7:0] adder_1_out, \单项评分_1_total , \单项评分_1_扣分 , \单项评分_1_正确条数 , \单项评分_2_total , \单项评分_2_扣分 ,
       \单项评分_2_正确条数 , \单项评分_3_total , \单项评分_3_扣分 , \单项评分_3_正确条数 , \单项评分_4_total , \单项评分_4_扣分 , \单项评分_4_正确条数 ,
       \单项评分_5_total , \单项评分_5_扣分 , \单项评分_5_正确条数 , \单项评分_6_total , \单项评分_6_扣分 , \单项评分_6_正确条数 ,
       \单项评分_7_total , \单项评分_7_扣分 , \单项评分_7_正确条数 , \单项评分_8_total , \单项评分_8_扣分 , \单项评分_8_正确条数 ,
       \单项评分_9_total , \单项评分_9_扣分 , \单项评分_9_正确条数 , \单项评分_10_total , \单项评分_10_扣分 , \单项评分_10_正确条数 ,
       \单项评分_11_total , \单项评分_11_扣分 , \单项评分_11_正确条数 , \单项评分_12_total , \单项评分_12_扣分 , \单项评分_12_正确条数 ,
       \单项评分_13_total , \单项评分_13_扣分 , \单项评分_13_正确条数 , \单项评分_14_total , \单项评分_14_扣分 , \单项评分_14_正确条数 ,
       \单项评分_15_total , \单项评分_15_扣分 , \单项评分_15_正确条数 , \单项评分_16_total , \单项评分_16_扣分 , \单项评分_16_正确条数 ,
       \总评分_result ;
  wire [9:0] counter_1_q;
  wire [31:0] bit_extender_1_out, R, R2, R2_Standard, R_Standard, X, Y;

  Clock #(.highDuration(1), .lowDuration(1)) clock_1 (.out(CLK));
  Register #(.width(8), .trigger("rising"), .Select("low")) register_1 (
    .D(adder_1_out), .en(nHalt), .Q(Test_num), .clk(CLK));  // open: clr
  LED #(.active("true")) \u_测试完成  (.in(Halt));
  Counter #(.width(10), .max('h3ff), .ongoal("wrap"), .trigger("rising"), .behavior("old")) counter_1 (
    .count(NEQ), .Q(counter_1_q), .clk(CLK), .clr(Halt));  // open: load, D, carry, preset
  LED #(.active("false")) led_1 (.in(\逻辑左移 ));
  LED #(.active("false")) led_2 (.in(\逻辑右移 ));
  LED #(.active("false")) led_3 (.in(\EQ__标志 ));
  \单项评分  \u_单项评分_1  (
    .EQ(ROK), .EN(nHalt), .\分值 (5'b00101), .CLK(CLK), .\正确条数 (\单项评分_1_正确条数 ), .\扣分 (\单项评分_1_扣分 ),
    .Right(\逻辑左移 ), .ALU_SWITCH(SLL), .Total(\单项评分_1_total ));
  // Probe on \单项评分_1_total 
  // Probe on \单项评分_1_正确条数 
  // Probe on \单项评分_1_扣分 
  Adder #(.width(8)) adder_1 (.a(8'h1), .b(Test_num), .out(adder_1_out));  // open: cin, cout
  not not_1 (nHalt, Halt);
  Comparator #(.width(4), .mode("twosComplement")) comparator_1 (.a(ALUOP), .b(4'b1111), .eq(Halt));  // open: gt, lt
  and and_1 (and_1_out, ~Halt, NEQ);  // AND_Gate
  LED #(.active("false")) led_4 (.in(\算术右移 ));
  LED #(.active("true")) led_5 (.in(\悬空检测 ));
  \单项评分  \u_单项评分_2  (
    .EQ(ROK), .EN(nHalt), .\分值 (5'b00101), .CLK(CLK), .\正确条数 (\单项评分_2_正确条数 ), .\扣分 (\单项评分_2_扣分 ),
    .Right(\算术右移 ), .ALU_SWITCH(SAR), .Total(\单项评分_2_total ));
  // Probe on \单项评分_2_total 
  // Probe on \单项评分_3_total 
  // Probe on \单项评分_2_正确条数 
  // Probe on \单项评分_2_扣分 
  trace trace_1 (
    .in_1(Test_num), .X(X), .Y(Y), .AluOP(ALUOP), .R(R_Standard), .R2(R2_Standard),
    .FLAGS({FLAG_Standard[2], CF_S, EQ_S}));
  RAM #(.addrWidth(10), .dataWidth(32), .bus("separate"), .Select("high")) ram_1 (
    .addr(counter_1_q), .din(X), .str(and_1_out), .clk(CLK));  // open: data, sel, ld, clr
  LED #(.active("false")) led_6 (.in(\与 ));
  LED #(.active("false")) led_7 (.in(\或 ));
  LED #(.active("false")) led_8 (.in(\有符号溢出标志 ));
  \单项评分  \u_单项评分_3  (
    .EQ(ROK), .EN(nHalt), .\分值 (5'b00101), .CLK(CLK), .\正确条数 (\单项评分_3_正确条数 ), .\扣分 (\单项评分_3_扣分 ),
    .Right(\逻辑右移 ), .ALU_SWITCH(SLR), .Total(\单项评分_3_total ));
  // Probe on \单项评分_4_total 
  // Probe on \单项评分_3_正确条数 
  // Probe on \单项评分_4_正确条数 
  // Probe on \单项评分_3_扣分 
  \单项评分  \u_单项评分_4  (
    .EQ(ROK), .EN(nHalt), .\分值 (5'b00101), .CLK(CLK), .\正确条数 (\单项评分_4_正确条数 ), .\扣分 (\单项评分_4_扣分 ),
    .Right(\乘法 ), .ALU_SWITCH(MUL), .Total(\单项评分_4_total ));
  // Probe on \单项评分_6_total 
  // Probe on \单项评分_6_正确条数 
  // Probe on \单项评分_4_扣分 
  // Probe on \单项评分_6_扣分 
  RAM #(.addrWidth(10), .dataWidth(32), .bus("separate"), .Select("high")) ram_2 (
    .addr(counter_1_q), .din(Y), .str(and_1_out), .clk(CLK));  // open: data, sel, ld, clr
  assign bit_extender_1_out = {{28{1'b0}}, ALUOP};  // Bit_Extender bit_extender_1
  LED #(.active("false")) led_9 (.in(\或非 ));
  LED #(.active("false")) led_10 (.in(\异或 ));
  \单项评分  \u_单项评分_5  (
    .EQ(ROK), .EN(nHalt), .\分值 (5'b00101), .CLK(CLK), .\正确条数 (\单项评分_5_正确条数 ), .\扣分 (\单项评分_5_扣分 ),
    .Right(\加法 ), .ALU_SWITCH(ADD), .Total(\单项评分_5_total ));
  \单项评分  \u_单项评分_6  (
    .EQ(ROK), .EN(nHalt), .\分值 (5'b00101), .CLK(CLK), .\正确条数 (\单项评分_6_正确条数 ), .\扣分 (\单项评分_6_扣分 ),
    .Right(\除法 ), .ALU_SWITCH(DIV), .Total(\单项评分_6_total ));
  // Probe on \单项评分_5_total 
  // Probe on \单项评分_5_正确条数 
  // Probe on \单项评分_5_扣分 
  \算术逻辑运算单元ALU  \u_算术逻辑运算单元alu_1  (
    .AluOP(ALUOP), .X(X), .Equal(Equal), .Result(R), .Signed_Overflow(OF), .Y(Y), .Result_2(R2),
    .UnSigned_Overflow(CF));
  LED #(.active("false")) led_11 (.in(\乘法 ));
  LED #(.active("false")) led_12 (.in(\除法 ));
  LED #(.active("false")) led_13 (.in(\无符号溢出标志 ));
  \单项评分  \u_单项评分_7  (
    .EQ(ROK), .EN(nHalt), .\分值 (5'b00101), .CLK(CLK), .\正确条数 (\单项评分_7_正确条数 ), .\扣分 (\单项评分_7_扣分 ),
    .Right(\减法 ), .ALU_SWITCH(SUB), .Total(\单项评分_7_total ));
  // Probe on \单项评分_7_total 
  // Probe on \单项评分_7_正确条数 
  // Probe on \单项评分_7_扣分 
  RAM #(.addrWidth(10), .dataWidth(32), .bus("separate"), .Select("high")) ram_3 (
    .addr(counter_1_q), .din(bit_extender_1_out), .str(and_1_out), .clk(CLK));  // open: data, sel, ld, clr
  LED #(.active("false")) led_14 (.in(\加法 ));
  LED #(.active("false")) led_15 (.in(\减法 ));
  \单项评分  \u_单项评分_8  (
    .EQ(ROK), .EN(nHalt), .\分值 (5'b00101), .CLK(CLK), .\正确条数 (\单项评分_8_正确条数 ), .\扣分 (\单项评分_8_扣分 ),
    .Right(\与 ), .ALU_SWITCH(AND), .Total(\单项评分_8_total ));
  // Probe on \单项评分_8_total 
  // Probe on \单项评分_8_正确条数 
  // Probe on \单项评分_8_扣分 
  \总评分  \u_总评分  (
    .in_1(\单项评分_1_扣分 ), .in_2(\单项评分_2_扣分 ), .in_3(\单项评分_3_扣分 ), .in_4(\单项评分_4_扣分 ), .in_5(\单项评分_6_扣分 ),
    .in_6(\单项评分_5_扣分 ), .in_7(\单项评分_7_扣分 ), .in_8(\单项评分_8_扣分 ), .in_9(\单项评分_9_扣分 ), .in_10(\单项评分_10_扣分 ),
    .in_11(\单项评分_11_扣分 ), .in_12(\单项评分_12_扣分 ), .in_13(\单项评分_14_扣分 ), .in_14(\单项评分_13_扣分 ),
    .in_15(\单项评分_15_扣分 ), .in_16(\单项评分_16_扣分 ), .\悬空扣分 (\悬空检测 ), .Result(\总评分_result ), .High(High),
    .Low(Low), .Mid(Mid));
  Hex_Digit_Display hex_digit_display_1 (.value(High));  // open: dp
  Hex_Digit_Display hex_digit_display_2 (.value(Mid));  // open: dp
  \单项评分  \u_单项评分_9  (
    .EQ(ROK), .EN(nHalt), .\分值 (5'b00101), .CLK(CLK), .\正确条数 (\单项评分_9_正确条数 ), .\扣分 (\单项评分_9_扣分 ),
    .Right(\或 ), .ALU_SWITCH(OR), .Total(\单项评分_9_total ));
  // Probe on nothing
  // Probe on \单项评分_9_正确条数 
  // Probe on \单项评分_9_扣分 
  // Probe on \总评分_result 
  Hex_Digit_Display hex_digit_display_3 (.value(Low));  // open: dp
  LED #(.active("false")) led_16 (.in(\有符号比较 ));
  LED #(.active("false")) led_17 (.in(\无符号比较 ));
  \单项评分  \u_单项评分_10  (
    .EQ(ROK), .EN(nHalt), .\分值 (5'b00101), .CLK(CLK), .\正确条数 (\单项评分_10_正确条数 ), .\扣分 (\单项评分_10_扣分 ),
    .Right(\异或 ), .ALU_SWITCH(XOR), .Total(\单项评分_10_total ));
  // Probe on \单项评分_10_total 
  // Probe on \单项评分_11_total 
  // Probe on \单项评分_10_正确条数 
  // Probe on \单项评分_10_扣分 
  \单项评分  \u_单项评分_11  (
    .EQ(ROK), .EN(nHalt), .\分值 (5'b00101), .CLK(CLK), .\正确条数 (\单项评分_11_正确条数 ), .\扣分 (\单项评分_11_扣分 ),
    .Right(\或非 ), .ALU_SWITCH(NOR), .Total(\单项评分_11_total ));
  // Probe on \单项评分_12_total 
  // Probe on \单项评分_11_正确条数 
  // Probe on \单项评分_12_正确条数 
  // Probe on \单项评分_11_扣分 
  \单项评分  \u_单项评分_12  (
    .EQ(ROK), .EN(nHalt), .\分值 (5'b00101), .CLK(CLK), .\正确条数 (\单项评分_12_正确条数 ), .\扣分 (\单项评分_12_扣分 ),
    .Right(\有符号比较 ), .ALU_SWITCH(SCMP), .Total(\单项评分_12_total ));
  // Probe on \单项评分_14_total 
  // Probe on \单项评分_14_正确条数 
  // Probe on \单项评分_12_扣分 
  // Probe on \单项评分_14_扣分 
  \单项评分  \u_单项评分_13  (
    .EQ(EQ_OK), .EN(nHalt), .\分值 (5'b01000), .CLK(CLK), .\正确条数 (\单项评分_13_正确条数 ), .\扣分 (\单项评分_13_扣分 ),
    .Right(\EQ__标志 ), .ALU_SWITCH(EQ_OK), .Total(\单项评分_13_total ));
  \单项评分  \u_单项评分_14  (
    .EQ(ROK), .EN(nHalt), .\分值 (5'b00101), .CLK(CLK), .\正确条数 (\单项评分_14_正确条数 ), .\扣分 (\单项评分_14_扣分 ),
    .Right(\无符号比较 ), .ALU_SWITCH(UCMP), .Total(\单项评分_14_total ));
  // Probe on \单项评分_13_total 
  // Probe on \单项评分_13_正确条数 
  // Probe on \单项评分_13_扣分 
  \单项评分  \u_单项评分_15  (
    .EQ(OF_OK), .EN(nHalt), .\分值 (5'b01000), .CLK(CLK), .\正确条数 (\单项评分_15_正确条数 ), .\扣分 (\单项评分_15_扣分 ),
    .Right(\有符号溢出标志 ), .ALU_SWITCH(1'b1), .Total(\单项评分_15_total ));
  // Probe on \单项评分_15_total 
  // Probe on \单项评分_15_正确条数 
  // Probe on \单项评分_15_扣分 
  \单项评分  \u_单项评分_16  (
    .EQ(UOF_OK), .EN(nHalt), .\分值 (5'b01000), .CLK(CLK), .\正确条数 (\单项评分_16_正确条数 ), .\扣分 (\单项评分_16_扣分 ),
    .Right(\无符号溢出标志 ), .ALU_SWITCH(1'b1), .Total(\单项评分_16_total ));
  // Probe on \单项评分_16_total 
  // Probe on \单项评分_16_正确条数 
  // Probe on \单项评分_16_扣分 
  // Probe on ALUOP
  Decoder #(.select(4), .tristate("false"), .disabled("Z"), .enable("false")) decoder_1 (
    .out0(SLL), .out1(SAR), .out2(SLR), .out3(MUL), .out4(DIV), .out5(ADD), .out6(SUB), .out7(AND),
    .out8(OR), .out9(XOR), .out10(NOR), .out11(SCMP), .out12(UCMP), .sel(ALUOP));  // open: out13, out14, out15
  xnor xnor_1 (EQ_OK, EQ_S, Equal);
  xnor xnor_2 (OF_OK, FLAG_Standard[2], OF);
  xnor xnor_3 (UOF_OK, CF_S, CF);
  Comparator #(.width(32), .mode("twosComplement")) comparator_2 (
    .a(R_Standard), .b(R), .eq(comparator_2_eq));  // open: gt, lt
  Comparator #(.width(32), .mode("twosComplement")) comparator_3 (
    .a(R2_Standard), .b(R2), .eq(comparator_3_eq));  // open: gt, lt
  Multiplexer #(.select(1), .width(1), .disabled(0), .enable("false")) multiplexer_1 (
    .in0(1'b1), .in1(1'b1), .out(multiplexer_1_out), .sel(CF));
  and and_2 (ROK, comparator_2_eq, comparator_3_eq);
  or or_1 (tunnel, ADD, SUB);
  Priority_Encoder #(.select(1), .disabled("Z")) priority_encoder_1 (
    .in0(multiplexer_1_out), .in1(multiplexer_1_out), .gs(priority_encoder_1_gs));  // open: out, en_out, en_in
  not not_2 (\悬空检测 , priority_encoder_1_gs);
  nand nand_1 (NEQ, EQ_OK, OF_OK, UOF_OK, ROK);

  // Other names for the same wires on the sheet: EQ = Equal; FLAG_Standard[1:0] = {CF_S, EQ_S};
  //   OF_S = FLAG_Standard[2]

  // Notes on the sheet:
  //   操作码为F停止
  //   错误记录X
  //   错误记录Y
  //   运算故障指示灯，红色异常
  //   错误记录ALUOP
  //   3个存储器存储的是所有错误的测试用例
  //   错误扣分值
  //   成绩
  //   ctrl+K驱动时钟自动测试
  //   华中科技大学：计算机组成课程组
  //   悬空扣5分
  //   错误扣分值
  //   各部分分值
  //   各部分扣分
  //   悬空检测
endmodule

// 与门阵列
module \_5位乘法与门阵列  (
  input  [4:0] X,
  input  [4:0] Y,
  output [4:0] XY0,
  output [4:0] XY1,
  output [4:0] XY2,
  output [4:0] XY3,
  output [4:0] XY4
);

  and and_1 (XY0[4], X[4], Y[0]);
  and and_2 (XY1[4], X[4], Y[1]);
  and and_3 (XY2[4], X[4], Y[2]);
  and and_4 (XY3[4], X[4], Y[3]);
  and and_5 (XY4[4], X[4], Y[4]);
  and and_6 (XY0[3], X[3], Y[0]);
  and and_7 (XY1[3], X[3], Y[1]);
  and and_8 (XY2[3], X[3], Y[2]);
  and and_9 (XY3[3], X[3], Y[3]);
  and and_10 (XY4[3], X[3], Y[4]);
  and and_11 (XY0[2], X[2], Y[0]);
  and and_12 (XY1[2], X[2], Y[1]);
  and and_13 (XY2[2], X[2], Y[2]);
  and and_14 (XY3[2], X[2], Y[3]);
  and and_15 (XY4[2], X[2], Y[4]);
  and and_16 (XY0[1], X[1], Y[0]);
  and and_17 (XY0[0], X[0], Y[0]);
  and and_18 (XY1[1], X[1], Y[1]);
  and and_19 (XY1[0], X[0], Y[1]);
  and and_20 (XY2[1], X[1], Y[2]);
  and and_21 (XY2[0], X[0], Y[2]);
  and and_22 (XY3[1], X[1], Y[3]);
  and and_23 (XY3[0], X[0], Y[3]);
  and and_24 (XY4[1], X[1], Y[4]);
  and and_25 (XY4[0], X[0], Y[4]);

  // Other names for the same wires on the sheet: X0Y0 = XY0[0]; X1Y0 = XY0[1]; X2Y0 = XY0[2]; X3Y0 = XY0[3];
  //   X4Y0 = XY0[4]; X0Y1 = XY1[0]; X1Y1 = XY1[1]; X2Y1 = XY1[2]; X3Y1 = XY1[3]; X4Y1 = XY1[4]; X0Y2 = XY2[0];
  //   X1Y2 = XY2[1]; X2Y2 = XY2[2]; X3Y2 = XY2[3]; X4Y2 = XY2[4]; X0Y3 = XY3[0]; X1Y3 = XY3[1]; X2Y3 = XY3[2];
  //   X3Y3 = XY3[3]; X4Y3 = XY3[4]; X0Y4 = XY4[0]; X1Y4 = XY4[1]; X2Y4 = XY4[2]; X3Y4 = XY4[3]; X4Y4 = XY4[4]
endmodule

module \乘法线流水接口  (
  input  [4:0] X,
  input  [4:0] Y,
  input  [4:0] XY0,
  input  [4:0] XY1,
  input  [4:0] XY2,
  input  [4:0] XY3,
  input  [4:0] XY4,
  input  [9:0] in_8,
  input  CLK,
  input  \同步清零_高电平有效 ,
  input  \使能端_低电平有效 ,
  output [4:0] X_prime,
  output [4:0] Y_prime,
  output [4:0] XY0_prime,
  output [4:0] XY1_prime,
  output [4:0] XY2_prime,
  output [4:0] XY3_2,
  output [4:0] XY4_2,
  output [9:0] out_19,
  output [9:0] EDU
);

  wire pull_resistor_2_node;
  wire [4:0] multiplexer_1_out, multiplexer_2_out, multiplexer_3_out, multiplexer_4_out, multiplexer_5_out,
       multiplexer_6_out, multiplexer_7_out;
  wire [9:0] multiplexer_8_out;

  Multiplexer #(.select(1), .width(5), .disabled("Z"), .enable("false")) multiplexer_1 (
    .in0(X), .in1({5{1'b0}}), .out(multiplexer_1_out), .sel(\同步清零_高电平有效 ));
  Multiplexer #(.select(1), .width(5), .disabled("Z"), .enable("false")) multiplexer_2 (
    .in0(Y), .in1({5{1'b0}}), .out(multiplexer_2_out), .sel(\同步清零_高电平有效 ));
  Multiplexer #(.select(1), .width(5), .disabled("Z"), .enable("false")) multiplexer_3 (
    .in0(XY0), .in1({5{1'b0}}), .out(multiplexer_3_out), .sel(\同步清零_高电平有效 ));
  Multiplexer #(.select(1), .width(5), .disabled("Z"), .enable("false")) multiplexer_4 (
    .in0(XY1), .in1({5{1'b0}}), .out(multiplexer_4_out), .sel(\同步清零_高电平有效 ));
  Multiplexer #(.select(1), .width(5), .disabled("Z"), .enable("false")) multiplexer_5 (
    .in0(XY2), .in1({5{1'b0}}), .out(multiplexer_5_out), .sel(\同步清零_高电平有效 ));
  Multiplexer #(.select(1), .width(5), .disabled("Z"), .enable("false")) multiplexer_6 (
    .in0(XY3), .in1({5{1'b0}}), .out(multiplexer_6_out), .sel(\同步清零_高电平有效 ));
  Multiplexer #(.select(1), .width(5), .disabled("Z"), .enable("false")) multiplexer_7 (
    .in0(XY4), .in1({5{1'b0}}), .out(multiplexer_7_out), .sel(\同步清零_高电平有效 ));
  Multiplexer #(.select(1), .width(10), .disabled("Z"), .enable("false")) multiplexer_8 (
    .in0(in_8), .in1({10{1'b0}}), .out(multiplexer_8_out), .sel(\同步清零_高电平有效 ));
  Pull_Resistor #(.pull(0)) pull_resistor_1 (.node(\同步清零_高电平有效 ));
  Register #(.width(5), .trigger("rising"), .Select("low")) register_1 (
    .D(multiplexer_1_out), .en(pull_resistor_2_node), .Q(X_prime), .clk(CLK));  // open: clr
  Register #(.width(5), .trigger("rising"), .Select("low")) register_2 (
    .D(multiplexer_2_out), .en(pull_resistor_2_node), .Q(Y_prime), .clk(CLK));  // open: clr
  Register #(.width(5), .trigger("rising"), .Select("low")) register_3 (
    .D(multiplexer_3_out), .en(pull_resistor_2_node), .Q(XY0_prime), .clk(CLK));  // open: clr
  Register #(.width(5), .trigger("rising"), .Select("low")) register_4 (
    .D(multiplexer_4_out), .en(pull_resistor_2_node), .Q(XY1_prime), .clk(CLK));  // open: clr
  Register #(.width(5), .trigger("rising"), .Select("low")) register_5 (
    .D(multiplexer_5_out), .en(pull_resistor_2_node), .Q(XY2_prime), .clk(CLK));  // open: clr
  Register #(.width(5), .trigger("rising"), .Select("low")) register_6 (
    .D(multiplexer_6_out), .en(pull_resistor_2_node), .Q(XY3_2), .clk(CLK));  // open: clr
  Register #(.width(5), .trigger("rising"), .Select("low")) register_7 (
    .D(multiplexer_7_out), .en(pull_resistor_2_node), .Q(XY4_2), .clk(CLK));  // open: clr
  Register #(.width(10), .trigger("rising"), .Select("low")) register_8 (
    .D(multiplexer_8_out), .en(pull_resistor_2_node), .Q(EDU), .clk(CLK));  // open: clr
  Pull_Resistor #(.pull(0)) pull_resistor_2 (.node(pull_resistor_2_node));
  not not_1 (pull_resistor_2_node, \使能端_低电平有效 );

  assign out_19 = EDU;

  // Notes on the sheet:
  //   使能端_低电平有效: pull=down
  //   同步清零_高电平有效: pull=down
  //   下拉电阻使得引脚可以悬空
  //   流水接口传输XY的目的是为了测试
endmodule

// FA
module \一位全加器FA封装1  (
  input  Cin,
  input  Xi,
  input  Yi,
  output Cout,
  output Si
);

  wire AND_2_out, AND_out, XOR_2_out;

  or OR (Cout, AND_out, AND_2_out);
  and AND (AND_out, Xi, Yi);
  and AND_2 (AND_2_out, Cin, XOR_2_out);
  xor XOR (Si, Cin, XOR_2_out);
  xor XOR_2 (XOR_2_out, Xi, Yi);

  // Notes on the sheet:
  //   Xi: pull=down
  //   Cin: pull=down
  //   Yi: pull=down
  //   Si = Xi ^ Yi ^ Cin
  //   Cout = Xi Yi + Cin (Xi ^ Yi)
endmodule

module \一位全加器FA封装2  (
  input  Cin,
  input  Xi,
  input  Yi,
  output Cout,
  output Si
);

  wire AND_2_out, AND_out, XOR_2_out;

  or OR (Cout, AND_out, AND_2_out);
  and AND (AND_out, Xi, Yi);
  and AND_2 (AND_2_out, Cin, XOR_2_out);
  xor XOR (Si, Cin, XOR_2_out);
  xor XOR_2 (XOR_2_out, Xi, Yi);

  // Notes on the sheet:
  //   Si = Xi ^ Yi ^ Cin
  //   Cout = Xi Yi + Cin (Xi ^ Yi)
endmodule

module \一位全加器FA封装3  (
  input  Cin,
  input  Xi,
  input  Yi,
  output Cout,
  output Si
);

  wire AND_2_out, AND_out, XOR_2_out;

  or OR (Cout, AND_out, AND_2_out);
  and AND (AND_out, Xi, Yi);
  and AND_2 (AND_2_out, Cin, XOR_2_out);
  xor XOR (Si, Cin, XOR_2_out);
  xor XOR_2 (XOR_2_out, Xi, Yi);

  // Notes on the sheet:
  //   Si = Xi ^ Yi ^ Cin
  //   Cout = Xi Yi + Cin (Xi ^ Yi)
endmodule

module \_8位串行加法器  (
  input  [7:0] X,
  input  [7:0] Y,
  input  Cin,
  output [7:0] S,
  output Cout,
  output Overflow
);

  wire \一位全加器fa封装1_2_cout , \一位全加器fa封装1_3_cout , \一位全加器fa封装1_4_cout , \一位全加器fa封装1_5_cout ,
       \一位全加器fa封装1_6_cout , \一位全加器fa封装1_7_cout , \一位全加器fa封装1_8_cout ;

  xor xor_1 (Overflow, Cout, \一位全加器fa封装1_2_cout );
  \一位全加器FA封装1  \u_一位全加器fa封装1_1  (.Cout(Cout), .Si(S[7]), .Cin(\一位全加器fa封装1_2_cout ), .Xi(X[7]), .Yi(Y[7]));
  \一位全加器FA封装1  \u_一位全加器fa封装1_2  (
    .Cout(\一位全加器fa封装1_2_cout ), .Si(S[6]), .Cin(\一位全加器fa封装1_3_cout ), .Xi(X[6]), .Yi(Y[6]));
  \一位全加器FA封装1  \u_一位全加器fa封装1_3  (
    .Cout(\一位全加器fa封装1_3_cout ), .Si(S[5]), .Cin(\一位全加器fa封装1_4_cout ), .Xi(X[5]), .Yi(Y[5]));
  \一位全加器FA封装1  \u_一位全加器fa封装1_4  (
    .Cout(\一位全加器fa封装1_4_cout ), .Si(S[4]), .Cin(\一位全加器fa封装1_5_cout ), .Xi(X[4]), .Yi(Y[4]));
  \一位全加器FA封装1  \u_一位全加器fa封装1_5  (
    .Cout(\一位全加器fa封装1_5_cout ), .Si(S[3]), .Cin(\一位全加器fa封装1_6_cout ), .Xi(X[3]), .Yi(Y[3]));
  \一位全加器FA封装1  \u_一位全加器fa封装1_6  (
    .Cout(\一位全加器fa封装1_6_cout ), .Si(S[2]), .Cin(\一位全加器fa封装1_7_cout ), .Xi(X[2]), .Yi(Y[2]));
  // Probe on X
  // Probe on Y
  // Probe on S
  \一位全加器FA封装1  \u_一位全加器fa封装1_7  (
    .Cout(\一位全加器fa封装1_7_cout ), .Si(S[1]), .Cin(\一位全加器fa封装1_8_cout ), .Xi(X[1]), .Yi(Y[1]));
  // Probe on X
  // Probe on Y
  // Probe on S
  \一位全加器FA封装1  \u_一位全加器fa封装1_8  (.Cout(\一位全加器fa封装1_8_cout ), .Si(S[0]), .Cin(Cin), .Xi(X[0]), .Yi(Y[0]));

  // Other names for the same wires on the sheet: OF = Overflow

  // Notes on the sheet:
  //   X: pull=down
  //   Cin: pull=down
  //   Y: pull=down
  //   输入引脚区
  //   符号位
  //   输出引脚区
  //   +
  //   =
  //   有符号加法
  //   +
  //   =
  //   无符号加法
endmodule

module \华莱士树  (
);

  wire undriven, undriven_2, undriven_3, undriven_4, undriven_5, undriven_6, undriven_7, undriven_8,
       undriven_9, undriven_10, undriven_11, undriven_12, undriven_13, undriven_14, undriven_15, undriven_16,
       undriven_17, undriven_18, undriven_19, undriven_20, undriven_21, undriven_22, undriven_23,
       undriven_24, undriven_25, undriven_26, undriven_27, undriven_28, undriven_29, undriven_30,
       undriven_31, undriven_32, undriven_33, undriven_34, undriven_35, undriven_36, undriven_37,
       undriven_38, undriven_39, undriven_40, undriven_41, undriven_42, undriven_43, undriven_44,
       undriven_45, undriven_46, undriven_47, undriven_48, undriven_49, undriven_50, undriven_51,
       undriven_52, undriven_53, undriven_54, undriven_55, undriven_56, undriven_57, undriven_58,
       undriven_59, undriven_60, undriven_61, undriven_62, undriven_63, undriven_64, undriven_65,
       undriven_66, undriven_67, undriven_68, undriven_69, undriven_70, undriven_71, undriven_72,
       undriven_73, undriven_74, undriven_75, undriven_76, undriven_77, undriven_78, undriven_79,
       undriven_80, undriven_81, undriven_82, undriven_83, undriven_84, undriven_85, undriven_86,
       undriven_87, undriven_88, undriven_89, undriven_90, undriven_91, undriven_92, undriven_93,
       undriven_94, undriven_95, undriven_96, undriven_97, undriven_98, undriven_99, undriven_100,
       undriven_101, undriven_102, undriven_103, undriven_104, undriven_105, undriven_106, undriven_107,
       undriven_108, undriven_109, undriven_110, undriven_111, undriven_112, undriven_113, undriven_114,
       undriven_115, undriven_116, undriven_117, undriven_118, undriven_119, undriven_120, undriven_121,
       undriven_122, undriven_123, undriven_124, undriven_125, undriven_126, undriven_127, undriven_128,
       undriven_130, \一位全加器fa封装2_1_cout , \一位全加器fa封装2_1_si , \一位全加器fa封装2_2_si , \一位全加器fa封装2_3_cout ,
       \一位全加器fa封装2_3_si , \一位全加器fa封装2_4_si , \一位全加器fa封装2_5_si , \一位全加器fa封装2_6_si , \一位全加器fa封装2_7_si ,
       \一位全加器fa封装2_8_si , \一位全加器fa封装2_9_cout , \一位全加器fa封装2_9_si , \一位全加器fa封装2_10_si , \一位全加器fa封装2_11_si ,
       \一位全加器fa封装2_12_cout , \一位全加器fa封装2_12_si , \一位全加器fa封装2_13_si , \一位全加器fa封装2_14_si ,
       \一位全加器fa封装2_15_cout , \一位全加器fa封装2_15_si , \一位全加器fa封装2_16_si , \一位全加器fa封装2_17_cout ,
       \一位全加器fa封装2_17_si , \一位全加器fa封装2_18_si , \一位全加器fa封装2_19_si , \一位全加器fa封装2_20_si , \一位全加器fa封装2_21_si ,
       \一位全加器fa封装2_22_si , \一位全加器fa封装2_23_cout , \一位全加器fa封装2_23_si , \一位全加器fa封装2_24_si ,
       \一位全加器fa封装2_25_cout , \一位全加器fa封装2_25_si , \一位全加器fa封装2_26_si , \一位全加器fa封装2_27_si , \一位全加器fa封装2_28_si ,
       \一位全加器fa封装2_29_cout , \一位全加器fa封装2_29_si , \一位全加器fa封装2_30_si , \一位全加器fa封装2_31_cout ,
       \一位全加器fa封装2_31_si , \一位全加器fa封装2_32_si , \一位全加器fa封装2_33_si , \一位全加器fa封装2_34_si , \一位全加器fa封装2_35_si ,
       \一位全加器fa封装2_36_si , \一位全加器fa封装2_37_cout , \一位全加器fa封装2_37_si , \一位全加器fa封装2_38_si , \一位全加器fa封装2_39_si ,
       \一位全加器fa封装2_40_cout , \一位全加器fa封装2_40_si , \一位全加器fa封装2_41_si , \一位全加器fa封装2_42_si ,
       \一位全加器fa封装2_43_cout , \一位全加器fa封装2_43_si , \一位全加器fa封装2_44_si , \一位全加器fa封装2_45_cout ,
       \一位全加器fa封装2_45_si , \一位全加器fa封装2_46_si , \一位全加器fa封装2_47_si , \一位全加器fa封装2_48_si , \一位全加器fa封装2_49_si ,
       \一位全加器fa封装2_50_si , \一位全加器fa封装2_51_cout , \一位全加器fa封装2_51_si , \一位全加器fa封装2_52_si ,
       \一位全加器fa封装2_53_cout , \一位全加器fa封装2_53_si , \一位全加器fa封装2_54_si , \一位全加器fa封装2_55_si , \一位全加器fa封装2_56_si ,
       \一位全加器fa封装2_57_cout , \一位全加器fa封装2_57_si , \一位全加器fa封装2_58_si , \一位全加器fa封装2_59_cout ,
       \一位全加器fa封装2_59_si , \一位全加器fa封装2_60_si , \一位全加器fa封装2_61_si , \一位全加器fa封装2_62_si , \一位全加器fa封装2_63_si ,
       \一位全加器fa封装2_64_si , \一位全加器fa封装2_65_cout , \一位全加器fa封装2_65_si , \一位全加器fa封装2_66_si , \一位全加器fa封装2_67_si ,
       \一位全加器fa封装2_68_cout , \一位全加器fa封装2_68_si , \一位全加器fa封装2_69_si , \一位全加器fa封装2_70_si ,
       \一位全加器fa封装2_71_cout , \一位全加器fa封装2_71_si , \一位全加器fa封装2_72_si , \一位全加器fa封装2_73_cout ,
       \一位全加器fa封装2_73_si , \一位全加器fa封装2_74_si , \一位全加器fa封装2_75_si , \一位全加器fa封装2_76_si , \一位全加器fa封装2_77_si ,
       \一位全加器fa封装2_78_si , \一位全加器fa封装2_79_cout , \一位全加器fa封装2_79_si , \一位全加器fa封装2_80_si ,
       \一位全加器fa封装2_81_cout , \一位全加器fa封装2_81_si , \一位全加器fa封装2_82_si , \一位全加器fa封装2_83_si , \一位全加器fa封装2_84_si ,
       \一位全加器fa封装2_85_cout , \一位全加器fa封装2_85_si , \一位全加器fa封装2_86_si , \一位全加器fa封装2_87_cout ,
       \一位全加器fa封装2_87_si , \一位全加器fa封装2_88_si , \一位全加器fa封装2_89_si , \一位全加器fa封装2_90_si , \一位全加器fa封装2_91_si ,
       \一位全加器fa封装2_92_si , \一位全加器fa封装2_93_cout , \一位全加器fa封装2_93_si , \一位全加器fa封装2_94_si ,
       \一位全加器fa封装2_95_cout , \一位全加器fa封装2_95_si , \一位全加器fa封装2_96_si , \一位全加器fa封装2_97_si , \一位全加器fa封装2_98_si ,
       \一位全加器fa封装2_99_cout , \一位全加器fa封装2_99_si , \一位全加器fa封装2_100_si , \一位全加器fa封装2_101_cout ,
       \一位全加器fa封装2_101_si , \一位全加器fa封装2_102_si , \一位全加器fa封装2_103_si , \一位全加器fa封装2_104_si ,
       \一位全加器fa封装2_105_si , \一位全加器fa封装2_106_si , \一位全加器fa封装2_107_cout , \一位全加器fa封装2_107_si ,
       \一位全加器fa封装2_108_si , \一位全加器fa封装2_109_cout , \一位全加器fa封装2_109_si , \一位全加器fa封装2_110_si ,
       \一位全加器fa封装2_111_si , \一位全加器fa封装2_112_si ;
  wire [1:0] undriven_131, \一位全加器fa封装2_4_cout , \一位全加器fa封装2_10_cout , \一位全加器fa封装2_16_cout ,
       \一位全加器fa封装2_22_cout , \一位全加器fa封装2_32_cout , \一位全加器fa封装2_38_cout , \一位全加器fa封装2_44_cout ,
       \一位全加器fa封装2_50_cout , \一位全加器fa封装2_60_cout , \一位全加器fa封装2_66_cout , \一位全加器fa封装2_72_cout ,
       \一位全加器fa封装2_78_cout , \一位全加器fa封装2_88_cout , \一位全加器fa封装2_94_cout , \一位全加器fa封装2_100_cout ,
       \一位全加器fa封装2_106_cout ;
  wire [2:0] undriven_129, \一位全加器fa封装2_6_cout , \一位全加器fa封装2_14_cout , \一位全加器fa封装2_21_cout ,
       \一位全加器fa封装2_27_cout , \一位全加器fa封装2_34_cout , \一位全加器fa封装2_42_cout , \一位全加器fa封装2_49_cout ,
       \一位全加器fa封装2_55_cout , \一位全加器fa封装2_63_cout , \一位全加器fa封装2_70_cout , \一位全加器fa封装2_77_cout ,
       \一位全加器fa封装2_84_cout , \一位全加器fa封装2_91_cout , \一位全加器fa封装2_98_cout , \一位全加器fa封装2_105_cout ,
       \一位全加器fa封装2_111_cout ;

  shape shape_1 ();
  \一位全加器FA封装2  \u_一位全加器fa封装2_1  (
    .Cout(\一位全加器fa封装2_1_cout ), .Si(\一位全加器fa封装2_1_si ), .Cin(\一位全加器fa封装2_6_si ), .Xi(\一位全加器fa封装2_2_si ),
    .Yi(\一位全加器fa封装2_7_si ));
  \一位全加器FA封装2  \u_一位全加器fa封装2_2  (
    .Cout(\一位全加器fa封装2_6_cout [2]), .Si(\一位全加器fa封装2_2_si ), .Cin(undriven_3), .Xi(undriven), .Yi(undriven_2));
  \一位全加器FA封装2  \u_一位全加器fa封装2_3  (
    .Cout(\一位全加器fa封装2_3_cout ), .Si(\一位全加器fa封装2_3_si ), .Cin(\一位全加器fa封装2_10_cout [0]),
    .Xi(\一位全加器fa封装2_4_si ), .Yi(\一位全加器fa封装2_10_cout [1]));
  \一位全加器FA封装2  \u_一位全加器fa封装2_4  (
    .Cout(\一位全加器fa封装2_4_cout [0]), .Si(\一位全加器fa封装2_4_si ), .Cin(\一位全加器fa封装2_12_cout ),
    .Xi(\一位全加器fa封装2_1_si ), .Yi(\一位全加器fa封装2_5_si ));
  \一位全加器FA封装2  \u_一位全加器fa封装2_5  (
    .Cout(\一位全加器fa封装2_4_cout [1]), .Si(\一位全加器fa封装2_5_si ), .Cin(\一位全加器fa封装2_14_cout [0]),
    .Xi(\一位全加器fa封装2_14_cout [2]), .Yi(\一位全加器fa封装2_14_cout [1]));
  \一位全加器FA封装2  \u_一位全加器fa封装2_6  (
    .Cout(\一位全加器fa封装2_6_cout [0]), .Si(\一位全加器fa封装2_6_si ), .Cin(1'b0), .Xi(undriven_7), .Yi(undriven_8));
  \一位全加器FA封装2  \u_一位全加器fa封装2_7  (
    .Cout(\一位全加器fa封装2_6_cout [1]), .Si(\一位全加器fa封装2_7_si ), .Cin(undriven_6), .Xi(undriven_4), .Yi(undriven_5));
  \一位全加器FA封装2  \u_一位全加器fa封装2_8  (
    .Cout(\一位全加器fa封装2_14_cout [2]), .Si(\一位全加器fa封装2_8_si ), .Cin(undriven_11), .Xi(undriven_9),
    .Yi(undriven_10));
  \一位全加器FA封装2  \u_一位全加器fa封装2_9  (
    .Cout(\一位全加器fa封装2_9_cout ), .Si(\一位全加器fa封装2_9_si ), .Cin(\一位全加器fa封装2_16_cout [0]),
    .Xi(\一位全加器fa封装2_10_si ), .Yi(\一位全加器fa封装2_16_cout [1]));
  \一位全加器FA封装2  \u_一位全加器fa封装2_10  (
    .Cout(\一位全加器fa封装2_10_cout [0]), .Si(\一位全加器fa封装2_10_si ), .Cin(\一位全加器fa封装2_17_cout ),
    .Xi(\一位全加器fa封装2_12_si ), .Yi(\一位全加器fa封装2_11_si ));
  \一位全加器FA封装2  \u_一位全加器fa封装2_11  (
    .Cout(\一位全加器fa封装2_10_cout [1]), .Si(\一位全加器fa封装2_11_si ), .Cin(\一位全加器fa封装2_21_cout [0]),
    .Xi(\一位全加器fa封装2_21_cout [2]), .Yi(\一位全加器fa封装2_21_cout [1]));
  \一位全加器FA封装2  \u_一位全加器fa封装2_12  (
    .Cout(\一位全加器fa封装2_12_cout ), .Si(\一位全加器fa封装2_12_si ), .Cin(\一位全加器fa封装2_14_si ), .Xi(\一位全加器fa封装2_8_si ),
    .Yi(\一位全加器fa封装2_13_si ));
  \一位全加器FA封装2  \u_一位全加器fa封装2_13  (
    .Cout(\一位全加器fa封装2_14_cout [1]), .Si(\一位全加器fa封装2_13_si ), .Cin(undriven_14), .Xi(undriven_12),
    .Yi(undriven_13));
  shape shape_2 ();
  \一位全加器FA封装2  \u_一位全加器fa封装2_14  (
    .Cout(\一位全加器fa封装2_14_cout [0]), .Si(\一位全加器fa封装2_14_si ), .Cin(1'b0), .Xi(undriven_15), .Yi(undriven_16));
  \一位全加器FA封装2  \u_一位全加器fa封装2_15  (
    .Cout(\一位全加器fa封装2_15_cout ), .Si(\一位全加器fa封装2_15_si ), .Cin(\一位全加器fa封装2_22_cout [0]),
    .Xi(\一位全加器fa封装2_16_si ), .Yi(\一位全加器fa封装2_22_cout [1]));
  \一位全加器FA封装2  \u_一位全加器fa封装2_16  (
    .Cout(\一位全加器fa封装2_16_cout [0]), .Si(\一位全加器fa封装2_16_si ), .Cin(\一位全加器fa封装2_23_cout ),
    .Xi(\一位全加器fa封装2_17_si ), .Yi(\一位全加器fa封装2_20_si ));
  \一位全加器FA封装2  \u_一位全加器fa封装2_17  (
    .Cout(\一位全加器fa封装2_17_cout ), .Si(\一位全加器fa封装2_17_si ), .Cin(\一位全加器fa封装2_21_si ), .Xi(\一位全加器fa封装2_18_si ),
    .Yi(\一位全加器fa封装2_19_si ));
  \一位全加器FA封装2  \u_一位全加器fa封装2_18  (
    .Cout(\一位全加器fa封装2_21_cout [2]), .Si(\一位全加器fa封装2_18_si ), .Cin(undriven_19), .Xi(undriven_17),
    .Yi(undriven_18));
  \一位全加器FA封装2  \u_一位全加器fa封装2_19  (
    .Cout(\一位全加器fa封装2_21_cout [1]), .Si(\一位全加器fa封装2_19_si ), .Cin(undriven_22), .Xi(undriven_20),
    .Yi(undriven_21));
  \一位全加器FA封装2  \u_一位全加器fa封装2_20  (
    .Cout(\一位全加器fa封装2_16_cout [1]), .Si(\一位全加器fa封装2_20_si ), .Cin(\一位全加器fa封装2_27_cout [0]),
    .Xi(\一位全加器fa封装2_27_cout [2]), .Yi(\一位全加器fa封装2_27_cout [1]));
  \一位全加器FA封装2  \u_一位全加器fa封装2_21  (
    .Cout(\一位全加器fa封装2_21_cout [0]), .Si(\一位全加器fa封装2_21_si ), .Cin(1'b0), .Xi(undriven_23), .Yi(undriven_24));
  \一位全加器FA封装2  \u_一位全加器fa封装2_22  (
    .Cout(\一位全加器fa封装2_22_cout [0]), .Si(\一位全加器fa封装2_22_si ), .Cin(\一位全加器fa封装2_29_cout ),
    .Xi(\一位全加器fa封装2_23_si ), .Yi(\一位全加器fa封装2_26_si ));
  \一位全加器FA封装2  \u_一位全加器fa封装2_23  (
    .Cout(\一位全加器fa封装2_23_cout ), .Si(\一位全加器fa封装2_23_si ), .Cin(\一位全加器fa封装2_27_si ), .Xi(\一位全加器fa封装2_24_si ),
    .Yi(\一位全加器fa封装2_28_si ));
  \一位全加器FA封装2  \u_一位全加器fa封装2_24  (
    .Cout(\一位全加器fa封装2_27_cout [2]), .Si(\一位全加器fa封装2_24_si ), .Cin(undriven_27), .Xi(undriven_25),
    .Yi(undriven_26));
  shape shape_3 ();
  \一位全加器FA封装2  \u_一位全加器fa封装2_25  (
    .Cout(\一位全加器fa封装2_25_cout ), .Si(\一位全加器fa封装2_25_si ), .Cin(\一位全加器fa封装2_32_cout [0]),
    .Xi(\一位全加器fa封装2_22_si ), .Yi(\一位全加器fa封装2_32_cout [1]));
  \一位全加器FA封装2  \u_一位全加器fa封装2_26  (
    .Cout(\一位全加器fa封装2_22_cout [1]), .Si(\一位全加器fa封装2_26_si ), .Cin(\一位全加器fa封装2_34_cout [0]),
    .Xi(\一位全加器fa封装2_34_cout [2]), .Yi(\一位全加器fa封装2_34_cout [1]));
  \一位全加器FA封装2  \u_一位全加器fa封装2_27  (
    .Cout(\一位全加器fa封装2_27_cout [0]), .Si(\一位全加器fa封装2_27_si ), .Cin(1'b0), .Xi(undriven_31), .Yi(undriven_32));
  \一位全加器FA封装2  \u_一位全加器fa封装2_28  (
    .Cout(\一位全加器fa封装2_27_cout [1]), .Si(\一位全加器fa封装2_28_si ), .Cin(undriven_30), .Xi(undriven_28),
    .Yi(undriven_29));
  \一位全加器FA封装2  \u_一位全加器fa封装2_29  (
    .Cout(\一位全加器fa封装2_29_cout ), .Si(\一位全加器fa封装2_29_si ), .Cin(\一位全加器fa封装2_34_si ), .Xi(\一位全加器fa封装2_30_si ),
    .Yi(\一位全加器fa封装2_35_si ));
  \一位全加器FA封装2  \u_一位全加器fa封装2_30  (
    .Cout(\一位全加器fa封装2_34_cout [2]), .Si(\一位全加器fa封装2_30_si ), .Cin(undriven_35), .Xi(undriven_33),
    .Yi(undriven_34));
  \一位全加器FA封装2  \u_一位全加器fa封装2_31  (
    .Cout(\一位全加器fa封装2_31_cout ), .Si(\一位全加器fa封装2_31_si ), .Cin(\一位全加器fa封装2_38_cout [0]),
    .Xi(\一位全加器fa封装2_32_si ), .Yi(\一位全加器fa封装2_38_cout [1]));
  \一位全加器FA封装2  \u_一位全加器fa封装2_32  (
    .Cout(\一位全加器fa封装2_32_cout [0]), .Si(\一位全加器fa封装2_32_si ), .Cin(\一位全加器fa封装2_40_cout ),
    .Xi(\一位全加器fa封装2_29_si ), .Yi(\一位全加器fa封装2_33_si ));
  \一位全加器FA封装2  \u_一位全加器fa封装2_33  (
    .Cout(\一位全加器fa封装2_32_cout [1]), .Si(\一位全加器fa封装2_33_si ), .Cin(\一位全加器fa封装2_42_cout [0]),
    .Xi(\一位全加器fa封装2_42_cout [2]), .Yi(\一位全加器fa封装2_42_cout [1]));
  \一位全加器FA封装2  \u_一位全加器fa封装2_34  (
    .Cout(\一位全加器fa封装2_34_cout [0]), .Si(\一位全加器fa封装2_34_si ), .Cin(1'b0), .Xi(undriven_39), .Yi(undriven_40));
  \一位全加器FA封装2  \u_一位全加器fa封装2_35  (
    .Cout(\一位全加器fa封装2_34_cout [1]), .Si(\一位全加器fa封装2_35_si ), .Cin(undriven_38), .Xi(undriven_36),
    .Yi(undriven_37));
  \一位全加器FA封装2  \u_一位全加器fa封装2_36  (
    .Cout(\一位全加器fa封装2_42_cout [2]), .Si(\一位全加器fa封装2_36_si ), .Cin(undriven_43), .Xi(undriven_41),
    .Yi(undriven_42));
  \一位全加器FA封装2  \u_一位全加器fa封装2_37  (
    .Cout(\一位全加器fa封装2_37_cout ), .Si(\一位全加器fa封装2_37_si ), .Cin(\一位全加器fa封装2_44_cout [0]),
    .Xi(\一位全加器fa封装2_38_si ), .Yi(\一位全加器fa封装2_44_cout [1]));
  \一位全加器FA封装2  \u_一位全加器fa封装2_38  (
    .Cout(\一位全加器fa封装2_38_cout [0]), .Si(\一位全加器fa封装2_38_si ), .Cin(\一位全加器fa封装2_45_cout ),
    .Xi(\一位全加器fa封装2_40_si ), .Yi(\一位全加器fa封装2_39_si ));
  \一位全加器FA封装2  \u_一位全加器fa封装2_39  (
    .Cout(\一位全加器fa封装2_38_cout [1]), .Si(\一位全加器fa封装2_39_si ), .Cin(\一位全加器fa封装2_49_cout [0]),
    .Xi(\一位全加器fa封装2_49_cout [2]), .Yi(\一位全加器fa封装2_49_cout [1]));
  \一位全加器FA封装2  \u_一位全加器fa封装2_40  (
    .Cout(\一位全加器fa封装2_40_cout ), .Si(\一位全加器fa封装2_40_si ), .Cin(\一位全加器fa封装2_42_si ), .Xi(\一位全加器fa封装2_36_si ),
    .Yi(\一位全加器fa封装2_41_si ));
  \一位全加器FA封装2  \u_一位全加器fa封装2_41  (
    .Cout(\一位全加器fa封装2_42_cout [1]), .Si(\一位全加器fa封装2_41_si ), .Cin(undriven_46), .Xi(undriven_44),
    .Yi(undriven_45));
  shape shape_4 ();
  \一位全加器FA封装2  \u_一位全加器fa封装2_42  (
    .Cout(\一位全加器fa封装2_42_cout [0]), .Si(\一位全加器fa封装2_42_si ), .Cin(1'b0), .Xi(undriven_47), .Yi(undriven_48));
  \一位全加器FA封装2  \u_一位全加器fa封装2_43  (
    .Cout(\一位全加器fa封装2_43_cout ), .Si(\一位全加器fa封装2_43_si ), .Cin(\一位全加器fa封装2_50_cout [0]),
    .Xi(\一位全加器fa封装2_44_si ), .Yi(\一位全加器fa封装2_50_cout [1]));
  \一位全加器FA封装2  \u_一位全加器fa封装2_44  (
    .Cout(\一位全加器fa封装2_44_cout [0]), .Si(\一位全加器fa封装2_44_si ), .Cin(\一位全加器fa封装2_51_cout ),
    .Xi(\一位全加器fa封装2_45_si ), .Yi(\一位全加器fa封装2_48_si ));
  \一位全加器FA封装2  \u_一位全加器fa封装2_45  (
    .Cout(\一位全加器fa封装2_45_cout ), .Si(\一位全加器fa封装2_45_si ), .Cin(\一位全加器fa封装2_49_si ), .Xi(\一位全加器fa封装2_46_si ),
    .Yi(\一位全加器fa封装2_47_si ));
  \一位全加器FA封装2  \u_一位全加器fa封装2_46  (
    .Cout(\一位全加器fa封装2_49_cout [2]), .Si(\一位全加器fa封装2_46_si ), .Cin(undriven_51), .Xi(undriven_49),
    .Yi(undriven_50));
  \一位全加器FA封装2  \u_一位全加器fa封装2_47  (
    .Cout(\一位全加器fa封装2_49_cout [1]), .Si(\一位全加器fa封装2_47_si ), .Cin(undriven_54), .Xi(undriven_52),
    .Yi(undriven_53));
  \一位全加器FA封装2  \u_一位全加器fa封装2_48  (
    .Cout(\一位全加器fa封装2_44_cout [1]), .Si(\一位全加器fa封装2_48_si ), .Cin(\一位全加器fa封装2_55_cout [0]),
    .Xi(\一位全加器fa封装2_55_cout [2]), .Yi(\一位全加器fa封装2_55_cout [1]));
  \一位全加器FA封装2  \u_一位全加器fa封装2_49  (
    .Cout(\一位全加器fa封装2_49_cout [0]), .Si(\一位全加器fa封装2_49_si ), .Cin(1'b0), .Xi(undriven_55), .Yi(undriven_56));
  \一位全加器FA封装2  \u_一位全加器fa封装2_50  (
    .Cout(\一位全加器fa封装2_50_cout [0]), .Si(\一位全加器fa封装2_50_si ), .Cin(\一位全加器fa封装2_57_cout ),
    .Xi(\一位全加器fa封装2_51_si ), .Yi(\一位全加器fa封装2_54_si ));
  \一位全加器FA封装2  \u_一位全加器fa封装2_51  (
    .Cout(\一位全加器fa封装2_51_cout ), .Si(\一位全加器fa封装2_51_si ), .Cin(\一位全加器fa封装2_55_si ), .Xi(\一位全加器fa封装2_52_si ),
    .Yi(\一位全加器fa封装2_56_si ));
  \一位全加器FA封装2  \u_一位全加器fa封装2_52  (
    .Cout(\一位全加器fa封装2_55_cout [2]), .Si(\一位全加器fa封装2_52_si ), .Cin(undriven_59), .Xi(undriven_57),
    .Yi(undriven_58));
  shape shape_5 ();
  \一位全加器FA封装2  \u_一位全加器fa封装2_53  (
    .Cout(\一位全加器fa封装2_53_cout ), .Si(\一位全加器fa封装2_53_si ), .Cin(\一位全加器fa封装2_60_cout [0]),
    .Xi(\一位全加器fa封装2_50_si ), .Yi(\一位全加器fa封装2_60_cout [1]));
  \一位全加器FA封装2  \u_一位全加器fa封装2_54  (
    .Cout(\一位全加器fa封装2_50_cout [1]), .Si(\一位全加器fa封装2_54_si ), .Cin(\一位全加器fa封装2_63_cout [0]),
    .Xi(\一位全加器fa封装2_63_cout [2]), .Yi(\一位全加器fa封装2_63_cout [1]));
  \一位全加器FA封装2  \u_一位全加器fa封装2_55  (
    .Cout(\一位全加器fa封装2_55_cout [0]), .Si(\一位全加器fa封装2_55_si ), .Cin(1'b0), .Xi(undriven_63), .Yi(undriven_64));
  \一位全加器FA封装2  \u_一位全加器fa封装2_56  (
    .Cout(\一位全加器fa封装2_55_cout [1]), .Si(\一位全加器fa封装2_56_si ), .Cin(undriven_62), .Xi(undriven_60),
    .Yi(undriven_61));
  \一位全加器FA封装2  \u_一位全加器fa封装2_57  (
    .Cout(\一位全加器fa封装2_57_cout ), .Si(\一位全加器fa封装2_57_si ), .Cin(\一位全加器fa封装2_63_si ), .Xi(\一位全加器fa封装2_58_si ),
    .Yi(\一位全加器fa封装2_62_si ));
  \一位全加器FA封装2  \u_一位全加器fa封装2_58  (
    .Cout(\一位全加器fa封装2_63_cout [2]), .Si(\一位全加器fa封装2_58_si ), .Cin(undriven_67), .Xi(undriven_65),
    .Yi(undriven_66));
  \一位全加器FA封装2  \u_一位全加器fa封装2_59  (
    .Cout(\一位全加器fa封装2_59_cout ), .Si(\一位全加器fa封装2_59_si ), .Cin(\一位全加器fa封装2_66_cout [0]),
    .Xi(\一位全加器fa封装2_60_si ), .Yi(\一位全加器fa封装2_66_cout [1]));
  \一位全加器FA封装2  \u_一位全加器fa封装2_60  (
    .Cout(\一位全加器fa封装2_60_cout [0]), .Si(\一位全加器fa封装2_60_si ), .Cin(\一位全加器fa封装2_68_cout ),
    .Xi(\一位全加器fa封装2_57_si ), .Yi(\一位全加器fa封装2_61_si ));
  \一位全加器FA封装2  \u_一位全加器fa封装2_61  (
    .Cout(\一位全加器fa封装2_60_cout [1]), .Si(\一位全加器fa封装2_61_si ), .Cin(\一位全加器fa封装2_70_cout [0]),
    .Xi(\一位全加器fa封装2_70_cout [2]), .Yi(\一位全加器fa封装2_70_cout [1]));
  \一位全加器FA封装2  \u_一位全加器fa封装2_62  (
    .Cout(\一位全加器fa封装2_63_cout [1]), .Si(\一位全加器fa封装2_62_si ), .Cin(undriven_70), .Xi(undriven_68),
    .Yi(undriven_69));
  \一位全加器FA封装2  \u_一位全加器fa封装2_63  (
    .Cout(\一位全加器fa封装2_63_cout [0]), .Si(\一位全加器fa封装2_63_si ), .Cin(1'b0), .Xi(undriven_71), .Yi(undriven_72));
  \一位全加器FA封装2  \u_一位全加器fa封装2_64  (
    .Cout(\一位全加器fa封装2_70_cout [2]), .Si(\一位全加器fa封装2_64_si ), .Cin(undriven_75), .Xi(undriven_73),
    .Yi(undriven_74));
  \一位全加器FA封装2  \u_一位全加器fa封装2_65  (
    .Cout(\一位全加器fa封装2_65_cout ), .Si(\一位全加器fa封装2_65_si ), .Cin(\一位全加器fa封装2_72_cout [0]),
    .Xi(\一位全加器fa封装2_66_si ), .Yi(\一位全加器fa封装2_72_cout [1]));
  \一位全加器FA封装2  \u_一位全加器fa封装2_66  (
    .Cout(\一位全加器fa封装2_66_cout [0]), .Si(\一位全加器fa封装2_66_si ), .Cin(\一位全加器fa封装2_73_cout ),
    .Xi(\一位全加器fa封装2_68_si ), .Yi(\一位全加器fa封装2_67_si ));
  \一位全加器FA封装2  \u_一位全加器fa封装2_67  (
    .Cout(\一位全加器fa封装2_66_cout [1]), .Si(\一位全加器fa封装2_67_si ), .Cin(\一位全加器fa封装2_77_cout [0]),
    .Xi(\一位全加器fa封装2_77_cout [2]), .Yi(\一位全加器fa封装2_77_cout [1]));
  \一位全加器FA封装2  \u_一位全加器fa封装2_68  (
    .Cout(\一位全加器fa封装2_68_cout ), .Si(\一位全加器fa封装2_68_si ), .Cin(\一位全加器fa封装2_70_si ), .Xi(\一位全加器fa封装2_64_si ),
    .Yi(\一位全加器fa封装2_69_si ));
  \一位全加器FA封装2  \u_一位全加器fa封装2_69  (
    .Cout(\一位全加器fa封装2_70_cout [1]), .Si(\一位全加器fa封装2_69_si ), .Cin(undriven_78), .Xi(undriven_76),
    .Yi(undriven_77));
  shape shape_6 ();
  \一位全加器FA封装2  \u_一位全加器fa封装2_70  (
    .Cout(\一位全加器fa封装2_70_cout [0]), .Si(\一位全加器fa封装2_70_si ), .Cin(1'b0), .Xi(undriven_79), .Yi(undriven_80));
  \一位全加器FA封装2  \u_一位全加器fa封装2_71  (
    .Cout(\一位全加器fa封装2_71_cout ), .Si(\一位全加器fa封装2_71_si ), .Cin(\一位全加器fa封装2_78_cout [0]),
    .Xi(\一位全加器fa封装2_72_si ), .Yi(\一位全加器fa封装2_78_cout [1]));
  \一位全加器FA封装2  \u_一位全加器fa封装2_72  (
    .Cout(\一位全加器fa封装2_72_cout [0]), .Si(\一位全加器fa封装2_72_si ), .Cin(\一位全加器fa封装2_79_cout ),
    .Xi(\一位全加器fa封装2_73_si ), .Yi(\一位全加器fa封装2_76_si ));
  \一位全加器FA封装2  \u_一位全加器fa封装2_73  (
    .Cout(\一位全加器fa封装2_73_cout ), .Si(\一位全加器fa封装2_73_si ), .Cin(\一位全加器fa封装2_77_si ), .Xi(\一位全加器fa封装2_75_si ),
    .Yi(\一位全加器fa封装2_74_si ));
  \一位全加器FA封装2  \u_一位全加器fa封装2_74  (
    .Cout(\一位全加器fa封装2_77_cout [1]), .Si(\一位全加器fa封装2_74_si ), .Cin(undriven_86), .Xi(undriven_84),
    .Yi(undriven_85));
  \一位全加器FA封装2  \u_一位全加器fa封装2_75  (
    .Cout(\一位全加器fa封装2_77_cout [2]), .Si(\一位全加器fa封装2_75_si ), .Cin(undriven_83), .Xi(undriven_81),
    .Yi(undriven_82));
  \一位全加器FA封装2  \u_一位全加器fa封装2_76  (
    .Cout(\一位全加器fa封装2_72_cout [1]), .Si(\一位全加器fa封装2_76_si ), .Cin(\一位全加器fa封装2_84_cout [0]),
    .Xi(\一位全加器fa封装2_84_cout [2]), .Yi(\一位全加器fa封装2_84_cout [1]));
  \一位全加器FA封装2  \u_一位全加器fa封装2_77  (
    .Cout(\一位全加器fa封装2_77_cout [0]), .Si(\一位全加器fa封装2_77_si ), .Cin(1'b0), .Xi(undriven_87), .Yi(undriven_88));
  \一位全加器FA封装2  \u_一位全加器fa封装2_78  (
    .Cout(\一位全加器fa封装2_78_cout [0]), .Si(\一位全加器fa封装2_78_si ), .Cin(\一位全加器fa封装2_85_cout ),
    .Xi(\一位全加器fa封装2_79_si ), .Yi(\一位全加器fa封装2_82_si ));
  \一位全加器FA封装2  \u_一位全加器fa封装2_79  (
    .Cout(\一位全加器fa封装2_79_cout ), .Si(\一位全加器fa封装2_79_si ), .Cin(\一位全加器fa封装2_84_si ), .Xi(\一位全加器fa封装2_80_si ),
    .Yi(\一位全加器fa封装2_83_si ));
  \一位全加器FA封装2  \u_一位全加器fa封装2_80  (
    .Cout(\一位全加器fa封装2_84_cout [2]), .Si(\一位全加器fa封装2_80_si ), .Cin(undriven_91), .Xi(undriven_89),
    .Yi(undriven_90));
  shape shape_7 ();
  \一位全加器FA封装2  \u_一位全加器fa封装2_81  (
    .Cout(\一位全加器fa封装2_81_cout ), .Si(\一位全加器fa封装2_81_si ), .Cin(\一位全加器fa封装2_88_cout [0]),
    .Xi(\一位全加器fa封装2_78_si ), .Yi(\一位全加器fa封装2_88_cout [1]));
  \一位全加器FA封装2  \u_一位全加器fa封装2_82  (
    .Cout(\一位全加器fa封装2_78_cout [1]), .Si(\一位全加器fa封装2_82_si ), .Cin(\一位全加器fa封装2_91_cout [0]),
    .Xi(\一位全加器fa封装2_91_cout [2]), .Yi(\一位全加器fa封装2_91_cout [1]));
  \一位全加器FA封装2  \u_一位全加器fa封装2_83  (
    .Cout(\一位全加器fa封装2_84_cout [1]), .Si(\一位全加器fa封装2_83_si ), .Cin(undriven_94), .Xi(undriven_92),
    .Yi(undriven_93));
  \一位全加器FA封装2  \u_一位全加器fa封装2_84  (
    .Cout(\一位全加器fa封装2_84_cout [0]), .Si(\一位全加器fa封装2_84_si ), .Cin(1'b0), .Xi(undriven_95), .Yi(undriven_96));
  \一位全加器FA封装2  \u_一位全加器fa封装2_85  (
    .Cout(\一位全加器fa封装2_85_cout ), .Si(\一位全加器fa封装2_85_si ), .Cin(\一位全加器fa封装2_91_si ), .Xi(\一位全加器fa封装2_86_si ),
    .Yi(\一位全加器fa封装2_90_si ));
  \一位全加器FA封装2  \u_一位全加器fa封装2_86  (
    .Cout(\一位全加器fa封装2_91_cout [2]), .Si(\一位全加器fa封装2_86_si ), .Cin(undriven_99), .Xi(undriven_97),
    .Yi(undriven_98));
  \一位全加器FA封装2  \u_一位全加器fa封装2_87  (
    .Cout(\一位全加器fa封装2_87_cout ), .Si(\一位全加器fa封装2_87_si ), .Cin(\一位全加器fa封装2_94_cout [0]),
    .Xi(\一位全加器fa封装2_88_si ), .Yi(\一位全加器fa封装2_94_cout [1]));
  \一位全加器FA封装2  \u_一位全加器fa封装2_88  (
    .Cout(\一位全加器fa封装2_88_cout [0]), .Si(\一位全加器fa封装2_88_si ), .Cin(\一位全加器fa封装2_95_cout ),
    .Xi(\一位全加器fa封装2_85_si ), .Yi(\一位全加器fa封装2_89_si ));
  \一位全加器FA封装2  \u_一位全加器fa封装2_89  (
    .Cout(\一位全加器fa封装2_88_cout [1]), .Si(\一位全加器fa封装2_89_si ), .Cin(\一位全加器fa封装2_98_cout [0]),
    .Xi(\一位全加器fa封装2_98_cout [2]), .Yi(\一位全加器fa封装2_98_cout [1]));
  \一位全加器FA封装2  \u_一位全加器fa封装2_90  (
    .Cout(\一位全加器fa封装2_91_cout [1]), .Si(\一位全加器fa封装2_90_si ), .Cin(undriven_102), .Xi(undriven_100),
    .Yi(undriven_101));
  \一位全加器FA封装2  \u_一位全加器fa封装2_91  (
    .Cout(\一位全加器fa封装2_91_cout [0]), .Si(\一位全加器fa封装2_91_si ), .Cin(1'b0), .Xi(undriven_103), .Yi(undriven_104));
  \一位全加器FA封装2  \u_一位全加器fa封装2_92  (
    .Cout(\一位全加器fa封装2_98_cout [2]), .Si(\一位全加器fa封装2_92_si ), .Cin(undriven_107), .Xi(undriven_105),
    .Yi(undriven_106));
  \一位全加器FA封装2  \u_一位全加器fa封装2_93  (
    .Cout(\一位全加器fa封装2_93_cout ), .Si(\一位全加器fa封装2_93_si ), .Cin(\一位全加器fa封装2_100_cout [0]),
    .Xi(\一位全加器fa封装2_94_si ), .Yi(\一位全加器fa封装2_100_cout [1]));
  \一位全加器FA封装2  \u_一位全加器fa封装2_94  (
    .Cout(\一位全加器fa封装2_94_cout [0]), .Si(\一位全加器fa封装2_94_si ), .Cin(\一位全加器fa封装2_101_cout ),
    .Xi(\一位全加器fa封装2_95_si ), .Yi(\一位全加器fa封装2_96_si ));
  \一位全加器FA封装2  \u_一位全加器fa封装2_95  (
    .Cout(\一位全加器fa封装2_95_cout ), .Si(\一位全加器fa封装2_95_si ), .Cin(\一位全加器fa封装2_98_si ), .Xi(\一位全加器fa封装2_92_si ),
    .Yi(\一位全加器fa封装2_97_si ));
  \一位全加器FA封装2  \u_一位全加器fa封装2_96  (
    .Cout(\一位全加器fa封装2_94_cout [1]), .Si(\一位全加器fa封装2_96_si ), .Cin(\一位全加器fa封装2_105_cout [0]),
    .Xi(\一位全加器fa封装2_105_cout [2]), .Yi(\一位全加器fa封装2_105_cout [1]));
  \一位全加器FA封装2  \u_一位全加器fa封装2_97  (
    .Cout(\一位全加器fa封装2_98_cout [1]), .Si(\一位全加器fa封装2_97_si ), .Cin(undriven_110), .Xi(undriven_108),
    .Yi(undriven_109));
  shape shape_8 ();
  \一位全加器FA封装2  \u_一位全加器fa封装2_98  (
    .Cout(\一位全加器fa封装2_98_cout [0]), .Si(\一位全加器fa封装2_98_si ), .Cin(1'b0), .Xi(undriven_111), .Yi(undriven_112));
  \一位全加器FA封装2  \u_一位全加器fa封装2_99  (
    .Cout(\一位全加器fa封装2_99_cout ), .Si(\一位全加器fa封装2_99_si ), .Cin(\一位全加器fa封装2_106_cout [0]),
    .Xi(\一位全加器fa封装2_100_si ), .Yi(\一位全加器fa封装2_106_cout [1]));
  \一位全加器FA封装2  \u_一位全加器fa封装2_100  (
    .Cout(\一位全加器fa封装2_100_cout [0]), .Si(\一位全加器fa封装2_100_si ), .Cin(\一位全加器fa封装2_107_cout ),
    .Xi(\一位全加器fa封装2_101_si ), .Yi(\一位全加器fa封装2_104_si ));
  \一位全加器FA封装2  \u_一位全加器fa封装2_101  (
    .Cout(\一位全加器fa封装2_101_cout ), .Si(\一位全加器fa封装2_101_si ), .Cin(\一位全加器fa封装2_105_si ),
    .Xi(\一位全加器fa封装2_102_si ), .Yi(\一位全加器fa封装2_103_si ));
  \一位全加器FA封装2  \u_一位全加器fa封装2_102  (
    .Cout(\一位全加器fa封装2_105_cout [2]), .Si(\一位全加器fa封装2_102_si ), .Cin(undriven_115), .Xi(undriven_113),
    .Yi(undriven_114));
  \一位全加器FA封装2  \u_一位全加器fa封装2_103  (
    .Cout(\一位全加器fa封装2_105_cout [1]), .Si(\一位全加器fa封装2_103_si ), .Cin(undriven_118), .Xi(undriven_116),
    .Yi(undriven_117));
  \一位全加器FA封装2  \u_一位全加器fa封装2_104  (
    .Cout(\一位全加器fa封装2_100_cout [1]), .Si(\一位全加器fa封装2_104_si ), .Cin(\一位全加器fa封装2_111_cout [0]),
    .Xi(\一位全加器fa封装2_111_cout [2]), .Yi(\一位全加器fa封装2_111_cout [1]));
  \一位全加器FA封装2  \u_一位全加器fa封装2_105  (
    .Cout(\一位全加器fa封装2_105_cout [0]), .Si(\一位全加器fa封装2_105_si ), .Cin(1'b0), .Xi(undriven_119),
    .Yi(undriven_120));
  \一位全加器FA封装2  \u_一位全加器fa封装2_106  (
    .Cout(\一位全加器fa封装2_106_cout [0]), .Si(\一位全加器fa封装2_106_si ), .Cin(undriven_125), .Xi(\一位全加器fa封装2_107_si ),
    .Yi(\一位全加器fa封装2_110_si ));
  \一位全加器FA封装2  \u_一位全加器fa封装2_107  (
    .Cout(\一位全加器fa封装2_107_cout ), .Si(\一位全加器fa封装2_107_si ), .Cin(\一位全加器fa封装2_111_si ),
    .Xi(\一位全加器fa封装2_108_si ), .Yi(\一位全加器fa封装2_112_si ));
  \一位全加器FA封装2  \u_一位全加器fa封装2_108  (
    .Cout(\一位全加器fa封装2_111_cout [2]), .Si(\一位全加器fa封装2_108_si ), .Cin(undriven_123), .Xi(undriven_121),
    .Yi(undriven_122));
  \一位全加器FA封装2  \u_一位全加器fa封装2_109  (
    .Cout(\一位全加器fa封装2_109_cout ), .Si(\一位全加器fa封装2_109_si ), .Cin(undriven_131[0]), .Xi(\一位全加器fa封装2_106_si ),
    .Yi(undriven_131[1]));
  \一位全加器FA封装2  \u_一位全加器fa封装2_110  (
    .Cout(\一位全加器fa封装2_106_cout [1]), .Si(\一位全加器fa封装2_110_si ), .Cin(undriven_129[0]), .Xi(undriven_129[2]),
    .Yi(undriven_129[1]));
  \一位全加器FA封装2  \u_一位全加器fa封装2_111  (
    .Cout(\一位全加器fa封装2_111_cout [0]), .Si(\一位全加器fa封装2_111_si ), .Cin(1'b0), .Xi(undriven_128),
    .Yi(undriven_130));
  \一位全加器FA封装2  \u_一位全加器fa封装2_112  (
    .Cout(\一位全加器fa封装2_111_cout [1]), .Si(\一位全加器fa封装2_112_si ), .Cin(undriven_127), .Xi(undriven_124),
    .Yi(undriven_126));
endmodule

// Trace
module trace (
  input  [7:0] in_1,
  output [31:0] X,
  output [31:0] Y,
  output [3:0] AluOP,
  output [31:0] R,
  output [31:0] R2,
  output [2:0] FLAGS
);

  ROM #(.addrWidth(8), .dataWidth(32), .Select("high")) rom_1 (.addr(in_1), .data(X));
  ROM #(.addrWidth(8), .dataWidth(32), .Select("high")) rom_2 (.addr(in_1), .data(Y));
  ROM #(.addrWidth(8), .dataWidth(4), .Select("high")) rom_3 (.addr(in_1), .data(AluOP));
  ROM #(.addrWidth(8), .dataWidth(32), .Select("high")) rom_4 (.addr(in_1), .data(R));
  ROM #(.addrWidth(8), .dataWidth(32), .Select("high")) rom_5 (.addr(in_1), .data(R2));
  ROM #(.addrWidth(8), .dataWidth(3), .Select("high")) rom_6 (.addr(in_1), .data(FLAGS));

  // Notes on the sheet:
  //   X trace
  //   Y trace
  //   ALU OP Trace
  //   Result Benchmark
  //   Result2 Benchmark
  //   FLAGS Benchmark
  //   contents of rom_1 (hex, n*v repeats v):
  //   ff00ffff ff00ffff ff000000 ff00ffff 7fffffff fffffffe ffff ffffffff 7fffffff 80000000 7ff00000 7c
  //   80000000 7fffffff ff00ffff 7fffffff 18*fffffffe
  //   contents of rom_2 (hex, n*v repeats v):
  //   7 ff00ffff 18 18 10 10 80 ffffffff c 80000000 7c 7ff00000 1 fffffffe 18 74 fffffffe 88 10 ffffffff
  //   10 ffffffff 12*10
  //   contents of rom_3 (hex, n*v repeats v):
  //   0 0 1 2 3 4 4*5 4*6 7 8 9 a b b c c f 11*9 f
  //   contents of rom_4 (hex, n*v repeats v):
  //   807fff80 80000000 ffffffff ff fffffff0 fffffff 1007f fffffffe 8000000b 0 7fefff84 8010007c 7fffffff
  //   80000001 18 7fffffff 0 1 1 1 0 1 300000 11*ffffffee 1
  //   contents of rom_5 (hex, n*v repeats v):
  //   4*0 7 e
  //   contents of rom_6 (hex, n*v repeats v):
  //   0 1 5*0 3 4 7 0 2 4 6 0 0 1 17*0 66*1
endmodule

// 单项评分
module \单项评分  (
  input  ALU_SWITCH,
  input  EQ,
  input  EN,
  input  [4:0] \分值 ,
  input  CLK,
  output [7:0] \正确条数 ,
  output [7:0] \扣分 ,
  output Right,
  output [7:0] Total
);

  wire and_1_out, and_2_out, not_1_out, priority_encoder_1_gs, priority_encoder_1_out;
  wire [7:0] bit_extender_1_out;

  and and_1 (and_1_out, ALU_SWITCH, EN);
  Priority_Encoder #(.select(1), .disabled("Z")) priority_encoder_1 (
    .in0(EQ), .in1(EQ), .out(priority_encoder_1_out), .gs(priority_encoder_1_gs));  // open: en_out, en_in
  Counter #(.width(8), .max('hff), .ongoal("wrap"), .trigger("rising"), .behavior("old")) counter_1 (
    .count(and_1_out), .Q(Total), .clk(CLK));  // open: load, D, carry, clr, preset
  and and_2 (and_2_out, ALU_SWITCH, priority_encoder_1_out, priority_encoder_1_gs, EN);
  Counter #(.width(8), .max('hff), .ongoal("wrap"), .trigger("rising"), .behavior("old")) counter_2 (
    .count(and_2_out), .Q(\正确条数 ), .clk(CLK));  // open: load, D, carry, clr, preset
  Comparator #(.width(8), .mode("twosComplement")) comparator_1 (.a(\正确条数 ), .b(Total), .eq(Right));  // open: gt, lt
  assign bit_extender_1_out = {{3{1'b0}}, \分值 };  // Bit_Extender bit_extender_1
  Multiplexer #(.select(1), .width(8), .disabled("Z"), .enable("false")) multiplexer_1 (
    .in0({8{1'b0}}), .in1(bit_extender_1_out), .out(\扣分 ), .sel(not_1_out));
  not not_1 (not_1_out, Right);

  // Notes on the sheet:
  //   只有使用优先编码器才能屏蔽掉位置状态
endmodule

module \总评分  (
  input  [7:0] in_1,
  input  [7:0] in_2,
  input  [7:0] in_3,
  input  [7:0] in_4,
  input  [7:0] in_5,
  input  [7:0] in_6,
  input  [7:0] in_7,
  input  [7:0] in_8,
  input  [7:0] in_9,
  input  [7:0] in_10,
  input  [7:0] in_11,
  input  [7:0] in_12,
  input  [7:0] in_13,
  input  [7:0] in_14,
  input  [7:0] in_15,
  input  [7:0] in_16,
  input  \悬空扣分 ,
  output [7:0] Result,
  output [3:0] High,
  output [3:0] Low,
  output [3:0] Mid
);

  wire [7:0] adder_1_out, adder_2_out, adder_3_out, adder_4_out, adder_5_out, adder_6_out, adder_7_out,
       adder_8_out, adder_9_out, adder_10_out, adder_11_out, adder_12_out, adder_13_out, adder_14_out,
       adder_15_out, divider_1_out, subtractor_1_out, subtractor_2_out;
  wire [7:4] divider_1_rem, divider_2_out, divider_2_rem;

  Adder #(.width(8)) adder_1 (.a(in_1), .b(in_2), .out(adder_1_out));  // open: cin, cout
  Adder #(.width(8)) adder_2 (.a(in_3), .b(in_4), .out(adder_2_out));  // open: cin, cout
  Adder #(.width(8)) adder_3 (.a(in_5), .b(in_6), .out(adder_3_out));  // open: cin, cout
  Adder #(.width(8)) adder_4 (.a(in_7), .b(in_8), .out(adder_4_out));  // open: cin, cout
  Adder #(.width(8)) adder_5 (.a(in_9), .b(in_10), .out(adder_5_out));  // open: cin, cout
  Adder #(.width(8)) adder_6 (.a(in_11), .b(in_12), .out(adder_6_out));  // open: cin, cout
  Adder #(.width(8)) adder_7 (.a(in_13), .b(in_14), .out(adder_7_out));  // open: cin, cout
  Adder #(.width(8)) adder_8 (.a(in_15), .b(in_16), .out(adder_8_out));  // open: cin, cout
  Adder #(.width(8)) adder_9 (.a(adder_1_out), .b(adder_2_out), .out(adder_9_out));  // open: cin, cout
  Adder #(.width(8)) adder_10 (.a(adder_3_out), .b(adder_4_out), .out(adder_10_out));  // open: cin, cout
  Adder #(.width(8)) adder_11 (.a(adder_5_out), .b(adder_6_out), .out(adder_11_out));  // open: cin, cout
  Adder #(.width(8)) adder_12 (.a(adder_7_out), .b(adder_8_out), .out(adder_12_out));  // open: cin, cout
  Adder #(.width(8)) adder_13 (.a(adder_9_out), .b(adder_10_out), .out(adder_13_out));  // open: cin, cout
  Adder #(.width(8)) adder_14 (.a(adder_11_out), .b(adder_12_out), .out(adder_14_out));  // open: cin, cout
  Adder #(.width(8)) adder_15 (.a(adder_13_out), .b(adder_14_out), .out(adder_15_out));  // open: cin, cout
  Subtractor #(.width(8)) subtractor_1 (.a(8'h64), .b(adder_15_out), .out(subtractor_1_out));  // open: bin, bout
  Subtractor #(.width(8)) subtractor_2 (.a(subtractor_1_out), .b(8'h5), .out(subtractor_2_out));  // open: bin, bout
  Multiplexer #(.select(1), .width(8), .disabled("Z"), .enable("false")) multiplexer_1 (
    .in0(subtractor_1_out), .in1(subtractor_2_out), .out(Result), .sel(\悬空扣分 ));
  Divider #(.width(8)) divider_1 (
    .a(Result), .b(8'ha), .out(divider_1_out), .rem({divider_1_rem, Low}));  // open: upper
  Divider #(.width(8)) divider_2 (
    .a(divider_1_out), .b(8'ha), .out({divider_2_out, High}), .rem({divider_2_rem, Mid}));  // open: upper
endmodule

module \四位乘法器  (
  input  [3:0] A,
  input  [3:0] B,
  output [7:0] out_3
);

  wire [7:0] adder_1_out, adder_2_out, adder_3_out, adder_4_out, multiplexer_1_out, multiplexer_2_out,
       multiplexer_3_out, shifter_1_out, shifter_2_out;

  Adder #(.width(8)) adder_1 (.a({8{1'b0}}), .b({4'b0000, B}), .out(adder_1_out), .cin(1'b0));  // open: cout
  Multiplexer #(.select(1), .width(8), .disabled("Z"), .enable("false")) multiplexer_1 (
    .in0({8{1'b0}}), .in1(adder_1_out), .out(multiplexer_1_out), .sel(A[0]));
  Adder #(.width(8)) adder_2 (
    .a(multiplexer_1_out), .b({3'b000, B, 1'b0}), .out(adder_2_out), .cin(1'b0));  // open: cout
  Multiplexer #(.select(1), .width(8), .disabled("Z"), .enable("false")) multiplexer_2 (
    .in0(multiplexer_1_out), .in1(adder_2_out), .out(multiplexer_2_out), .sel(A[1]));
  Shifter #(.width(8), .shift("ll")) shifter_1 (.in({3'b000, B, 1'b0}), .\dist (3'b001), .out(shifter_1_out));
  Adder #(.width(8)) adder_3 (.a(multiplexer_2_out), .b(shifter_1_out), .out(adder_3_out), .cin(1'b0));  // open: cout
  Multiplexer #(.select(1), .width(8), .disabled("Z"), .enable("false")) multiplexer_3 (
    .in0(multiplexer_2_out), .in1(adder_3_out), .out(multiplexer_3_out), .sel(A[2]));
  Shifter #(.width(8), .shift("ll")) shifter_2 (.in(shifter_1_out), .\dist (3'b001), .out(shifter_2_out));
  Adder #(.width(8)) adder_4 (.a(multiplexer_3_out), .b(shifter_2_out), .out(adder_4_out), .cin(1'b0));  // open: cout
  Multiplexer #(.select(1), .width(8), .disabled("Z"), .enable("false")) multiplexer_4 (
    .in0(multiplexer_3_out), .in1(adder_4_out), .out(out_3), .sel(A[3]));
endmodule

module \_32X4乘法器  (
  input  [3:0] A,
  input  [31:0] \B低32 ,
  output [31:0] \输出高 ,
  output [31:0] \输出低 
);

  wire [31:0] \n64位加法器_1_输出低 , \n64位加法器_1_输出高 , \n64位加法器_2_输出低 , \n64位加法器_2_输出高 , \n64位加法器_3_输出低 ,
       \n64位加法器_3_输出高 , \n64位加法器_4_输出低 , \n64位加法器_4_输出高 , \n64位多路选择器_1_p低 , \n64位多路选择器_1_p高 ,
       \n64位多路选择器_2_p低 , \n64位多路选择器_2_p高 , \n64位多路选择器_3_p低 , \n64位多路选择器_3_p高 ;

  \_64位加法器  \u_64位加法器_1  (
    .\A低 ({32{1'b0}}), .\B低 (\B低32 ), .\A高 ({32{1'b0}}), .\B高 ({32{1'b0}}), .\输出低 (\n64位加法器_1_输出低 ),
    .\输出高 (\n64位加法器_1_输出高 ));
  \_64位多路选择器  \u_64位多路选择器_1  (
    .\A高 ({32{1'b0}}), .\B高 (\n64位加法器_1_输出高 ), .\A低 ({32{1'b0}}), .\B低 (\n64位加法器_1_输出低 ),
    .\p高 (\n64位多路选择器_1_p高 ), .in_3(A[0]), .\p低 (\n64位多路选择器_1_p低 ));
  \_64位加法器  \u_64位加法器_2  (
    .\A低 (\n64位多路选择器_1_p低 ), .\B低 ({\B低32 [30:0], 1'b0}), .\A高 (\n64位多路选择器_1_p高 ),
    .\B高 ({{31{1'b0}}, \B低32 [31]}), .\输出低 (\n64位加法器_2_输出低 ), .\输出高 (\n64位加法器_2_输出高 ));
  \_64位多路选择器  \u_64位多路选择器_2  (
    .\A高 (\n64位多路选择器_1_p高 ), .\B高 (\n64位加法器_2_输出高 ), .\A低 (\n64位多路选择器_1_p低 ), .\B低 (\n64位加法器_2_输出低 ),
    .\p高 (\n64位多路选择器_2_p高 ), .in_3(A[1]), .\p低 (\n64位多路选择器_2_p低 ));
  \_64位加法器  \u_64位加法器_3  (
    .\A低 (\n64位多路选择器_2_p低 ), .\B低 ({\B低32 [29:0], 2'b00}), .\A高 (\n64位多路选择器_2_p高 ),
    .\B高 ({{30{1'b0}}, \B低32 [31:30]}), .\输出低 (\n64位加法器_3_输出低 ), .\输出高 (\n64位加法器_3_输出高 ));
  \_64位多路选择器  \u_64位多路选择器_3  (
    .\A高 (\n64位多路选择器_2_p高 ), .\B高 (\n64位加法器_3_输出高 ), .\A低 (\n64位多路选择器_2_p低 ), .\B低 (\n64位加法器_3_输出低 ),
    .\p高 (\n64位多路选择器_3_p高 ), .in_3(A[2]), .\p低 (\n64位多路选择器_3_p低 ));
  \_64位加法器  \u_64位加法器_4  (
    .\A低 (\n64位多路选择器_3_p低 ), .\B低 ({\B低32 [28:0], 3'b000}), .\A高 (\n64位多路选择器_3_p高 ),
    .\B高 ({{29{1'b0}}, \B低32 [31:29]}), .\输出低 (\n64位加法器_4_输出低 ), .\输出高 (\n64位加法器_4_输出高 ));
  \_64位多路选择器  \u_64位多路选择器_4  (
    .\A高 (\n64位多路选择器_3_p高 ), .\B高 (\n64位加法器_4_输出高 ), .\A低 (\n64位多路选择器_3_p低 ), .\B低 (\n64位加法器_4_输出低 ),
    .\p高 (\输出高 ), .in_3(A[3]), .\p低 (\输出低 ));
endmodule
module \_32X32乘法器  (
  input  [31:0] a,
  input  [31:0] b,
  output [31:0] out_3,
  output [31:0] out_4
);

  wire [31:0] \n32x4乘法器_1_输出低 , \n32x4乘法器_1_输出高 , \n32x4乘法器_2_输出低 , \n32x4乘法器_2_输出高 , \n32x4乘法器_3_输出低 ,
       \n32x4乘法器_3_输出高 , \n32x4乘法器_4_输出低 , \n32x4乘法器_4_输出高 , \n32x4乘法器_5_输出低 , \n32x4乘法器_5_输出高 ,
       \n32x4乘法器_6_输出低 , \n32x4乘法器_6_输出高 , \n32x4乘法器_7_输出低 , \n32x4乘法器_7_输出高 , \n32x4乘法器_8_输出低 ,
       \n32x4乘法器_8_输出高 , \n64位加法器_1_输出低 , \n64位加法器_1_输出高 , \n64位加法器_2_输出低 , \n64位加法器_2_输出高 , \n64位加法器_3_输出低 ,
       \n64位加法器_3_输出高 , \n64位加法器_4_输出低 , \n64位加法器_4_输出高 , \n64位加法器_5_输出低 , \n64位加法器_5_输出高 , \n64位加法器_6_输出低 ,
       \n64位加法器_6_输出高 , \移4_1_out_3 , \移4_1_out_4 , \移8_1_out_3 , \移8_1_out_4 , \移12_1_out_3 , \移12_1_out_4 ,
       \移16_1_out_3 , \移16_1_out_4 , \移20_1_out_3 , \移20_1_out_4 , \移24_1_out_3 , \移24_1_out_4 ,
       \移28_1_out_3 , \移28_1_out_4 ;

  \_32X4乘法器  \u_32x4乘法器_1  (.A(a[31:28]), .\B低32 (b), .\输出低 (\n32x4乘法器_1_输出低 ), .\输出高 (\n32x4乘法器_1_输出高 ));
  \_32X4乘法器  \u_32x4乘法器_2  (.A(a[15:12]), .\B低32 (b), .\输出低 (\n32x4乘法器_2_输出低 ), .\输出高 (\n32x4乘法器_2_输出高 ));
  \_32X4乘法器  \u_32x4乘法器_3  (.A(a[11:8]), .\B低32 (b), .\输出低 (\n32x4乘法器_3_输出低 ), .\输出高 (\n32x4乘法器_3_输出高 ));
  \_32X4乘法器  \u_32x4乘法器_4  (.A(a[27:24]), .\B低32 (b), .\输出低 (\n32x4乘法器_4_输出低 ), .\输出高 (\n32x4乘法器_4_输出高 ));
  \_32X4乘法器  \u_32x4乘法器_5  (.A(a[3:0]), .\B低32 (b), .\输出低 (\n32x4乘法器_5_输出低 ), .\输出高 (\n32x4乘法器_5_输出高 ));
  \_32X4乘法器  \u_32x4乘法器_6  (.A(a[19:16]), .\B低32 (b), .\输出低 (\n32x4乘法器_6_输出低 ), .\输出高 (\n32x4乘法器_6_输出高 ));
  \_32X4乘法器  \u_32x4乘法器_7  (.A(a[23:20]), .\B低32 (b), .\输出低 (\n32x4乘法器_7_输出低 ), .\输出高 (\n32x4乘法器_7_输出高 ));
  \_32X4乘法器  \u_32x4乘法器_8  (.A(a[7:4]), .\B低32 (b), .\输出低 (\n32x4乘法器_8_输出低 ), .\输出高 (\n32x4乘法器_8_输出高 ));
  \移28  \u_移28_1  (.\低32位 (\n32x4乘法器_1_输出低 ), .\高32位 (\n32x4乘法器_1_输出高 ), .out_3(\移28_1_out_3 ), .out_4(\移28_1_out_4 ));
  \移12  \u_移12_1  (.\低32位 (\n32x4乘法器_2_输出低 ), .\高32位 (\n32x4乘法器_2_输出高 ), .out_3(\移12_1_out_3 ), .out_4(\移12_1_out_4 ));
  \移8  \u_移8_1  (.\低32位 (\n32x4乘法器_3_输出低 ), .\高32位 (\n32x4乘法器_3_输出高 ), .out_3(\移8_1_out_3 ), .out_4(\移8_1_out_4 ));
  \移24  \u_移24_1  (.\低32位 (\n32x4乘法器_4_输出低 ), .\高32位 (\n32x4乘法器_4_输出高 ), .out_3(\移24_1_out_3 ), .out_4(\移24_1_out_4 ));
  \移16  \u_移16_1  (.\低32位 (\n32x4乘法器_6_输出低 ), .\高32位 (\n32x4乘法器_6_输出高 ), .out_3(\移16_1_out_3 ), .out_4(\移16_1_out_4 ));
  \移20  \u_移20_1  (.\低32位 (\n32x4乘法器_7_输出低 ), .\高32位 (\n32x4乘法器_7_输出高 ), .out_3(\移20_1_out_3 ), .out_4(\移20_1_out_4 ));
  \移4  \u_移4_1  (.\低32位 (\n32x4乘法器_8_输出低 ), .\高32位 (\n32x4乘法器_8_输出高 ), .out_3(\移4_1_out_3 ), .out_4(\移4_1_out_4 ));
  \_64位加法器  \u_64位加法器_1  (
    .\A低 (\移28_1_out_3 ), .\B低 (\移12_1_out_3 ), .\A高 (\移28_1_out_4 ), .\B高 (\移12_1_out_4 ),
    .\输出低 (\n64位加法器_1_输出低 ), .\输出高 (\n64位加法器_1_输出高 ));
  \_64位加法器  \u_64位加法器_2  (
    .\A低 (\移8_1_out_3 ), .\B低 (\移24_1_out_3 ), .\A高 (\移8_1_out_4 ), .\B高 (\移24_1_out_4 ),
    .\输出低 (\n64位加法器_2_输出低 ), .\输出高 (\n64位加法器_2_输出高 ));
  \_64位加法器  \u_64位加法器_3  (
    .\A低 (\n32x4乘法器_5_输出低 ), .\B低 (\移16_1_out_3 ), .\A高 (\n32x4乘法器_5_输出高 ), .\B高 (\移16_1_out_4 ),
    .\输出低 (\n64位加法器_3_输出低 ), .\输出高 (\n64位加法器_3_输出高 ));
  \_64位加法器  \u_64位加法器_4  (
    .\A低 (\移20_1_out_3 ), .\B低 (\移4_1_out_3 ), .\A高 (\移20_1_out_4 ), .\B高 (\移4_1_out_4 ),
    .\输出低 (\n64位加法器_4_输出低 ), .\输出高 (\n64位加法器_4_输出高 ));
  \_64位加法器  \u_64位加法器_5  (
    .\A低 (\n64位加法器_1_输出低 ), .\B低 (\n64位加法器_2_输出低 ), .\A高 (\n64位加法器_1_输出高 ), .\B高 (\n64位加法器_2_输出高 ),
    .\输出低 (\n64位加法器_5_输出低 ), .\输出高 (\n64位加法器_5_输出高 ));
  \_64位加法器  \u_64位加法器_6  (
    .\A低 (\n64位加法器_3_输出低 ), .\B低 (\n64位加法器_4_输出低 ), .\A高 (\n64位加法器_3_输出高 ), .\B高 (\n64位加法器_4_输出高 ),
    .\输出低 (\n64位加法器_6_输出低 ), .\输出高 (\n64位加法器_6_输出高 ));
  \_64位加法器  \u_64位加法器_7  (
    .\A低 (\n64位加法器_5_输出低 ), .\B低 (\n64位加法器_6_输出低 ), .\A高 (\n64位加法器_5_输出高 ), .\B高 (\n64位加法器_6_输出高 ),
    .\输出低 (out_4), .\输出高 (out_3));
endmodule

module \_64位加法器  (
  input  [31:0] \A低 ,
  input  [31:0] \B低 ,
  input  [31:0] \A高 ,
  input  [31:0] \B高 ,
  output [31:0] \输出低 ,
  output [31:0] \输出高 
);

  wire adder_1_cout;

  Adder #(.width(32)) adder_1 (.a(\A低 ), .b(\B低 ), .out(\输出低 ), .cin(1'b0), .cout(adder_1_cout));
  Adder #(.width(32)) adder_2 (.a(\A高 ), .b(\B高 ), .out(\输出高 ), .cin(adder_1_cout));  // open: cout
endmodule

module \_64位多路选择器  (
  input  [31:0] \A高 ,
  input  [31:0] \B高 ,
  input  in_3,
  input  [31:0] \A低 ,
  input  [31:0] \B低 ,
  output [31:0] \p高 ,
  output [31:0] \p低 
);

  Multiplexer #(.select(1), .width(32), .disabled("Z"), .enable("false")) multiplexer_1 (
    .in0(\A高 ), .in1(\B高 ), .out(\p高 ), .sel(in_3));
  Multiplexer #(.select(1), .width(32), .disabled("Z"), .enable("false")) multiplexer_2 (
    .in0(\A低 ), .in1(\B低 ), .out(\p低 ), .sel(in_3));
endmodule

module \移4  (
  input  [31:0] \低32位 ,
  input  [31:0] \高32位 ,
  output [31:0] out_3,
  output [31:0] out_4
);


  assign out_3 = {\低32位 [27:0], 4'b0000};
  assign out_4 = {\高32位 [27:0], \低32位 [31:28]};
endmodule

module \移8  (
  input  [31:0] \低32位 ,
  input  [31:0] \高32位 ,
  output [31:0] out_3,
  output [31:0] out_4
);


  assign out_3 = {\低32位 [23:0], {8{1'b0}}};
  assign out_4 = {\高32位 [23:0], \低32位 [31:24]};
endmodule

module \移12  (
  input  [31:0] \低32位 ,
  input  [31:0] \高32位 ,
  output [31:0] out_3,
  output [31:0] out_4
);


  assign out_3 = {\低32位 [19:0], {12{1'b0}}};
  assign out_4 = {\高32位 [19:0], \低32位 [31:20]};
endmodule

module \移16  (
  input  [31:0] \低32位 ,
  input  [31:0] \高32位 ,
  output [31:0] out_3,
  output [31:0] out_4
);


  assign out_3 = {\低32位 [15:0], {16{1'b0}}};
  assign out_4 = {\高32位 [15:0], \低32位 [31:16]};
endmodule

module \移20  (
  input  [31:0] \低32位 ,
  input  [31:0] \高32位 ,
  output [31:0] out_3,
  output [31:0] out_4
);


  assign out_3 = {\低32位 [11:0], {20{1'b0}}};
  assign out_4 = {\高32位 [11:0], \低32位 [31:12]};
endmodule

module \移24  (
  input  [31:0] \低32位 ,
  input  [31:0] \高32位 ,
  output [31:0] out_3,
  output [31:0] out_4
);


  assign out_3 = {\低32位 [7:0], {24{1'b0}}};
  assign out_4 = {\高32位 [7:0], \低32位 [31:8]};
endmodule

module \移28  (
  input  [31:0] \低32位 ,
  input  [31:0] \高32位 ,
  output [31:0] out_3,
  output [31:0] out_4
);


  assign out_3 = {\低32位 [3:0], {28{1'b0}}};
  assign out_4 = {\高32位 [3:0], \低32位 [31:4]};
endmodule
